// Logisim project makecomputer.circ as structural Verilog
module \LED计数  (
  input  in_1,
  input  in_2,
  input  in_3,
  input  in_4,
  input  in_5,
  output out_6,
  output out_7,
  output out_8,
  output out_9,
  output out_10
);

  or or_1 (out_6, in_1, in_2, in_3, in_4, in_5);
  or or_2 (out_7, in_2, in_3, in_4, in_5);
  or or_3 (out_8, in_3, in_4, in_5);
  or or_4 (out_9, in_4, in_5);

  assign out_10 = in_5;
endmodule

module TEST1 (
);

  wire button_1_out, button_2_out, button_3_out, button_4_out, button_5_out, \led计数_1_out_6 ,
       \led计数_1_out_7 , \led计数_1_out_8 , \led计数_1_out_9 , \led计数_1_out_10 ;

  Button button_1 (.out(button_1_out));
  Button button_2 (.out(button_2_out));
  Button button_3 (.out(button_3_out));
  Button button_4 (.out(button_4_out));
  Button button_5 (.out(button_5_out));
  \LED计数  \led计数_1  (
    .in_1(button_1_out), .in_2(button_2_out), .in_3(button_3_out), .in_4(button_4_out), .in_5(button_5_out),
    .out_6(\led计数_1_out_6 ), .out_7(\led计数_1_out_7 ), .out_8(\led计数_1_out_8 ), .out_9(\led计数_1_out_9 ),
    .out_10(\led计数_1_out_10 ));
  LED led_1 (.in(\led计数_1_out_6 ));
  LED led_2 (.in(\led计数_1_out_7 ));
  LED led_3 (.in(\led计数_1_out_8 ));
  LED led_4 (.in(\led计数_1_out_9 ));
  LED led_5 (.in(\led计数_1_out_10 ));

  // Notes on the sheet:
  //   1
  //   3
  //   2
  //   4
  //   5
endmodule

module \按键编码器  (
  input  I1,
  input  I2,
  input  I3,
  input  I4,
  input  I5,
  output O1,
  output O2,
  output O3
);

  wire and_1_out, and_2_out, and_3_out, and_4_out, and_5_out, and_6_out, and_7_out, and_8_out, and_9_out,
       not_1_out, not_2_out, not_3_out, not_4_out, not_5_out, not_6_out, not_7_out, not_8_out, not_9_out,
       not_10_out, not_11_out, not_12_out;

  not not_1 (not_1_out, I4);
  not not_2 (not_2_out, I2);
  not not_3 (not_3_out, I4);
  not not_4 (not_4_out, I3);
  not not_5 (not_5_out, I4);
  not not_6 (not_6_out, I5);
  not not_7 (not_7_out, I4);
  not not_8 (not_8_out, I5);
  not not_9 (not_9_out, I3);
  not not_10 (not_10_out, I5);
  not not_11 (not_11_out, I1);
  not not_12 (not_12_out, I2);
  and and_1 (and_1_out, I3, not_1_out);
  and and_2 (and_2_out, I1, not_2_out, not_3_out);
  and and_3 (and_3_out, I1, I2, not_4_out, I4);
  and and_4 (and_4_out, I3, not_5_out, not_6_out);
  and and_5 (and_5_out, I2, not_7_out, not_8_out);
  and and_6 (and_6_out, I1, I2, not_9_out, not_10_out);
  and and_7 (and_7_out, not_11_out, I4);
  and and_8 (and_8_out, not_12_out, I4);
  and and_9 (and_9_out, I3, I4);
  or or_1 (O1, I5, and_1_out, and_2_out, and_3_out);
  or or_2 (O2, and_4_out, and_5_out, and_6_out);
  or or_3 (O3, I5, and_7_out, and_8_out, and_9_out);
endmodule

module TEST2 (
);

  wire button_1_out, button_2_out, button_3_out, button_4_out, button_5_out;
  wire [2:0] \按键编码器_1_o1 ;

  Button button_1 (.out(button_1_out));
  Button button_2 (.out(button_2_out));
  Button button_3 (.out(button_3_out));
  Button button_4 (.out(button_4_out));
  Button button_5 (.out(button_5_out));
  \按键编码器  \u_按键编码器_1  (
    .I1(button_1_out), .I2(button_2_out), .I3(button_3_out), .I4(button_4_out), .I5(button_5_out),
    .O1(\按键编码器_1_o1 [0]), .O2(\按键编码器_1_o1 [1]), .O3(\按键编码器_1_o1 [2]));
  // Probe on \按键编码器_1_o1 
  Hex_Digit_Display hex_digit_display_1 (.value({1'b0, \按键编码器_1_o1 }), .dp(1'b1));

  // Notes on the sheet:
  //   1
  //   3
  //   2
  //   4
  //   5
endmodule

module \数码管  (
  input  a,
  input  b,
  input  c,
  input  d,
  output x,
  output y,
  output z,
  output u,
  output v,
  output w,
  output s
);

  wire and_1_out, and_2_out, and_3_out, and_4_out, and_5_out, and_6_out, and_7_out, and_8_out, and_9_out,
       and_10_out, and_11_out, and_12_out, and_13_out, and_14_out, and_15_out, and_16_out, and_17_out,
       and_18_out, and_19_out, and_20_out, and_21_out, and_22_out, and_23_out, and_24_out, and_25_out,
       and_26_out, and_27_out, and_28_out, and_29_out, and_30_out, and_31_out, not_1_out, not_2_out,
       not_3_out, not_4_out, not_5_out, not_6_out, not_7_out, not_8_out, not_9_out, not_10_out, not_11_out,
       not_12_out, not_13_out, not_14_out, not_15_out, not_16_out, not_17_out, not_18_out, not_19_out,
       not_20_out, not_21_out, not_22_out, not_23_out, not_24_out, not_25_out, not_26_out, not_27_out,
       not_28_out, not_29_out, not_30_out, not_31_out, not_32_out, not_33_out, not_34_out, not_35_out,
       not_36_out, not_37_out, not_38_out, not_39_out, not_40_out, not_41_out, not_42_out, not_43_out;

  not not_1 (not_1_out, b);
  and and_1 (and_1_out, not_1_out, not_2_out);
  not not_2 (not_2_out, d);
  not not_3 (not_3_out, a);
  and and_2 (and_2_out, not_3_out, c);
  and and_3 (and_3_out, b, d);
  and and_4 (and_4_out, a, not_4_out);
  not not_4 (not_4_out, c);
  not not_5 (not_5_out, b);
  not not_6 (not_6_out, c);
  and and_5 (and_5_out, not_6_out, not_7_out);
  not not_7 (not_7_out, d);
  not not_8 (not_8_out, a);
  and and_6 (and_6_out, not_8_out, c, d);
  and and_7 (and_7_out, a, not_9_out);
  not not_9 (not_9_out, c);
  and and_8 (and_8_out, a, not_10_out);
  not not_10 (not_10_out, d);
  not not_11 (not_11_out, a);
  and and_9 (and_9_out, not_11_out, not_12_out);
  not not_12 (not_12_out, c);
  and and_10 (and_10_out, b, c);
  and and_11 (and_11_out, a, not_13_out);
  not not_13 (not_13_out, b);
  not not_14 (not_14_out, b);
  and and_12 (and_12_out, not_14_out, not_15_out);
  not not_15 (not_15_out, d);
  not not_16 (not_16_out, a);
  not not_17 (not_17_out, b);
  and and_13 (and_13_out, not_16_out, not_17_out, c);
  not not_18 (not_18_out, a);
  and and_14 (and_14_out, not_18_out, c, not_19_out);
  not not_19 (not_19_out, d);
  and and_15 (and_15_out, b, not_20_out, d);
  not not_20 (not_20_out, c);
  and and_16 (and_16_out, a, not_21_out);
  not not_21 (not_21_out, c);
  and and_17 (and_17_out, a, b, d);
  not not_22 (not_22_out, b);
  and and_18 (and_18_out, not_22_out, not_23_out);
  not not_23 (not_23_out, d);
  not not_24 (not_24_out, a);
  and and_19 (and_19_out, not_24_out, c, not_25_out);
  not not_25 (not_25_out, d);
  and and_20 (and_20_out, a, not_26_out, not_27_out);
  not not_26 (not_26_out, c);
  not not_27 (not_27_out, d);
  not not_28 (not_28_out, a);
  not not_29 (not_29_out, c);
  and and_21 (and_21_out, not_28_out, not_29_out, not_30_out);
  not not_30 (not_30_out, d);
  not not_31 (not_31_out, a);
  and and_22 (and_22_out, not_31_out, b, not_32_out);
  not not_32 (not_32_out, c);
  not not_33 (not_33_out, a);
  and and_23 (and_23_out, not_33_out, b, not_34_out);
  not not_34 (not_34_out, d);
  and and_24 (and_24_out, a, not_35_out, not_36_out);
  not not_35 (not_35_out, b);
  not not_36 (not_36_out, c);
  not not_37 (not_37_out, b);
  and and_25 (and_25_out, a, not_37_out, not_38_out);
  not not_38 (not_38_out, d);
  and and_26 (and_26_out, a, b, c);
  not not_39 (not_39_out, a);
  and and_27 (and_27_out, not_39_out, not_40_out, c);
  not not_40 (not_40_out, b);
  and and_28 (and_28_out, b, not_41_out);
  not not_41 (not_41_out, c);
  and and_29 (and_29_out, b, not_42_out);
  not not_42 (not_42_out, d);
  and and_30 (and_30_out, a, not_43_out);
  not not_43 (not_43_out, c);
  and and_31 (and_31_out, a, b);
  or or_1 (x, and_1_out, and_2_out, and_3_out, and_4_out);
  or or_2 (y, not_5_out, and_5_out, and_6_out, and_7_out, and_8_out);
  or or_3 (z, and_9_out, d, and_10_out, and_11_out);
  or or_4 (v, and_18_out, and_19_out, and_20_out);
  or or_5 (s, and_27_out, and_28_out, and_29_out, and_30_out, and_31_out);
  or or_6 (u, and_12_out, and_13_out, and_14_out, and_15_out, and_16_out, and_17_out);
  or or_7 (w, and_21_out, and_22_out, and_23_out, and_24_out, and_25_out, and_26_out);
endmodule

module TEST3 (
);

  wire clock_1_out, \数码管_1_s , \数码管_1_u , \数码管_1_v , \数码管_1_w , \数码管_1_x , \数码管_1_y , \数码管_1_z ;
  wire [3:0] counter_1_q;

  Counter #(.width(4), .max('h9)) counter_1 (.Q(counter_1_q), .clk(clock_1_out));  // open: load, D, count, carry, clr
  Clock clock_1 (.out(clock_1_out));
  \数码管  \u_数码管_1  (
    .a(counter_1_q[3]), .b(counter_1_q[2]), .c(counter_1_q[1]), .d(counter_1_q[0]), .x(\数码管_1_x ),
    .y(\数码管_1_y ), .z(\数码管_1_z ), .u(\数码管_1_u ), .v(\数码管_1_v ), .w(\数码管_1_w ), .s(\数码管_1_s ));
  _7_Segment_Display u_7_segment_display_1 (
    .g(\数码管_1_s ), .f(\数码管_1_w ), .a(\数码管_1_x ), .b(\数码管_1_y ), .e(\数码管_1_v ), .d(\数码管_1_u ), .c(\数码管_1_z ));  // open: dp
endmodule

module TEST4 (
);

  wire button_1_out, button_2_out, button_3_out, button_4_out, button_5_out, \led计数_1_out_6 ,
       \led计数_1_out_7 , \led计数_1_out_8 , \led计数_1_out_9 , \led计数_1_out_10 , \数码管_1_s , \数码管_1_u , \数码管_1_v ,
       \数码管_1_w , \数码管_1_x , \数码管_1_y , \数码管_1_z ;
  wire [2:0] \按键编码器_1_o1 ;

  Button button_1 (.out(button_1_out));
  Button button_2 (.out(button_2_out));
  Button button_3 (.out(button_3_out));
  Button button_4 (.out(button_4_out));
  Button button_5 (.out(button_5_out));
  \LED计数  \led计数_1  (
    .in_1(button_1_out), .in_2(button_2_out), .in_3(button_3_out), .in_4(button_4_out), .in_5(button_5_out),
    .out_6(\led计数_1_out_6 ), .out_7(\led计数_1_out_7 ), .out_8(\led计数_1_out_8 ), .out_9(\led计数_1_out_9 ),
    .out_10(\led计数_1_out_10 ));
  \按键编码器  \u_按键编码器_1  (
    .I1(button_1_out), .I2(button_2_out), .I3(button_3_out), .I4(button_4_out), .I5(button_5_out),
    .O1(\按键编码器_1_o1 [0]), .O2(\按键编码器_1_o1 [1]), .O3(\按键编码器_1_o1 [2]));
  LED led_1 (.in(\led计数_1_out_6 ));
  LED led_2 (.in(\led计数_1_out_7 ));
  LED led_3 (.in(\led计数_1_out_8 ));
  LED led_4 (.in(\led计数_1_out_9 ));
  LED led_5 (.in(\led计数_1_out_10 ));
  // Probe on \按键编码器_1_o1 
  \数码管  \u_数码管_1  (
    .a(1'b0), .b(\按键编码器_1_o1 [2]), .c(\按键编码器_1_o1 [1]), .d(\按键编码器_1_o1 [0]), .x(\数码管_1_x ), .y(\数码管_1_y ),
    .z(\数码管_1_z ), .u(\数码管_1_u ), .v(\数码管_1_v ), .w(\数码管_1_w ), .s(\数码管_1_s ));
  _7_Segment_Display u_7_segment_display_1 (
    .g(\数码管_1_s ), .f(\数码管_1_w ), .a(\数码管_1_x ), .b(\数码管_1_y ), .e(\数码管_1_v ), .d(\数码管_1_u ), .c(\数码管_1_z ));  // open: dp
  Hex_Digit_Display hex_digit_display_1 (.value({1'b0, \按键编码器_1_o1 }), .dp(1'b1));

  // Notes on the sheet:
  //   1
  //   2
  //   3
  //   4
  //   5
endmodule
