// Logisim project reg8.circ as structural Verilog: 1 circuit, main circuit reg8
module reg8 (
  input  in_1,
  input  in_2,
  input  in_3,
  input  in_4,
  input  in_5,
  input  in_6,
  input  in_7,
  input  in_8,
  input  in_9,
  output out_10,
  output out_11,
  output out_12,
  output out_13,
  output out_14,
  output out_15,
  output out_16,
  output out_17
);

  Register register_1 (
    .D({in_1, in_2, in_3, in_4, in_5, in_6, in_7, in_9}),
    .Q({out_10, out_11, out_12, out_13, out_14, out_15, out_16, out_17}), .clk(in_8));  // open: en, clr
endmodule
