// Logisim project seg.circ as structural Verilog: 9 circuits, main circuit Seg-A
module Seg_A (
  input  D3,
  input  D2,
  input  D1,
  input  D0,
  output A
);

  wire and_1_out, and_2_out, and_3_out, and_4_out, not_1_out, not_2_out, not_3_out, not_4_out, not_5_out,
       not_6_out, not_7_out, not_8_out;

  not not_1 (not_1_out, D3);
  not not_2 (not_2_out, D2);
  not not_3 (not_3_out, D1);
  not not_4 (not_4_out, D3);
  not not_5 (not_5_out, D1);
  not not_6 (not_6_out, D0);
  not not_7 (not_7_out, D2);
  not not_8 (not_8_out, D1);
  and and_1 (and_1_out, not_1_out, not_2_out, not_3_out, D0);
  and and_2 (and_2_out, not_4_out, D2, not_5_out, not_6_out);
  and and_3 (and_3_out, D3, not_7_out, D1, D0);
  and and_4 (and_4_out, D3, D2, not_8_out, D0);
  or or_1 (A, and_1_out, and_2_out, and_3_out, and_4_out);
endmodule

module Seg_B (
  input  D3,
  input  D2,
  input  D1,
  input  D0,
  output B
);

  wire and_1_out, and_2_out, and_3_out, and_4_out, and_5_out, and_6_out, not_1_out, not_2_out, not_3_out,
       not_4_out, not_5_out, not_6_out, not_7_out, not_8_out;

  not not_1 (not_1_out, D3);
  not not_2 (not_2_out, D1);
  not not_3 (not_3_out, D3);
  not not_4 (not_4_out, D0);
  not not_5 (not_5_out, D2);
  not not_6 (not_6_out, D1);
  not not_7 (not_7_out, D0);
  not not_8 (not_8_out, D0);
  and and_1 (and_1_out, not_1_out, D2, not_2_out, D0);
  and and_2 (and_2_out, not_3_out, D2, D1, not_4_out);
  and and_3 (and_3_out, D3, not_5_out, D1, D0);
  and and_4 (and_4_out, D3, D2, not_6_out, not_7_out);
  and and_5 (and_5_out, D3, D2, D1, not_8_out);
  and and_6 (and_6_out, D3, D2, D1, D0);
  or or_1 (B, and_1_out, and_2_out, and_3_out, and_4_out, and_5_out, and_6_out);
endmodule

module Seg_C (
  input  D3,
  input  D2,
  input  D1,
  input  D0,
  output C
);

  wire and_1_out, and_2_out, and_3_out, and_4_out, not_1_out, not_2_out, not_3_out, not_4_out, not_5_out,
       not_6_out;

  not not_1 (not_1_out, D3);
  not not_2 (not_2_out, D2);
  not not_3 (not_3_out, D0);
  not not_4 (not_4_out, D1);
  not not_5 (not_5_out, D0);
  not not_6 (not_6_out, D0);
  and and_1 (and_1_out, not_1_out, not_2_out, D1, not_3_out);
  and and_2 (and_2_out, D3, D2, not_4_out, not_5_out);
  and and_3 (and_3_out, D3, D2, D1, not_6_out);
  and and_4 (and_4_out, D3, D2, D1, D0);
  or or_1 (C, and_1_out, and_2_out, and_3_out, and_4_out);
endmodule

module Seg_D (
  input  D3,
  input  D2,
  input  D1,
  input  D0,
  output D
);

  wire and_1_out, and_2_out, and_3_out, and_4_out, and_5_out, not_1_out, not_2_out, not_3_out, not_4_out,
       not_5_out, not_6_out, not_7_out, not_8_out, not_9_out;

  not not_1 (not_1_out, D3);
  not not_2 (not_2_out, D2);
  not not_3 (not_3_out, D1);
  not not_4 (not_4_out, D3);
  not not_5 (not_5_out, D1);
  not not_6 (not_6_out, D0);
  not not_7 (not_7_out, D3);
  not not_8 (not_8_out, D2);
  not not_9 (not_9_out, D0);
  and and_1 (and_1_out, not_1_out, not_2_out, not_3_out, D0);
  and and_2 (and_2_out, not_4_out, D2, not_5_out, not_6_out);
  and and_3 (and_3_out, not_7_out, D2, D1, D0);
  and and_4 (and_4_out, D3, not_8_out, D1, not_9_out);
  and and_5 (and_5_out, D3, D2, D1, D0);
  or or_1 (D, and_1_out, and_2_out, and_3_out, and_4_out, and_5_out);
endmodule

module Seg_E (
  input  D3,
  input  D2,
  input  D1,
  input  D0,
  output E
);

  wire and_1_out, and_2_out, and_3_out, and_4_out, and_5_out, and_6_out, not_1_out, not_2_out, not_3_out,
       not_4_out, not_5_out, not_6_out, not_7_out, not_8_out, not_9_out, not_10_out, not_11_out, not_12_out,
       not_13_out;

  not not_1 (not_1_out, D3);
  not not_2 (not_2_out, D2);
  not not_3 (not_3_out, D1);
  not not_4 (not_4_out, D3);
  not not_5 (not_5_out, D2);
  not not_6 (not_6_out, D3);
  not not_7 (not_7_out, D1);
  not not_8 (not_8_out, D0);
  not not_9 (not_9_out, D3);
  not not_10 (not_10_out, D1);
  not not_11 (not_11_out, D3);
  not not_12 (not_12_out, D2);
  not not_13 (not_13_out, D1);
  and and_1 (and_1_out, not_1_out, not_2_out, not_3_out, D0);
  and and_2 (and_2_out, not_4_out, not_5_out, D1, D0);
  and and_3 (and_3_out, not_6_out, D2, not_7_out, not_8_out);
  and and_4 (and_4_out, not_9_out, D2, not_10_out, D0);
  and and_5 (and_5_out, not_11_out, D2, D1, D0);
  and and_6 (and_6_out, D3, not_12_out, not_13_out, D0);
  or or_1 (E, and_1_out, and_2_out, and_3_out, and_4_out, and_5_out, and_6_out);
endmodule

module Seg_F (
  input  D3,
  input  D2,
  input  D1,
  input  D0,
  output F
);

  wire and_1_out, and_2_out, and_3_out, and_4_out, and_5_out, not_1_out, not_2_out, not_3_out, not_4_out,
       not_5_out, not_6_out, not_7_out, not_8_out, not_9_out, not_10_out;

  not not_1 (not_1_out, D3);
  not not_2 (not_2_out, D2);
  not not_3 (not_3_out, D1);
  not not_4 (not_4_out, D3);
  not not_5 (not_5_out, D2);
  not not_6 (not_6_out, D0);
  not not_7 (not_7_out, D3);
  not not_8 (not_8_out, D2);
  not not_9 (not_9_out, D3);
  not not_10 (not_10_out, D1);
  and and_1 (and_1_out, not_1_out, not_2_out, not_3_out, D0);
  and and_2 (and_2_out, not_4_out, not_5_out, D1, not_6_out);
  and and_3 (and_3_out, not_7_out, not_8_out, D1, D0);
  and and_4 (and_4_out, not_9_out, D2, D1, D0);
  and and_5 (and_5_out, D3, D2, not_10_out, D0);
  or or_1 (F, and_1_out, and_2_out, and_3_out, and_4_out, and_5_out);
endmodule

module Seg_G (
  input  D3,
  input  D2,
  input  D1,
  input  D0,
  output G
);

  wire and_1_out, and_2_out, and_3_out, and_4_out, not_1_out, not_2_out, not_3_out, not_4_out, not_5_out,
       not_6_out, not_7_out, not_8_out, not_9_out, not_10_out;

  not not_1 (not_1_out, D3);
  not not_2 (not_2_out, D2);
  not not_3 (not_3_out, D1);
  not not_4 (not_4_out, D0);
  not not_5 (not_5_out, D3);
  not not_6 (not_6_out, D2);
  not not_7 (not_7_out, D1);
  not not_8 (not_8_out, D3);
  not not_9 (not_9_out, D1);
  not not_10 (not_10_out, D0);
  and and_1 (and_1_out, not_1_out, not_2_out, not_3_out, not_4_out);
  and and_2 (and_2_out, not_5_out, not_6_out, not_7_out, D0);
  and and_3 (and_3_out, not_8_out, D2, D1, D0);
  and and_4 (and_4_out, D3, D2, not_9_out, not_10_out);
  or or_1 (G, and_1_out, and_2_out, and_3_out, and_4_out);
endmodule

module Seg (
  input  in_1,
  input  in_2,
  input  in_3,
  input  in_4,
  output out_5,
  output out_6,
  output out_7,
  output out_8,
  output out_9,
  output out_10,
  output out_11
);

  Seg_A seg_a_1 (.D3(in_1), .D2(in_2), .D1(in_3), .D0(in_4), .A(out_5));
  Seg_B seg_b_1 (.D3(in_1), .D2(in_2), .D1(in_3), .D0(in_4), .B(out_6));
  Seg_C seg_c_1 (.D3(in_1), .D2(in_2), .D1(in_3), .D0(in_4), .C(out_7));
  Seg_D seg_d_1 (.D3(in_1), .D2(in_2), .D1(in_3), .D0(in_4), .D(out_8));
  Seg_E seg_e_1 (.D3(in_1), .D2(in_2), .D1(in_3), .D0(in_4), .E(out_9));
  Seg_F seg_f_1 (.D3(in_1), .D2(in_2), .D1(in_3), .D0(in_4), .F(out_10));
  Seg_G seg_g_1 (.D3(in_1), .D2(in_2), .D1(in_3), .D0(in_4), .G(out_11));
endmodule

module Seg_Example (
  input  in_1,
  input  in_2,
  input  in_3,
  input  in_4,
  input  in_5,
  input  in_6,
  input  in_7,
  input  in_8,
  input  in_9,
  input  in_10,
  input  in_11,
  input  in_12,
  input  in_13,
  input  in_14,
  input  in_15,
  input  in_16,
  input  in_17,
  input  in_18,
  input  in_19,
  input  in_20,
  input  in_21,
  input  in_22,
  input  in_23,
  input  in_24,
  input  in_25,
  input  in_26,
  input  in_27,
  input  in_28,
  input  in_29,
  input  in_30,
  input  in_31,
  input  in_32
);

  wire seg_1_out_5, seg_1_out_6, seg_1_out_7, seg_1_out_8, seg_1_out_9, seg_1_out_10, seg_1_out_11,
       seg_2_out_5, seg_2_out_6, seg_2_out_7, seg_2_out_8, seg_2_out_9, seg_2_out_10, seg_2_out_11,
       seg_3_out_5, seg_3_out_6, seg_3_out_7, seg_3_out_8, seg_3_out_9, seg_3_out_10, seg_3_out_11,
       seg_4_out_5, seg_4_out_6, seg_4_out_7, seg_4_out_8, seg_4_out_9, seg_4_out_10, seg_4_out_11,
       seg_5_out_5, seg_5_out_6, seg_5_out_7, seg_5_out_8, seg_5_out_9, seg_5_out_10, seg_5_out_11,
       seg_6_out_5, seg_6_out_6, seg_6_out_7, seg_6_out_8, seg_6_out_9, seg_6_out_10, seg_6_out_11,
       seg_7_out_5, seg_7_out_6, seg_7_out_7, seg_7_out_8, seg_7_out_9, seg_7_out_10, seg_7_out_11,
       seg_8_out_5, seg_8_out_6, seg_8_out_7, seg_8_out_8, seg_8_out_9, seg_8_out_10, seg_8_out_11;

  Seg seg_1 (
    .in_1(in_1), .in_2(in_3), .in_3(in_5), .in_4(in_7), .out_5(seg_1_out_5), .out_6(seg_1_out_6),
    .out_7(seg_1_out_7), .out_8(seg_1_out_8), .out_9(seg_1_out_9), .out_10(seg_1_out_10),
    .out_11(seg_1_out_11));
  Seg seg_2 (
    .in_1(in_9), .in_2(in_11), .in_3(in_13), .in_4(in_15), .out_5(seg_2_out_5), .out_6(seg_2_out_6),
    .out_7(seg_2_out_7), .out_8(seg_2_out_8), .out_9(seg_2_out_9), .out_10(seg_2_out_10),
    .out_11(seg_2_out_11));
  Seg seg_3 (
    .in_1(in_17), .in_2(in_19), .in_3(in_21), .in_4(in_23), .out_5(seg_3_out_5), .out_6(seg_3_out_6),
    .out_7(seg_3_out_7), .out_8(seg_3_out_8), .out_9(seg_3_out_9), .out_10(seg_3_out_10),
    .out_11(seg_3_out_11));
  Seg seg_4 (
    .in_1(in_25), .in_2(in_27), .in_3(in_29), .in_4(in_31), .out_5(seg_4_out_5), .out_6(seg_4_out_6),
    .out_7(seg_4_out_7), .out_8(seg_4_out_8), .out_9(seg_4_out_9), .out_10(seg_4_out_10),
    .out_11(seg_4_out_11));
  _7_Segment_Display #(.active("false")) u_7_segment_display_1 (
    .g(seg_1_out_11), .f(seg_1_out_10), .a(seg_1_out_5), .b(seg_1_out_6), .e(seg_1_out_9), .d(seg_1_out_8),
    .c(seg_1_out_7), .dp(1'b1));
  _7_Segment_Display #(.active("false")) u_7_segment_display_2 (
    .g(seg_2_out_11), .f(seg_2_out_10), .a(seg_2_out_5), .b(seg_2_out_6), .e(seg_2_out_9), .d(seg_2_out_8),
    .c(seg_2_out_7), .dp(1'b1));
  _7_Segment_Display #(.active("false")) u_7_segment_display_3 (
    .g(seg_3_out_11), .f(seg_3_out_10), .a(seg_3_out_5), .b(seg_3_out_6), .e(seg_3_out_9), .d(seg_3_out_8),
    .c(seg_3_out_7), .dp(1'b1));
  _7_Segment_Display #(.active("false")) u_7_segment_display_4 (
    .g(seg_4_out_11), .f(seg_4_out_10), .a(seg_4_out_5), .b(seg_4_out_6), .e(seg_4_out_9), .d(seg_4_out_8),
    .c(seg_4_out_7), .dp(1'b1));
  Seg seg_5 (
    .in_1(in_2), .in_2(in_4), .in_3(in_6), .in_4(in_8), .out_5(seg_5_out_5), .out_6(seg_5_out_6),
    .out_7(seg_5_out_7), .out_8(seg_5_out_8), .out_9(seg_5_out_9), .out_10(seg_5_out_10),
    .out_11(seg_5_out_11));
  Seg seg_6 (
    .in_1(in_10), .in_2(in_12), .in_3(in_14), .in_4(in_16), .out_5(seg_6_out_5), .out_6(seg_6_out_6),
    .out_7(seg_6_out_7), .out_8(seg_6_out_8), .out_9(seg_6_out_9), .out_10(seg_6_out_10),
    .out_11(seg_6_out_11));
  Seg seg_7 (
    .in_1(in_18), .in_2(in_20), .in_3(in_22), .in_4(in_24), .out_5(seg_7_out_5), .out_6(seg_7_out_6),
    .out_7(seg_7_out_7), .out_8(seg_7_out_8), .out_9(seg_7_out_9), .out_10(seg_7_out_10),
    .out_11(seg_7_out_11));
  Seg seg_8 (
    .in_1(in_26), .in_2(in_28), .in_3(in_30), .in_4(in_32), .out_5(seg_8_out_5), .out_6(seg_8_out_6),
    .out_7(seg_8_out_7), .out_8(seg_8_out_8), .out_9(seg_8_out_9), .out_10(seg_8_out_10),
    .out_11(seg_8_out_11));
  _7_Segment_Display #(.active("false")) u_7_segment_display_5 (
    .g(seg_5_out_11), .f(seg_5_out_10), .a(seg_5_out_5), .b(seg_5_out_6), .e(seg_5_out_9), .d(seg_5_out_8),
    .c(seg_5_out_7), .dp(1'b1));
  _7_Segment_Display #(.active("false")) u_7_segment_display_6 (
    .g(seg_6_out_11), .f(seg_6_out_10), .a(seg_6_out_5), .b(seg_6_out_6), .e(seg_6_out_9), .d(seg_6_out_8),
    .c(seg_6_out_7), .dp(1'b1));
  _7_Segment_Display #(.active("false")) u_7_segment_display_7 (
    .g(seg_7_out_11), .f(seg_7_out_10), .a(seg_7_out_5), .b(seg_7_out_6), .e(seg_7_out_9), .d(seg_7_out_8),
    .c(seg_7_out_7), .dp(1'b1));
  _7_Segment_Display #(.active("false")) u_7_segment_display_8 (
    .g(seg_8_out_11), .f(seg_8_out_10), .a(seg_8_out_5), .b(seg_8_out_6), .e(seg_8_out_9), .d(seg_8_out_8),
    .c(seg_8_out_7), .dp(1'b1));
endmodule
