// Logisim project yutiancomputer.circ as structural Verilog: 8 circuits, main circuit main
module main (
  input  in_1,
  input  in_2,
  input  [5:0] in_3,
  input  [15:0] in_4,
  input  [15:0] in_5,
  input  [15:0] in_6
);

  wire button_1_out;
  wire [15:0] multiplier_1_out, rom_1_out_6;

  // Probe on in_5
  // Probe on in_6
  Button button_1 (.out(button_1_out));
  Multiplier #(.width(16)) multiplier_1 (.a(in_5), .b(in_6), .out(multiplier_1_out));  // open: cin, cout
  rom rom_1 (.in_3(in_3), .in_4(in_4), .out_6(rom_1_out_6), .in_1(in_2), .in_2(in_1), .in_5(button_1_out));
  // Probe on multiplier_1_out
  // Probe on multiplier_1_out
  // Probe on rom_1_out_6
endmodule

module single_rom (
  input  in_1,
  input  in_2,
  input  [15:0] in_3,
  input  [2:0] in_4,
  input  in_5,
  output [15:0] out_6
);

  wire and_1_out, and_2_out, and_3_out, and_4_out, and_5_out, and_6_out, and_7_out, and_8_out, and_9_out,
       and_10_out, and_11_out, and_12_out, and_13_out, and_14_out, and_15_out, and_16_out, and_17_out,
       decoder_1_out0, decoder_1_out1, decoder_1_out2, decoder_1_out3, decoder_1_out4, decoder_1_out5,
       decoder_1_out6, decoder_1_out7, not_1_out;
  wire [15:0] controlled_buffer_1_out, controlled_buffer_2_out, controlled_buffer_4_out,
       controlled_buffer_7_out, controlled_buffer_8_out, controlled_buffer_11_out, controlled_buffer_12_out,
       controlled_buffer_14_out, controlled_buffer_17_out, register_1_q, register_2_q, register_3_q,
       register_4_q, register_5_q, register_6_q, register_7_q, register_8_q;

  assign controlled_buffer_1_out = not_1_out ? in_3 : 16'bz;  // Controlled_Buffer controlled_buffer_1
  Decoder #(.select(3)) decoder_1 (
    .out0(decoder_1_out0), .out1(decoder_1_out1), .out2(decoder_1_out2), .out3(decoder_1_out3),
    .out4(decoder_1_out4), .out5(decoder_1_out5), .out6(decoder_1_out6), .out7(decoder_1_out7), .sel(in_4),
    .en(in_1));
  not not_1 (not_1_out, in_2);
  and and_1 (and_1_out, not_1_out, decoder_1_out0);
  assign controlled_buffer_2_out = and_1_out ? controlled_buffer_1_out : 16'bz;  // Controlled_Buffer controlled_buffer_2
  assign controlled_buffer_1_out = and_2_out ? register_1_q : 16'bz;  // Controlled_Buffer controlled_buffer_3
  and and_2 (and_2_out, in_2, decoder_1_out0);
  Register #(.width(16)) register_1 (.D(controlled_buffer_2_out), .Q(register_1_q), .clk(in_5));  // open: en, clr
  and and_3 (and_3_out, not_1_out, decoder_1_out1);
  assign controlled_buffer_4_out = and_3_out ? controlled_buffer_1_out : 16'bz;  // Controlled_Buffer controlled_buffer_4
  assign controlled_buffer_1_out = and_4_out ? register_2_q : 16'bz;  // Controlled_Buffer controlled_buffer_5
  and and_4 (and_4_out, in_2, decoder_1_out1);
  Register #(.width(16)) register_2 (.D(controlled_buffer_4_out), .Q(register_2_q), .clk(in_5));  // open: en, clr
  assign controlled_buffer_1_out = and_6_out ? register_3_q : 16'bz;  // Controlled_Buffer controlled_buffer_6
  and and_5 (and_5_out, not_1_out, decoder_1_out2);
  assign controlled_buffer_7_out = and_5_out ? controlled_buffer_1_out : 16'bz;  // Controlled_Buffer controlled_buffer_7
  Register #(.width(16)) register_3 (.D(controlled_buffer_7_out), .Q(register_3_q), .clk(in_5));  // open: en, clr
  and and_6 (and_6_out, in_2, decoder_1_out2);
  and and_7 (and_7_out, not_1_out, decoder_1_out3);
  assign controlled_buffer_8_out = and_7_out ? controlled_buffer_1_out : 16'bz;  // Controlled_Buffer controlled_buffer_8
  assign controlled_buffer_1_out = and_8_out ? register_4_q : 16'bz;  // Controlled_Buffer controlled_buffer_9
  and and_8 (and_8_out, in_2, decoder_1_out3);
  Register #(.width(16)) register_4 (.D(controlled_buffer_8_out), .Q(register_4_q), .clk(in_5));  // open: en, clr
  and and_9 (and_9_out, not_1_out, decoder_1_out4);
  assign controlled_buffer_1_out = and_10_out ? register_5_q : 16'bz;  // Controlled_Buffer controlled_buffer_10
  and and_10 (and_10_out, in_2, decoder_1_out4);
  assign controlled_buffer_11_out = and_9_out ? controlled_buffer_1_out : 16'bz;  // Controlled_Buffer controlled_buffer_11
  Register #(.width(16)) register_5 (.D(controlled_buffer_11_out), .Q(register_5_q), .clk(in_5));  // open: en, clr
  and and_11 (and_11_out, not_1_out, decoder_1_out5);
  assign controlled_buffer_12_out = and_11_out ? controlled_buffer_1_out : 16'bz;  // Controlled_Buffer controlled_buffer_12
  Register #(.width(16)) register_6 (.D(controlled_buffer_12_out), .Q(register_6_q), .clk(in_5));  // open: en, clr
  assign controlled_buffer_1_out = and_12_out ? register_6_q : 16'bz;  // Controlled_Buffer controlled_buffer_13
  and and_12 (and_12_out, in_2, decoder_1_out5);
  and and_13 (and_13_out, not_1_out, decoder_1_out6);
  assign controlled_buffer_14_out = and_13_out ? controlled_buffer_1_out : 16'bz;  // Controlled_Buffer controlled_buffer_14
  assign controlled_buffer_1_out = and_14_out ? register_7_q : 16'bz;  // Controlled_Buffer controlled_buffer_15
  and and_14 (and_14_out, in_2, decoder_1_out6);
  Register #(.width(16)) register_7 (.D(controlled_buffer_14_out), .Q(register_7_q), .clk(in_5));  // open: en, clr
  assign controlled_buffer_1_out = and_16_out ? register_8_q : 16'bz;  // Controlled_Buffer controlled_buffer_16
  and and_15 (and_15_out, not_1_out, decoder_1_out7);
  and and_16 (and_16_out, in_2, decoder_1_out7);
  assign controlled_buffer_17_out = and_15_out ? controlled_buffer_1_out : 16'bz;  // Controlled_Buffer controlled_buffer_17
  Register #(.width(16)) register_8 (.D(controlled_buffer_17_out), .Q(register_8_q), .clk(in_5));  // open: en, clr
  assign out_6 = and_17_out ? controlled_buffer_1_out : 16'bz;  // Controlled_Buffer controlled_buffer_18
  and and_17 (and_17_out, in_1, in_2);
endmodule

module rom (
  input  in_1,
  input  in_2,
  input  [5:0] in_3,
  input  [15:0] in_4,
  input  in_5,
  output [15:0] out_6
);

  wire and_1_out, and_2_out, decoder_1_out0, decoder_1_out1, decoder_1_out2, decoder_1_out3, decoder_1_out4,
       decoder_1_out5, decoder_1_out6, decoder_1_out7, not_1_out;
  wire [15:0] controlled_buffer_1_out, single_rom_1_out_6;

  and and_1 (and_1_out, not_1_out, in_1);
  and and_2 (and_2_out, in_1, in_2);
  Decoder #(.select(3)) decoder_1 (
    .out0(decoder_1_out0), .out1(decoder_1_out1), .out2(decoder_1_out2), .out3(decoder_1_out3),
    .out4(decoder_1_out4), .out5(decoder_1_out5), .out6(decoder_1_out6), .out7(decoder_1_out7),
    .sel(in_3[5:3]), .en(in_1));
  assign controlled_buffer_1_out = and_1_out ? in_4 : 16'bz;  // Controlled_Buffer controlled_buffer_1
  not not_1 (not_1_out, and_2_out);
  single_rom single_rom_1 (
    .in_3(controlled_buffer_1_out), .in_4(in_3[2:0]), .out_6(single_rom_1_out_6), .in_1(decoder_1_out0),
    .in_2(and_2_out), .in_5(in_5));
  single_rom single_rom_2 (
    .in_3(controlled_buffer_1_out), .in_4(in_3[2:0]), .out_6(single_rom_1_out_6), .in_1(decoder_1_out1),
    .in_2(and_2_out), .in_5(in_5));
  single_rom single_rom_3 (
    .in_3(controlled_buffer_1_out), .in_4(in_3[2:0]), .out_6(single_rom_1_out_6), .in_1(decoder_1_out2),
    .in_2(and_2_out), .in_5(in_5));
  single_rom single_rom_4 (
    .in_3(controlled_buffer_1_out), .in_4(in_3[2:0]), .out_6(single_rom_1_out_6), .in_1(decoder_1_out3),
    .in_2(and_2_out), .in_5(in_5));
  single_rom single_rom_5 (
    .in_3(controlled_buffer_1_out), .in_4(in_3[2:0]), .out_6(single_rom_1_out_6), .in_1(decoder_1_out4),
    .in_2(and_2_out), .in_5(in_5));
  single_rom single_rom_6 (
    .in_3(controlled_buffer_1_out), .in_4(in_3[2:0]), .out_6(single_rom_1_out_6), .in_1(decoder_1_out5),
    .in_2(and_2_out), .in_5(in_5));
  single_rom single_rom_7 (
    .in_3(controlled_buffer_1_out), .in_4(in_3[2:0]), .out_6(single_rom_1_out_6), .in_1(decoder_1_out6),
    .in_2(and_2_out), .in_5(in_5));
  single_rom single_rom_8 (
    .in_3(controlled_buffer_1_out), .in_4(in_3[2:0]), .out_6(single_rom_1_out_6), .in_1(decoder_1_out7),
    .in_2(and_2_out), .in_5(in_5));
  assign out_6 = and_2_out ? single_rom_1_out_6 : 16'bz;  // Controlled_Buffer controlled_buffer_2
endmodule

module _16cach (
  input  [15:0] in_1,
  input  in_2,
  output [15:0] out_3
);

  Register #(.width(16)) register_1 (.D(in_1), .Q(out_3), .clk(in_2));  // open: en, clr
endmodule

module alu (
  input  [15:0] in_1,
  input  in_2,
  input  in_3,
  input  in_4,
  input  in_5,
  input  in_6,
  input  in_7,
  input  in_8,
  input  in_9,
  input  in_10,
  input  in_11,
  input  in_12,
  input  in_13,
  input  in_14,
  output out_15,
  output out_16,
  output out_17,
  output out_18,
  output out_19,
  output [15:0] out_20
);

  wire comparator_1_eq, comparator_1_gt, comparator_1_lt;
  wire [15:0] adder_1_out, controlled_buffer_1_out, controlled_buffer_3_out, divider_1_out, multiplier_1_out,
       negator_1_out, register_1_q, register_2_q, register_3_q, shifter_1_out, subtractor_1_out;

  assign controlled_buffer_1_out = in_3 ? in_1 : 16'bz;  // Controlled_Buffer controlled_buffer_1
  assign controlled_buffer_1_out = in_2 ? controlled_buffer_3_out : 16'bz;  // Controlled_Buffer controlled_buffer_2
  Register #(.width(16)) register_1 (.D(controlled_buffer_1_out), .Q(register_1_q), .clk(in_4));  // open: en, clr
  Register #(.width(16)) register_2 (.D(register_1_q), .Q(register_2_q), .clk(in_5));  // open: en, clr
  Register #(.width(16)) register_3 (.D(register_1_q), .Q(register_3_q), .clk(in_6));  // open: en, clr
  Adder #(.width(16)) adder_1 (.a(register_2_q), .b(register_3_q), .out(adder_1_out), .cout(out_15));  // open: cin
  Subtractor #(.width(16)) subtractor_1 (
    .a(register_2_q), .b(register_3_q), .out(subtractor_1_out), .bout(out_16));  // open: bin
  Multiplier #(.width(16)) multiplier_1 (
    .a(register_2_q), .b(register_3_q), .out(multiplier_1_out));  // open: cin, cout
  Divider #(.width(16)) divider_1 (.a(register_2_q), .b(register_3_q), .out(divider_1_out));  // open: upper, rem
  Negator #(.width(16)) negator_1 (.in(register_2_q), .out(negator_1_out));
  Comparator #(.width(16)) comparator_1 (
    .a(register_2_q), .b(register_3_q), .gt(comparator_1_gt), .eq(comparator_1_eq), .lt(comparator_1_lt));
  Shifter #(.width(16)) shifter_1 (.in(register_2_q), .\dist (register_3_q[3:0]), .out(shifter_1_out));
  assign controlled_buffer_3_out = in_8 ? adder_1_out : 16'bz;  // Controlled_Buffer controlled_buffer_3
  assign controlled_buffer_3_out = in_9 ? subtractor_1_out : 16'bz;  // Controlled_Buffer controlled_buffer_4
  assign controlled_buffer_3_out = in_10 ? multiplier_1_out : 16'bz;  // Controlled_Buffer controlled_buffer_5
  assign controlled_buffer_3_out = in_11 ? divider_1_out : 16'bz;  // Controlled_Buffer controlled_buffer_6
  assign controlled_buffer_3_out = in_12 ? negator_1_out : 16'bz;  // Controlled_Buffer controlled_buffer_7
  assign out_17 = in_7 ? comparator_1_gt : 1'bz;  // Controlled_Buffer controlled_buffer_8
  assign out_18 = in_7 ? comparator_1_eq : 1'bz;  // Controlled_Buffer controlled_buffer_9
  assign out_19 = in_7 ? comparator_1_lt : 1'bz;  // Controlled_Buffer controlled_buffer_10
  assign controlled_buffer_3_out = in_13 ? shifter_1_out : 16'bz;  // Controlled_Buffer controlled_buffer_11
  assign out_20 = in_14 ? register_1_q : 16'bz;  // Controlled_Buffer controlled_buffer_12
endmodule

module pc (
  input  in_1,
  input  [5:0] in_2,
  input  in_3,
  input  in_4,
  output [5:0] out_5
);

  wire clock_1_out, counter_1_carry;

  Counter #(.width(6), .max('h3f)) counter_1 (
    .load(in_1), .D(in_2), .count(in_3), .Q(out_5), .carry(counter_1_carry), .clk(clock_1_out), .clr(in_4));
  Clock clock_1 (.out(clock_1_out));
endmodule

module controller (
  input  [5:0] in_1,
  input  [2:0] in_2,
  input  [15:0] in_3,
  output out_4,
  output out_5,
  output out_6,
  output out_7,
  output out_8,
  output out_9,
  output out_10,
  output out_11,
  output out_12,
  output out_13,
  output out_14,
  output out_15,
  output out_16,
  output [5:0] out_17
);

  wire clock_1_out, comparator_1_eq, comparator_2_eq, comparator_3_eq, undriven, undriven_2, undriven_3,
       undriven_4, undriven_5, undriven_6;
  wire [2:0] register_2_q;
  wire [3:0] counter_1_q;
  wire [5:0] register_1_q;
  wire [15:0] register_3_q;
  wire [19:0] controlled_buffer_5_out, rom_1_data;

  Clock clock_1 (.out(clock_1_out));
  Register #(.width(6)) register_1 (.D(in_1), .Q(register_1_q), .clk(undriven_4));  // open: en, clr
  Register #(.width(3)) register_2 (.D(in_2), .Q(register_2_q), .clk(undriven_2));  // open: en, clr
  Register #(.width(16)) register_3 (.D(in_3), .Q(register_3_q), .clk(undriven_4));  // open: en, clr
  Counter #(.width(4), .max('hf)) counter_1 (
    .count(undriven), .Q(counter_1_q), .clk(clock_1_out), .clr(undriven_3));  // open: load, D, carry
  // Probe on register_3_q[15:10]
  Comparator #(.width(6)) comparator_1 (.a(register_3_q[15:10]), .b({6{1'b0}}), .eq(comparator_1_eq));  // open: gt, lt
  assign out_7 = undriven_5 ? comparator_2_eq : 1'bz;  // Controlled_Buffer controlled_buffer_1
  assign out_8 = undriven_5 ? comparator_3_eq : 1'bz;  // Controlled_Buffer controlled_buffer_2
  Comparator #(.width(4)) comparator_2 (.a(register_3_q[9:6]), .b(4'b0001), .eq(comparator_2_eq));  // open: gt, lt
  Comparator #(.width(4)) comparator_3 (.a(register_3_q[9:6]), .b(4'b0010), .eq(comparator_3_eq));  // open: gt, lt
  // alu alu_1: pin names not known; wires that end beside it: out_4, out_5, out_6, out_9, out_10, out_11, out_12, out_13
  Controlled_Buffer #(.width(6)) controlled_buffer_3 (.in(register_1_q), .out(out_17));  // open: en
  assign out_17 = undriven_6 ? register_3_q[5:0] : 6'bz;  // Controlled_Buffer controlled_buffer_4
  ROM #(.addrWidth(4), .dataWidth(20)) rom_1 (.addr(counter_1_q), .data(rom_1_data), .sel(comparator_1_eq));
  assign controlled_buffer_5_out = comparator_1_eq ? rom_1_data : 20'bz;  // Controlled_Buffer controlled_buffer_5
  rom rom_2 ();  // open: in_3, in_4, out_6, in_1, in_2, in_5

  // Notes on the sheet:
  //   LOAD
endmodule

module jump (
  input  in_1,
  input  in_2,
  input  in_3,
  input  in_4,
  input  in_5,
  input  in_6,
  input  in_7,
  input  in_8,
  input  in_9,
  output out_10
);
endmodule
