// Logisim project 加法器.circ as structural Verilog
module \半加器  (
  input  in_1,
  input  in_2,
  output out_3,
  output out_4
);

  wire and_1_out, and_2_out, not_1_out, not_2_out;

  not not_1 (not_1_out, in_1);
  not not_2 (not_2_out, in_2);
  and and_1 (and_1_out, not_1_out, in_2);
  and and_2 (and_2_out, in_1, not_2_out);
  and and_3 (out_4, in_2, in_1);
  or or_1 (out_3, and_1_out, and_2_out);
endmodule

module \全加  (
  input  in_1,
  input  in_2,
  input  in_3,
  output out_4,
  output out_5
);

  wire \半加器_1_out_3 , \半加器_1_out_4 , \半加器_2_out_4 ;

  \半加器  \u_半加器_1  (.in_1(in_2), .in_2(in_3), .out_3(\半加器_1_out_3 ), .out_4(\半加器_1_out_4 ));
  \半加器  \u_半加器_2  (.in_1(in_1), .in_2(\半加器_1_out_3 ), .out_3(out_4), .out_4(\半加器_2_out_4 ));
  or or_1 (out_5, \半加器_2_out_4 , \半加器_1_out_4 );
endmodule

module \_8加法  (
  input  in_1,
  input  in_2,
  input  in_3,
  input  in_4,
  input  in_5,
  input  in_6,
  input  in_7,
  input  in_8,
  input  in_9,
  input  in_10,
  input  in_11,
  input  in_12,
  input  in_13,
  input  in_14,
  input  in_15,
  input  in_16,
  output out_17,
  output out_18,
  output out_19,
  output out_20,
  output out_21,
  output out_22,
  output out_23,
  output out_24,
  output out_25
);

  wire \全加_1_out_5 , \全加_2_out_5 , \全加_3_out_5 , \全加_4_out_5 , \全加_5_out_5 , \全加_6_out_5 , \全加_7_out_5 ;

  \全加  \u_全加_1  (.in_1(in_7), .in_2(\全加_2_out_5 ), .in_3(in_15), .out_4(out_24), .out_5(\全加_1_out_5 ));
  \全加  \u_全加_2  (.in_1(1'b0), .in_2(in_8), .in_3(in_16), .out_4(out_25), .out_5(\全加_2_out_5 ));
  \全加  \u_全加_3  (.in_1(\全加_4_out_5 ), .in_2(in_5), .in_3(in_13), .out_4(out_22), .out_5(\全加_3_out_5 ));
  \全加  \u_全加_4  (.in_1(\全加_1_out_5 ), .in_2(in_6), .in_3(in_14), .out_4(out_23), .out_5(\全加_4_out_5 ));
  \全加  \u_全加_5  (.in_1(\全加_3_out_5 ), .in_2(in_4), .in_3(in_12), .out_4(out_21), .out_5(\全加_5_out_5 ));
  \全加  \u_全加_6  (.in_1(\全加_7_out_5 ), .in_2(in_2), .in_3(in_10), .out_4(out_19), .out_5(\全加_6_out_5 ));
  \全加  \u_全加_7  (.in_1(\全加_5_out_5 ), .in_2(in_3), .in_3(in_11), .out_4(out_20), .out_5(\全加_7_out_5 ));
  \全加  \u_全加_8  (.in_1(\全加_6_out_5 ), .in_2(in_1), .in_3(in_9), .out_4(out_18), .out_5(out_17));
endmodule

module alu (
  output out_1
);

  wire c8_1_out_10, c8_1_out_11, c8_1_out_12, c8_1_out_13, c8_1_out_14, c8_1_out_15, c8_1_out_16,
       c8_1_out_17, c8_3_out_10, c8_3_out_11, c8_3_out_12, c8_3_out_13, c8_3_out_14, c8_3_out_15,
       c8_3_out_16, c8_3_out_17, c8_4_out_10, c8_4_out_11, c8_4_out_12, c8_4_out_13, c8_4_out_14,
       c8_4_out_15, c8_4_out_16, c8_4_out_17, c8_5_out_10, c8_5_out_11, c8_5_out_12, c8_5_out_13,
       c8_5_out_14, c8_5_out_15, c8_5_out_16, c8_5_out_17, c8_6_out_10, c8_6_out_11, c8_6_out_12,
       c8_6_out_13, c8_6_out_14, c8_6_out_15, c8_6_out_16, c8_6_out_17, \n8加法_1_out_18 , \n8加法_1_out_19 ,
       \n8加法_1_out_20 , \n8加法_1_out_21 , \n8加法_1_out_22 , \n8加法_1_out_23 , \n8加法_1_out_24 , \n8加法_1_out_25 ;

  C8 c8_1 (
    .in_2(c8_3_out_17), .in_3(c8_3_out_16), .in_4(c8_3_out_15), .in_5(c8_3_out_14), .in_6(c8_3_out_13),
    .in_7(c8_3_out_12), .in_8(c8_3_out_11), .in_9(c8_3_out_10), .out_10(c8_1_out_10), .out_11(c8_1_out_11),
    .out_12(c8_1_out_12), .out_13(c8_1_out_13), .out_14(c8_1_out_14), .out_15(c8_1_out_15),
    .out_16(c8_1_out_16), .out_17(c8_1_out_17));  // open: in_1
  C8 c8_2 (
    .in_2(\n8加法_1_out_25 ), .in_3(\n8加法_1_out_24 ), .in_4(\n8加法_1_out_23 ), .in_5(\n8加法_1_out_22 ),
    .in_6(\n8加法_1_out_21 ), .in_7(\n8加法_1_out_20 ), .in_8(\n8加法_1_out_19 ), .in_9(\n8加法_1_out_18 ),
    .out_10(c8_1_out_17), .out_11(c8_1_out_16), .out_12(c8_1_out_15), .out_13(c8_1_out_14),
    .out_14(c8_1_out_13), .out_15(c8_1_out_12), .out_16(c8_1_out_11), .out_17(c8_1_out_10));  // open: in_1
  C8 c8_3 (
    .in_2(c8_5_out_17), .in_3(c8_5_out_16), .in_4(c8_5_out_15), .in_5(c8_5_out_14), .in_6(c8_5_out_13),
    .in_7(c8_5_out_12), .in_8(c8_5_out_11), .in_9(c8_5_out_10), .out_10(c8_3_out_10), .out_11(c8_3_out_11),
    .out_12(c8_3_out_12), .out_13(c8_3_out_13), .out_14(c8_3_out_14), .out_15(c8_3_out_15),
    .out_16(c8_3_out_16), .out_17(c8_3_out_17));  // open: in_1
  \_8加法  \u_8加法_1  (
    .in_1(c8_4_out_10), .in_2(c8_4_out_11), .in_3(c8_4_out_12), .in_4(c8_4_out_13), .in_5(c8_4_out_14),
    .in_6(c8_4_out_15), .in_7(c8_4_out_16), .in_8(c8_4_out_17), .in_9(c8_6_out_10), .in_10(c8_6_out_11),
    .in_11(c8_6_out_12), .in_12(c8_6_out_13), .in_13(c8_6_out_14), .in_14(c8_6_out_15), .in_15(c8_6_out_16),
    .in_16(c8_6_out_17), .out_17(out_1), .out_18(\n8加法_1_out_18 ), .out_19(\n8加法_1_out_19 ),
    .out_20(\n8加法_1_out_20 ), .out_21(\n8加法_1_out_21 ), .out_22(\n8加法_1_out_22 ), .out_23(\n8加法_1_out_23 ),
    .out_24(\n8加法_1_out_24 ), .out_25(\n8加法_1_out_25 ));
  C8 c8_4 (
    .in_2(c8_5_out_10), .in_3(c8_5_out_11), .in_4(c8_5_out_12), .in_5(c8_5_out_13), .in_6(c8_5_out_14),
    .in_7(c8_5_out_15), .in_8(c8_5_out_16), .in_9(c8_5_out_17), .out_10(c8_4_out_10), .out_11(c8_4_out_11),
    .out_12(c8_4_out_12), .out_13(c8_4_out_13), .out_14(c8_4_out_14), .out_15(c8_4_out_15),
    .out_16(c8_4_out_16), .out_17(c8_4_out_17));  // open: in_1
  C8 c8_5 (
    .in_2(c8_1_out_17), .in_3(c8_1_out_16), .in_4(c8_1_out_15), .in_5(c8_1_out_14), .in_6(c8_1_out_13),
    .in_7(c8_1_out_12), .in_8(c8_1_out_11), .in_9(c8_1_out_10), .out_10(c8_5_out_10), .out_11(c8_5_out_11),
    .out_12(c8_5_out_12), .out_13(c8_5_out_13), .out_14(c8_5_out_14), .out_15(c8_5_out_15),
    .out_16(c8_5_out_16), .out_17(c8_5_out_17));  // open: in_1
  C8 c8_6 (
    .in_2(c8_5_out_10), .in_3(c8_5_out_11), .in_4(c8_5_out_12), .in_5(c8_5_out_13), .in_6(c8_5_out_14),
    .in_7(c8_5_out_15), .in_8(c8_5_out_16), .in_9(c8_5_out_17), .out_10(c8_6_out_10), .out_11(c8_6_out_11),
    .out_12(c8_6_out_12), .out_13(c8_6_out_13), .out_14(c8_6_out_14), .out_15(c8_6_out_15),
    .out_16(c8_6_out_16), .out_17(c8_6_out_17));  // open: in_1
endmodule

module \验证  (
  input  in_1,
  input  in_2,
  input  in_3,
  input  in_4,
  input  in_5,
  input  in_6,
  input  in_7,
  input  in_8,
  input  in_9,
  input  in_10,
  input  in_11,
  input  in_12,
  input  in_13,
  input  in_14,
  input  in_15,
  input  in_16,
  input  in_17,
  input  in_18,
  input  in_19,
  input  in_20,
  input  in_21,
  input  in_22,
  input  in_23,
  input  in_24,
  input  in_25,
  input  in_26,
  input  in_27,
  input  in_28,
  input  in_29,
  input  in_30,
  input  in_31,
  input  in_32,
  input  in_33,
  input  in_34,
  output out_35
);

  wire c8_1_out_10, c8_1_out_11, c8_1_out_12, c8_1_out_13, c8_1_out_14, c8_1_out_15, c8_1_out_16,
       c8_1_out_17, clock_1_out, double_16key_1_out_37, double_16key_1_out_38, double_16key_1_out_39,
       double_16key_1_out_40, double_16key_1_out_41, double_16key_1_out_42, double_16key_1_out_43,
       double_16key_1_out_44, n2seg_1_out_10, n2seg_1_out_11, n2seg_1_out_12, n2seg_1_out_13, n2seg_1_out_14,
       n2seg_1_out_15, n2seg_1_out_16, n2seg_1_out_17, n2seg_1_out_18, n2seg_1_out_19, n2seg_1_out_20,
       n2seg_1_out_21, n2seg_1_out_22, n2seg_1_out_23, \n4_16译码器_1_out_5 , \n4_16译码器_1_out_6 ,
       \n4_16译码器_1_out_7 , \n4_16译码器_1_out_8 , \n4_16译码器_1_out_9 , \n4_16译码器_1_out_10 , \n4_16译码器_1_out_11 ,
       \n4_16译码器_1_out_12 , \n4_16译码器_1_out_13 , \n4_16译码器_1_out_14 , \n4_16译码器_1_out_15 ,
       \n4_16译码器_1_out_16 , \n4_16译码器_1_out_17 , \n4_16译码器_1_out_18 , \n4_16译码器_1_out_19 ,
       \n4_16译码器_1_out_20 , \n8加法_1_out_18 , \n8加法_1_out_19 , \n8加法_1_out_20 , \n8加法_1_out_21 ,
       \n8加法_1_out_22 , \n8加法_1_out_23 , \n8加法_1_out_24 , \n8加法_1_out_25 , or_1_out, or_2_out, reg8_1_out_10,
       reg8_1_out_11, reg8_1_out_12, reg8_1_out_13, reg8_1_out_14, reg8_1_out_15, reg8_1_out_16,
       reg8_1_out_17, reg8_2_out_10, reg8_2_out_11, reg8_2_out_12, reg8_2_out_13, reg8_2_out_14,
       reg8_2_out_15, reg8_2_out_16, reg8_2_out_17, reg8_3_out_10, reg8_3_out_11, reg8_3_out_12,
       reg8_3_out_13, reg8_3_out_14, reg8_3_out_15, reg8_3_out_16, reg8_3_out_17, s_r_ff_1_q, s_r_ff_2_q,
       s_r_ff_3_q, s_r_ff_4_q, s_r_ff_5_q, s_r_ff_6_q, s_r_ff_7_q, s_r_ff_8_q, s_r_ff_9_q;
  wire [3:0] counter_1_q;

  double_16key double_16key_1 (
    .in_1(in_1), .in_2(in_2), .in_3(in_3), .in_4(in_4), .in_5(in_5), .in_6(in_6), .in_7(in_7), .in_8(in_8),
    .in_9(in_9), .in_12(in_10), .in_13(in_11), .in_14(in_12), .in_15(in_13), .in_16(in_14), .in_17(in_15),
    .in_18(in_16), .in_19(in_17), .in_20(in_18), .in_21(in_19), .in_22(in_20), .in_23(in_21), .in_24(in_22),
    .in_25(in_23), .in_26(in_26), .in_27(in_27), .in_28(in_28), .in_29(in_29), .in_32(in_30), .in_33(in_31),
    .in_34(in_32), .in_35(in_33), .in_36(in_34), .out_37(double_16key_1_out_37),
    .out_38(double_16key_1_out_38), .out_39(double_16key_1_out_39), .out_40(double_16key_1_out_40),
    .out_41(double_16key_1_out_41), .out_42(double_16key_1_out_42), .out_43(double_16key_1_out_43),
    .out_44(double_16key_1_out_44), .in_10(s_r_ff_2_q), .in_11(s_r_ff_1_q), .in_30(in_24), .in_31(in_25));
  LED led_1 (.in(double_16key_1_out_37));
  LED led_2 (.in(double_16key_1_out_38));
  LED led_3 (.in(double_16key_1_out_41));
  LED led_4 (.in(double_16key_1_out_42));
  LED led_5 (.in(double_16key_1_out_39));
  LED led_6 (.in(double_16key_1_out_40));
  LED led_7 (.in(double_16key_1_out_43));
  LED led_8 (.in(double_16key_1_out_44));
  C8 c8_1 (
    .in_2(double_16key_1_out_44), .in_3(double_16key_1_out_43), .in_4(double_16key_1_out_42),
    .in_5(double_16key_1_out_41), .in_6(double_16key_1_out_40), .in_7(double_16key_1_out_39),
    .in_8(double_16key_1_out_38), .in_9(double_16key_1_out_37), .out_10(c8_1_out_10), .out_11(c8_1_out_11),
    .out_12(c8_1_out_12), .out_13(c8_1_out_13), .out_14(c8_1_out_14), .out_15(c8_1_out_15),
    .out_16(c8_1_out_16), .out_17(c8_1_out_17), .in_1(s_r_ff_3_q));
  S_R_Flip_Flop s_r_ff_1 (
    .Q(s_r_ff_1_q), .preset(\n4_16译码器_1_out_8 ), .reset(\n4_16译码器_1_out_10 ));  // open: S, clk, R, Qn, en
  S_R_Flip_Flop s_r_ff_2 (
    .Q(s_r_ff_2_q), .preset(\n4_16译码器_1_out_5 ), .reset(\n4_16译码器_1_out_7 ));  // open: S, clk, R, Qn, en
  S_R_Flip_Flop s_r_ff_3 (
    .Q(s_r_ff_3_q), .preset(\n4_16译码器_1_out_5 ), .reset(\n4_16译码器_1_out_11 ));  // open: S, clk, R, Qn, en
  C8 c8_2 (
    .in_2(\n8加法_1_out_25 ), .in_3(\n8加法_1_out_24 ), .in_4(\n8加法_1_out_23 ), .in_5(\n8加法_1_out_22 ),
    .in_6(\n8加法_1_out_21 ), .in_7(\n8加法_1_out_20 ), .in_8(\n8加法_1_out_19 ), .in_9(\n8加法_1_out_18 ),
    .out_10(c8_1_out_17), .out_11(c8_1_out_16), .out_12(c8_1_out_15), .out_13(c8_1_out_14),
    .out_14(c8_1_out_13), .out_15(c8_1_out_12), .out_16(c8_1_out_11), .out_17(c8_1_out_10), .in_1(s_r_ff_6_q));
  C8 c8_3 (
    .in_2(reg8_2_out_17), .in_3(reg8_2_out_16), .in_4(reg8_2_out_15), .in_5(reg8_2_out_14),
    .in_6(reg8_2_out_13), .in_7(reg8_2_out_12), .in_8(reg8_2_out_11), .in_9(reg8_2_out_10),
    .out_10(double_16key_1_out_37), .out_11(double_16key_1_out_38), .out_12(double_16key_1_out_39),
    .out_13(double_16key_1_out_40), .out_14(double_16key_1_out_41), .out_15(double_16key_1_out_42),
    .out_16(double_16key_1_out_43), .out_17(double_16key_1_out_44), .in_1(s_r_ff_4_q));
  S_R_Flip_Flop s_r_ff_4 (
    .Q(s_r_ff_4_q), .preset(\n4_16译码器_1_out_14 ), .reset(\n4_16译码器_1_out_20 ));  // open: S, clk, R, Qn, en
  _2seg u_2seg_1 (
    .in_2(double_16key_1_out_37), .in_3(double_16key_1_out_38), .in_4(double_16key_1_out_39),
    .in_5(double_16key_1_out_40), .in_6(double_16key_1_out_41), .in_7(double_16key_1_out_42),
    .in_8(double_16key_1_out_43), .in_9(double_16key_1_out_44), .out_10(n2seg_1_out_10),
    .out_11(n2seg_1_out_11), .out_12(n2seg_1_out_12), .out_13(n2seg_1_out_13), .out_14(n2seg_1_out_14),
    .out_15(n2seg_1_out_15), .out_16(n2seg_1_out_16), .out_17(n2seg_1_out_17), .out_18(n2seg_1_out_18),
    .out_19(n2seg_1_out_19), .out_20(n2seg_1_out_20), .out_21(n2seg_1_out_21), .out_22(n2seg_1_out_22),
    .out_23(n2seg_1_out_23), .in_1(s_r_ff_9_q));
  \_8加法  \u_8加法_1  (
    .in_1(reg8_1_out_10), .in_2(reg8_1_out_11), .in_3(reg8_1_out_12), .in_4(reg8_1_out_13),
    .in_5(reg8_1_out_14), .in_6(reg8_1_out_15), .in_7(reg8_1_out_16), .in_8(reg8_1_out_17),
    .in_9(reg8_3_out_10), .in_10(reg8_3_out_11), .in_11(reg8_3_out_12), .in_12(reg8_3_out_13),
    .in_13(reg8_3_out_14), .in_14(reg8_3_out_15), .in_15(reg8_3_out_16), .in_16(reg8_3_out_17),
    .out_17(out_35), .out_18(\n8加法_1_out_18 ), .out_19(\n8加法_1_out_19 ), .out_20(\n8加法_1_out_20 ),
    .out_21(\n8加法_1_out_21 ), .out_22(\n8加法_1_out_22 ), .out_23(\n8加法_1_out_23 ), .out_24(\n8加法_1_out_24 ),
    .out_25(\n8加法_1_out_25 ));
  reg8 reg8_1 (
    .in_1(reg8_2_out_10), .in_2(reg8_2_out_11), .in_3(reg8_2_out_12), .in_4(reg8_2_out_13),
    .in_5(reg8_2_out_14), .in_6(reg8_2_out_15), .in_7(reg8_2_out_16), .in_9(reg8_2_out_17),
    .in_8(s_r_ff_7_q), .out_10(reg8_1_out_10), .out_11(reg8_1_out_11), .out_12(reg8_1_out_12),
    .out_13(reg8_1_out_13), .out_14(reg8_1_out_14), .out_15(reg8_1_out_15), .out_16(reg8_1_out_16),
    .out_17(reg8_1_out_17));
  reg8 reg8_2 (
    .in_1(c8_1_out_17), .in_2(c8_1_out_16), .in_3(c8_1_out_15), .in_4(c8_1_out_14), .in_5(c8_1_out_13),
    .in_6(c8_1_out_12), .in_7(c8_1_out_11), .in_9(c8_1_out_10), .in_8(s_r_ff_5_q), .out_10(reg8_2_out_10),
    .out_11(reg8_2_out_11), .out_12(reg8_2_out_12), .out_13(reg8_2_out_13), .out_14(reg8_2_out_14),
    .out_15(reg8_2_out_15), .out_16(reg8_2_out_16), .out_17(reg8_2_out_17));
  S_R_Flip_Flop s_r_ff_5 (.Q(s_r_ff_5_q), .preset(or_1_out), .reset(or_2_out));  // open: S, clk, R, Qn, en
  S_R_Flip_Flop s_r_ff_6 (
    .Q(s_r_ff_6_q), .preset(\n4_16译码器_1_out_12 ), .reset(\n4_16译码器_1_out_14 ));  // open: S, clk, R, Qn, en
  or or_1 (or_1_out, \n4_16译码器_1_out_9 , \n4_16译码器_1_out_13 , \n4_16译码器_1_out_6 );
  reg8 reg8_3 (
    .in_1(reg8_2_out_10), .in_2(reg8_2_out_11), .in_3(reg8_2_out_12), .in_4(reg8_2_out_13),
    .in_5(reg8_2_out_14), .in_6(reg8_2_out_15), .in_7(reg8_2_out_16), .in_9(reg8_2_out_17),
    .in_8(s_r_ff_8_q), .out_10(reg8_3_out_10), .out_11(reg8_3_out_11), .out_12(reg8_3_out_12),
    .out_13(reg8_3_out_13), .out_14(reg8_3_out_14), .out_15(reg8_3_out_15), .out_16(reg8_3_out_16),
    .out_17(reg8_3_out_17));
  S_R_Flip_Flop s_r_ff_7 (
    .Q(s_r_ff_7_q), .preset(\n4_16译码器_1_out_7 ), .reset(\n4_16译码器_1_out_8 ));  // open: S, clk, R, Qn, en
  or or_2 (or_2_out, \n4_16译码器_1_out_7 , \n4_16译码器_1_out_14 , \n4_16译码器_1_out_10 );
  _7_Segment_Display #(.active("false")) u_7_segment_display_1 (
    .g(n2seg_1_out_16), .f(n2seg_1_out_15), .a(n2seg_1_out_10), .b(n2seg_1_out_11), .e(n2seg_1_out_14),
    .d(n2seg_1_out_13), .c(n2seg_1_out_12), .dp(1'b1));
  S_R_Flip_Flop s_r_ff_8 (
    .Q(s_r_ff_8_q), .preset(\n4_16译码器_1_out_11 ), .reset(\n4_16译码器_1_out_12 ));  // open: S, clk, R, Qn, en
  _7_Segment_Display #(.active("false")) u_7_segment_display_2 (
    .g(n2seg_1_out_23), .f(n2seg_1_out_22), .a(n2seg_1_out_17), .b(n2seg_1_out_18), .e(n2seg_1_out_21),
    .d(n2seg_1_out_20), .c(n2seg_1_out_19), .dp(1'b1));
  S_R_Flip_Flop s_r_ff_9 (
    .Q(s_r_ff_9_q), .preset(\n4_16译码器_1_out_5 ), .reset(\n4_16译码器_1_out_20 ));  // open: S, clk, R, Qn, en
  Counter #(.width(4), .max('hf)) counter_1 (.Q(counter_1_q), .clk(clock_1_out));  // open: load, D, count, carry, clr
  Clock clock_1 (.out(clock_1_out));
  \_4_16译码器  \u_4_16译码器_1  (
    .in_1(counter_1_q[0]), .in_2(counter_1_q[1]), .in_3(counter_1_q[2]), .in_4(counter_1_q[3]),
    .out_5(\n4_16译码器_1_out_5 ), .out_6(\n4_16译码器_1_out_6 ), .out_7(\n4_16译码器_1_out_7 ),
    .out_8(\n4_16译码器_1_out_8 ), .out_9(\n4_16译码器_1_out_9 ), .out_10(\n4_16译码器_1_out_10 ),
    .out_11(\n4_16译码器_1_out_11 ), .out_12(\n4_16译码器_1_out_12 ), .out_13(\n4_16译码器_1_out_13 ),
    .out_14(\n4_16译码器_1_out_14 ), .out_15(\n4_16译码器_1_out_15 ), .out_16(\n4_16译码器_1_out_16 ),
    .out_17(\n4_16译码器_1_out_17 ), .out_18(\n4_16译码器_1_out_18 ), .out_19(\n4_16译码器_1_out_19 ),
    .out_20(\n4_16译码器_1_out_20 ));
endmodule

module \验证2  (
  input  in_1,
  input  in_2,
  input  in_3,
  input  in_4,
  input  in_5,
  input  in_6,
  input  in_7,
  input  in_8,
  input  in_9,
  input  in_10,
  input  in_11,
  input  in_12,
  input  in_13,
  input  in_14,
  input  in_15,
  input  in_16,
  input  in_17,
  input  in_18,
  input  in_19,
  input  in_20,
  input  in_21,
  input  in_22,
  input  in_23,
  input  in_24,
  input  in_25,
  input  in_26,
  input  in_27,
  input  in_28,
  input  in_29,
  input  in_30,
  input  in_31,
  input  in_32,
  input  in_33,
  input  in_34,
  output out_35
);

  wire c8_1_out_10, c8_1_out_11, c8_1_out_12, c8_1_out_13, c8_1_out_14, c8_1_out_15, c8_1_out_16,
       c8_1_out_17, clock_1_out, double_16key_1_out_37, double_16key_1_out_38, double_16key_1_out_39,
       double_16key_1_out_40, double_16key_1_out_41, double_16key_1_out_42, double_16key_1_out_43,
       double_16key_1_out_44, n2seg_1_out_10, n2seg_1_out_11, n2seg_1_out_12, n2seg_1_out_13, n2seg_1_out_14,
       n2seg_1_out_15, n2seg_1_out_16, n2seg_1_out_17, n2seg_1_out_18, n2seg_1_out_19, n2seg_1_out_20,
       n2seg_1_out_21, n2seg_1_out_22, n2seg_1_out_23, \n8加法_1_out_18 , \n8加法_1_out_19 , \n8加法_1_out_20 ,
       \n8加法_1_out_21 , \n8加法_1_out_22 , \n8加法_1_out_23 , \n8加法_1_out_24 , \n8加法_1_out_25 , reg8_1_out_10,
       reg8_1_out_11, reg8_1_out_12, reg8_1_out_13, reg8_1_out_14, reg8_1_out_15, reg8_1_out_16,
       reg8_1_out_17, reg8_2_out_10, reg8_2_out_11, reg8_2_out_12, reg8_2_out_13, reg8_2_out_14,
       reg8_2_out_15, reg8_2_out_16, reg8_2_out_17, reg8_3_out_10, reg8_3_out_11, reg8_3_out_12,
       reg8_3_out_13, reg8_3_out_14, reg8_3_out_15, reg8_3_out_16, reg8_3_out_17;
  wire [3:0] counter_1_q;
  wire [8:0] rom_1_data;

  double_16key double_16key_1 (
    .in_1(in_1), .in_2(in_2), .in_3(in_3), .in_4(in_4), .in_5(in_5), .in_6(in_6), .in_7(in_7), .in_8(in_8),
    .in_9(in_9), .in_12(in_10), .in_13(in_11), .in_14(in_12), .in_15(in_13), .in_16(in_14), .in_17(in_15),
    .in_18(in_16), .in_19(in_17), .in_20(in_18), .in_21(in_19), .in_22(in_20), .in_23(in_21), .in_24(in_22),
    .in_25(in_23), .in_26(in_26), .in_27(in_27), .in_28(in_28), .in_29(in_29), .in_32(in_30), .in_33(in_31),
    .in_34(in_32), .in_35(in_33), .in_36(in_34), .out_37(double_16key_1_out_37),
    .out_38(double_16key_1_out_38), .out_39(double_16key_1_out_39), .out_40(double_16key_1_out_40),
    .out_41(double_16key_1_out_41), .out_42(double_16key_1_out_42), .out_43(double_16key_1_out_43),
    .out_44(double_16key_1_out_44), .in_10(rom_1_data[8]), .in_11(rom_1_data[7]), .in_30(in_24), .in_31(in_25));
  LED led_1 (.in(double_16key_1_out_37));
  LED led_2 (.in(double_16key_1_out_38));
  LED led_3 (.in(double_16key_1_out_41));
  LED led_4 (.in(double_16key_1_out_42));
  LED led_5 (.in(double_16key_1_out_39));
  LED led_6 (.in(double_16key_1_out_40));
  LED led_7 (.in(double_16key_1_out_43));
  LED led_8 (.in(double_16key_1_out_44));
  C8 c8_1 (
    .in_2(double_16key_1_out_44), .in_3(double_16key_1_out_43), .in_4(double_16key_1_out_42),
    .in_5(double_16key_1_out_41), .in_6(double_16key_1_out_40), .in_7(double_16key_1_out_39),
    .in_8(double_16key_1_out_38), .in_9(double_16key_1_out_37), .out_10(c8_1_out_10), .out_11(c8_1_out_11),
    .out_12(c8_1_out_12), .out_13(c8_1_out_13), .out_14(c8_1_out_14), .out_15(c8_1_out_15),
    .out_16(c8_1_out_16), .out_17(c8_1_out_17), .in_1(rom_1_data[6]));
  C8 c8_2 (
    .in_2(\n8加法_1_out_25 ), .in_3(\n8加法_1_out_24 ), .in_4(\n8加法_1_out_23 ), .in_5(\n8加法_1_out_22 ),
    .in_6(\n8加法_1_out_21 ), .in_7(\n8加法_1_out_20 ), .in_8(\n8加法_1_out_19 ), .in_9(\n8加法_1_out_18 ),
    .out_10(c8_1_out_17), .out_11(c8_1_out_16), .out_12(c8_1_out_15), .out_13(c8_1_out_14),
    .out_14(c8_1_out_13), .out_15(c8_1_out_12), .out_16(c8_1_out_11), .out_17(c8_1_out_10),
    .in_1(rom_1_data[4]));
  C8 c8_3 (
    .in_2(reg8_2_out_17), .in_3(reg8_2_out_16), .in_4(reg8_2_out_15), .in_5(reg8_2_out_14),
    .in_6(reg8_2_out_13), .in_7(reg8_2_out_12), .in_8(reg8_2_out_11), .in_9(reg8_2_out_10),
    .out_10(double_16key_1_out_37), .out_11(double_16key_1_out_38), .out_12(double_16key_1_out_39),
    .out_13(double_16key_1_out_40), .out_14(double_16key_1_out_41), .out_15(double_16key_1_out_42),
    .out_16(double_16key_1_out_43), .out_17(double_16key_1_out_44), .in_1(rom_1_data[5]));
  _2seg u_2seg_1 (
    .in_2(double_16key_1_out_37), .in_3(double_16key_1_out_38), .in_4(double_16key_1_out_39),
    .in_5(double_16key_1_out_40), .in_6(double_16key_1_out_41), .in_7(double_16key_1_out_42),
    .in_8(double_16key_1_out_43), .in_9(double_16key_1_out_44), .out_10(n2seg_1_out_10),
    .out_11(n2seg_1_out_11), .out_12(n2seg_1_out_12), .out_13(n2seg_1_out_13), .out_14(n2seg_1_out_14),
    .out_15(n2seg_1_out_15), .out_16(n2seg_1_out_16), .out_17(n2seg_1_out_17), .out_18(n2seg_1_out_18),
    .out_19(n2seg_1_out_19), .out_20(n2seg_1_out_20), .out_21(n2seg_1_out_21), .out_22(n2seg_1_out_22),
    .out_23(n2seg_1_out_23), .in_1(rom_1_data[0]));
  \_8加法  \u_8加法_1  (
    .in_1(reg8_1_out_10), .in_2(reg8_1_out_11), .in_3(reg8_1_out_12), .in_4(reg8_1_out_13),
    .in_5(reg8_1_out_14), .in_6(reg8_1_out_15), .in_7(reg8_1_out_16), .in_8(reg8_1_out_17),
    .in_9(reg8_3_out_10), .in_10(reg8_3_out_11), .in_11(reg8_3_out_12), .in_12(reg8_3_out_13),
    .in_13(reg8_3_out_14), .in_14(reg8_3_out_15), .in_15(reg8_3_out_16), .in_16(reg8_3_out_17),
    .out_17(out_35), .out_18(\n8加法_1_out_18 ), .out_19(\n8加法_1_out_19 ), .out_20(\n8加法_1_out_20 ),
    .out_21(\n8加法_1_out_21 ), .out_22(\n8加法_1_out_22 ), .out_23(\n8加法_1_out_23 ), .out_24(\n8加法_1_out_24 ),
    .out_25(\n8加法_1_out_25 ));
  reg8 reg8_1 (
    .in_1(reg8_2_out_10), .in_2(reg8_2_out_11), .in_3(reg8_2_out_12), .in_4(reg8_2_out_13),
    .in_5(reg8_2_out_14), .in_6(reg8_2_out_15), .in_7(reg8_2_out_16), .in_9(reg8_2_out_17),
    .in_8(rom_1_data[2]), .out_10(reg8_1_out_10), .out_11(reg8_1_out_11), .out_12(reg8_1_out_12),
    .out_13(reg8_1_out_13), .out_14(reg8_1_out_14), .out_15(reg8_1_out_15), .out_16(reg8_1_out_16),
    .out_17(reg8_1_out_17));
  reg8 reg8_2 (
    .in_1(c8_1_out_17), .in_2(c8_1_out_16), .in_3(c8_1_out_15), .in_4(c8_1_out_14), .in_5(c8_1_out_13),
    .in_6(c8_1_out_12), .in_7(c8_1_out_11), .in_9(c8_1_out_10), .in_8(rom_1_data[3]), .out_10(reg8_2_out_10),
    .out_11(reg8_2_out_11), .out_12(reg8_2_out_12), .out_13(reg8_2_out_13), .out_14(reg8_2_out_14),
    .out_15(reg8_2_out_15), .out_16(reg8_2_out_16), .out_17(reg8_2_out_17));
  reg8 reg8_3 (
    .in_1(reg8_2_out_10), .in_2(reg8_2_out_11), .in_3(reg8_2_out_12), .in_4(reg8_2_out_13),
    .in_5(reg8_2_out_14), .in_6(reg8_2_out_15), .in_7(reg8_2_out_16), .in_9(reg8_2_out_17),
    .in_8(rom_1_data[1]), .out_10(reg8_3_out_10), .out_11(reg8_3_out_11), .out_12(reg8_3_out_12),
    .out_13(reg8_3_out_13), .out_14(reg8_3_out_14), .out_15(reg8_3_out_15), .out_16(reg8_3_out_16),
    .out_17(reg8_3_out_17));
  _7_Segment_Display #(.active("false")) u_7_segment_display_1 (
    .g(n2seg_1_out_16), .f(n2seg_1_out_15), .a(n2seg_1_out_10), .b(n2seg_1_out_11), .e(n2seg_1_out_14),
    .d(n2seg_1_out_13), .c(n2seg_1_out_12), .dp(1'b1));
  _7_Segment_Display #(.active("false")) u_7_segment_display_2 (
    .g(n2seg_1_out_23), .f(n2seg_1_out_22), .a(n2seg_1_out_17), .b(n2seg_1_out_18), .e(n2seg_1_out_21),
    .d(n2seg_1_out_20), .c(n2seg_1_out_19), .dp(1'b1));
  Counter #(.width(4), .max('hf)) counter_1 (.Q(counter_1_q), .clk(clock_1_out));  // open: load, D, count, carry, clr
  Clock clock_1 (.out(clock_1_out));
  ROM #(.addrWidth(4), .dataWidth(9)) rom_1 (.addr(counter_1_q), .data(rom_1_data));  // open: sel

  // Notes on the sheet:
  //   contents of rom_1 (hex, n*v repeats v):
  //   141 149 45 c1 c9 13 19 8*21
endmodule

module \验证3  (
  input  in_1,
  input  in_2,
  input  in_3,
  input  in_4,
  input  in_5,
  input  in_6,
  input  in_7,
  input  in_8,
  input  in_9,
  input  in_10,
  input  in_11,
  input  in_12,
  input  in_13,
  input  in_14,
  input  in_15,
  input  in_16,
  input  in_17,
  input  in_18,
  input  in_19,
  input  in_20,
  input  in_21,
  input  in_22,
  input  in_23,
  input  in_24,
  input  in_25,
  input  in_26,
  input  in_27,
  input  in_28,
  input  in_29,
  input  in_30,
  input  in_31,
  input  in_32,
  input  in_33,
  input  in_34,
  output out_35
);

  wire c8_1_out_10, c8_1_out_11, c8_1_out_12, c8_1_out_13, c8_1_out_14, c8_1_out_15, c8_1_out_16,
       c8_1_out_17, clock_1_out, double_16key_1_out_37, double_16key_1_out_38, double_16key_1_out_39,
       double_16key_1_out_40, double_16key_1_out_41, double_16key_1_out_42, double_16key_1_out_43,
       double_16key_1_out_44, n2seg_1_out_10, n2seg_1_out_11, n2seg_1_out_12, n2seg_1_out_13, n2seg_1_out_14,
       n2seg_1_out_15, n2seg_1_out_16, n2seg_1_out_17, n2seg_1_out_18, n2seg_1_out_19, n2seg_1_out_20,
       n2seg_1_out_21, n2seg_1_out_22, n2seg_1_out_23, \n8加法_1_out_18 , \n8加法_1_out_19 , \n8加法_1_out_20 ,
       \n8加法_1_out_21 , \n8加法_1_out_22 , \n8加法_1_out_23 , \n8加法_1_out_24 , \n8加法_1_out_25 , reg8_1_out_10,
       reg8_1_out_11, reg8_1_out_12, reg8_1_out_13, reg8_1_out_14, reg8_1_out_15, reg8_1_out_16,
       reg8_1_out_17, reg8_2_out_10, reg8_2_out_11, reg8_2_out_12, reg8_2_out_13, reg8_2_out_14,
       reg8_2_out_15, reg8_2_out_16, reg8_2_out_17, reg8_3_out_10, reg8_3_out_11, reg8_3_out_12,
       reg8_3_out_13, reg8_3_out_14, reg8_3_out_15, reg8_3_out_16, reg8_3_out_17;
  wire [4:2] rom_1_data;
  wire [5:0] counter_1_q;
  wire [6:3] rom_1_data_2;
  wire [10:0] rom_2_data;

  double_16key double_16key_1 (
    .in_1(in_1), .in_2(in_2), .in_3(in_3), .in_4(in_4), .in_5(in_5), .in_6(in_6), .in_7(in_7), .in_8(in_8),
    .in_9(in_9), .in_12(in_10), .in_13(in_11), .in_14(in_12), .in_15(in_13), .in_16(in_14), .in_17(in_15),
    .in_18(in_16), .in_19(in_17), .in_20(in_18), .in_21(in_19), .in_22(in_20), .in_23(in_21), .in_24(in_22),
    .in_25(in_23), .in_26(in_26), .in_27(in_27), .in_28(in_28), .in_29(in_29), .in_32(in_30), .in_33(in_31),
    .in_34(in_32), .in_35(in_33), .in_36(in_34), .out_37(double_16key_1_out_37),
    .out_38(double_16key_1_out_38), .out_39(double_16key_1_out_39), .out_40(double_16key_1_out_40),
    .out_41(double_16key_1_out_41), .out_42(double_16key_1_out_42), .out_43(double_16key_1_out_43),
    .out_44(double_16key_1_out_44), .in_10(rom_2_data[8]), .in_11(rom_2_data[7]), .in_30(in_24), .in_31(in_25));
  LED led_1 (.in(double_16key_1_out_37));
  LED led_2 (.in(double_16key_1_out_38));
  LED led_3 (.in(double_16key_1_out_41));
  LED led_4 (.in(double_16key_1_out_42));
  LED led_5 (.in(double_16key_1_out_39));
  LED led_6 (.in(double_16key_1_out_40));
  LED led_7 (.in(double_16key_1_out_43));
  LED led_8 (.in(double_16key_1_out_44));
  C8 c8_1 (
    .in_2(double_16key_1_out_44), .in_3(double_16key_1_out_43), .in_4(double_16key_1_out_42),
    .in_5(double_16key_1_out_41), .in_6(double_16key_1_out_40), .in_7(double_16key_1_out_39),
    .in_8(double_16key_1_out_38), .in_9(double_16key_1_out_37), .out_10(c8_1_out_10), .out_11(c8_1_out_11),
    .out_12(c8_1_out_12), .out_13(c8_1_out_13), .out_14(c8_1_out_14), .out_15(c8_1_out_15),
    .out_16(c8_1_out_16), .out_17(c8_1_out_17), .in_1(rom_2_data[6]));
  C8 c8_2 (
    .in_2(\n8加法_1_out_25 ), .in_3(\n8加法_1_out_24 ), .in_4(\n8加法_1_out_23 ), .in_5(\n8加法_1_out_22 ),
    .in_6(\n8加法_1_out_21 ), .in_7(\n8加法_1_out_20 ), .in_8(\n8加法_1_out_19 ), .in_9(\n8加法_1_out_18 ),
    .out_10(c8_1_out_17), .out_11(c8_1_out_16), .out_12(c8_1_out_15), .out_13(c8_1_out_14),
    .out_14(c8_1_out_13), .out_15(c8_1_out_12), .out_16(c8_1_out_11), .out_17(c8_1_out_10),
    .in_1(rom_2_data[4]));
  C8 c8_3 (
    .in_2(reg8_2_out_17), .in_3(reg8_2_out_16), .in_4(reg8_2_out_15), .in_5(reg8_2_out_14),
    .in_6(reg8_2_out_13), .in_7(reg8_2_out_12), .in_8(reg8_2_out_11), .in_9(reg8_2_out_10),
    .out_10(double_16key_1_out_37), .out_11(double_16key_1_out_38), .out_12(double_16key_1_out_39),
    .out_13(double_16key_1_out_40), .out_14(double_16key_1_out_41), .out_15(double_16key_1_out_42),
    .out_16(double_16key_1_out_43), .out_17(double_16key_1_out_44), .in_1(rom_2_data[5]));
  _2seg u_2seg_1 (
    .in_2(double_16key_1_out_37), .in_3(double_16key_1_out_38), .in_4(double_16key_1_out_39),
    .in_5(double_16key_1_out_40), .in_6(double_16key_1_out_41), .in_7(double_16key_1_out_42),
    .in_8(double_16key_1_out_43), .in_9(double_16key_1_out_44), .out_10(n2seg_1_out_10),
    .out_11(n2seg_1_out_11), .out_12(n2seg_1_out_12), .out_13(n2seg_1_out_13), .out_14(n2seg_1_out_14),
    .out_15(n2seg_1_out_15), .out_16(n2seg_1_out_16), .out_17(n2seg_1_out_17), .out_18(n2seg_1_out_18),
    .out_19(n2seg_1_out_19), .out_20(n2seg_1_out_20), .out_21(n2seg_1_out_21), .out_22(n2seg_1_out_22),
    .out_23(n2seg_1_out_23), .in_1(rom_2_data[0]));
  \_8加法  \u_8加法_1  (
    .in_1(reg8_1_out_10), .in_2(reg8_1_out_11), .in_3(reg8_1_out_12), .in_4(reg8_1_out_13),
    .in_5(reg8_1_out_14), .in_6(reg8_1_out_15), .in_7(reg8_1_out_16), .in_8(reg8_1_out_17),
    .in_9(reg8_3_out_10), .in_10(reg8_3_out_11), .in_11(reg8_3_out_12), .in_12(reg8_3_out_13),
    .in_13(reg8_3_out_14), .in_14(reg8_3_out_15), .in_15(reg8_3_out_16), .in_16(reg8_3_out_17),
    .out_17(out_35), .out_18(\n8加法_1_out_18 ), .out_19(\n8加法_1_out_19 ), .out_20(\n8加法_1_out_20 ),
    .out_21(\n8加法_1_out_21 ), .out_22(\n8加法_1_out_22 ), .out_23(\n8加法_1_out_23 ), .out_24(\n8加法_1_out_24 ),
    .out_25(\n8加法_1_out_25 ));
  reg8 reg8_1 (
    .in_1(reg8_2_out_10), .in_2(reg8_2_out_11), .in_3(reg8_2_out_12), .in_4(reg8_2_out_13),
    .in_5(reg8_2_out_14), .in_6(reg8_2_out_15), .in_7(reg8_2_out_16), .in_9(reg8_2_out_17),
    .in_8(rom_2_data[2]), .out_10(reg8_1_out_10), .out_11(reg8_1_out_11), .out_12(reg8_1_out_12),
    .out_13(reg8_1_out_13), .out_14(reg8_1_out_14), .out_15(reg8_1_out_15), .out_16(reg8_1_out_16),
    .out_17(reg8_1_out_17));
  reg8 reg8_2 (
    .in_1(c8_1_out_17), .in_2(c8_1_out_16), .in_3(c8_1_out_15), .in_4(c8_1_out_14), .in_5(c8_1_out_13),
    .in_6(c8_1_out_12), .in_7(c8_1_out_11), .in_9(c8_1_out_10), .in_8(rom_2_data[3]), .out_10(reg8_2_out_10),
    .out_11(reg8_2_out_11), .out_12(reg8_2_out_12), .out_13(reg8_2_out_13), .out_14(reg8_2_out_14),
    .out_15(reg8_2_out_15), .out_16(reg8_2_out_16), .out_17(reg8_2_out_17));
  reg8 reg8_3 (
    .in_1(reg8_2_out_10), .in_2(reg8_2_out_11), .in_3(reg8_2_out_12), .in_4(reg8_2_out_13),
    .in_5(reg8_2_out_14), .in_6(reg8_2_out_15), .in_7(reg8_2_out_16), .in_9(reg8_2_out_17),
    .in_8(rom_2_data[1]), .out_10(reg8_3_out_10), .out_11(reg8_3_out_11), .out_12(reg8_3_out_12),
    .out_13(reg8_3_out_13), .out_14(reg8_3_out_14), .out_15(reg8_3_out_15), .out_16(reg8_3_out_16),
    .out_17(reg8_3_out_17));
  _7_Segment_Display #(.active("false")) u_7_segment_display_1 (
    .g(n2seg_1_out_16), .f(n2seg_1_out_15), .a(n2seg_1_out_10), .b(n2seg_1_out_11), .e(n2seg_1_out_14),
    .d(n2seg_1_out_13), .c(n2seg_1_out_12), .dp(1'b1));
  _7_Segment_Display #(.active("false")) u_7_segment_display_2 (
    .g(n2seg_1_out_23), .f(n2seg_1_out_22), .a(n2seg_1_out_17), .b(n2seg_1_out_18), .e(n2seg_1_out_21),
    .d(n2seg_1_out_20), .c(n2seg_1_out_19), .dp(1'b1));
  Clock clock_1 (.out(clock_1_out));
  // Probe on counter_1_q
  Counter #(.width(6), .max('h3f)) counter_1 (
    .Q(counter_1_q), .clk(clock_1_out), .clr(rom_2_data[9]));  // open: load, D, count, carry
  // Probe on {rom_1_data, counter_1_q[1:0]}
  // Probe on {rom_1_data, counter_1_q[1:0]}
  // Probe on rom_1_data
  ROM #(.addrWidth(4), .dataWidth(7)) rom_1 (.addr(counter_1_q[5:2]), .data({rom_1_data_2, rom_1_data}));  // open: sel
  // Probe on {rom_1_data_2, rom_1_data}
  ROM #(.addrWidth(5), .dataWidth(11)) rom_2 (.addr({rom_1_data, counter_1_q[1:0]}), .data(rom_2_data));  // open: sel
  // Probe on rom_2_data

  // Notes on the sheet:
  //   contents of rom_1 (hex, n*v repeats v):
  //   14 7 15 2 16 0 0 0 1
  //   contents of rom_2 (hex, n*v repeats v):
  //   4*0 c9 13 19 8*21 0 0 141 149 45 4*21 4*0 c1 c9 13 19
endmodule

module reg_plus (
  input  [7:0] in_1,
  input  in_2,
  output [7:0] out_3
);

  Register register_1 (.D(in_1), .Q(out_3), .clk(in_2));  // open: en, clr
endmodule

module c8_plus (
  input  [7:0] in_1,
  input  in_2,
  output [7:0] out_3
);

  assign out_3 = in_2 ? in_1 : 8'bz;  // Controlled_Buffer controlled_buffer_1
endmodule

module \end  (
  input  in_1,
  input  [15:0] in_2,
  input  [15:0] _0_1_2_3_4_5_6_7,
  input  in_4,
  input  in_5,
  input  in_6
);

  wire and_1_out, choose2_1_u, choose2_1_x, choose2_1_y, choose2_1_z, clock_1_out, d_ff_1_q, d_ff_2_q,
       n2seg_1_out_10, n2seg_1_out_11, n2seg_1_out_12, n2seg_1_out_13, n2seg_1_out_14, n2seg_1_out_15,
       n2seg_1_out_16, n2seg_1_out_17, n2seg_1_out_18, n2seg_1_out_19, n2seg_1_out_20, n2seg_1_out_21,
       n2seg_1_out_22, n2seg_1_out_23, n8addplus_1_out_3, not_1_out, not_2_out, not_3_out, or_1_out;
  wire [1:0] controlled_buffer_4_out, controlled_buffer_5_out;
  wire [2:0] counter_1_q, rom_1_data;
  wire [3:0] counter_1_q_2, rom_2_data;
  wire [5:2] rom_2_data_2;
  wire [6:0] controlled_buffer_1_out;
  wire [6:3] register_2_q, register_3_q;
  wire [7:0] c8_plus_1_out_3, double_16key_1_out_37, \n8_8乘法器封装_1_out_3 , n8addplus_1_out_4,
       reg_plus_1_out_3, reg_plus_2_out_3, reg_plus_3_out_3, register_1_q;
  wire [14:0] rom_3_data;

  double_16key double_16key_1 (
    .in_1(in_2[15]), .in_2(in_2[14]), .in_3(in_2[13]), .in_4(in_2[12]), .in_5(in_2[11]), .in_6(in_2[10]),
    .in_7(in_2[9]), .in_8(in_2[8]), .in_9(in_2[7]), .in_12(in_2[6]), .in_13(in_2[5]), .in_14(in_2[4]),
    .in_15(in_2[3]), .in_16(in_2[2]), .in_17(in_2[1]), .in_18(in_2[0]), .in_19(_0_1_2_3_4_5_6_7[15]),
    .in_20(_0_1_2_3_4_5_6_7[14]), .in_21(_0_1_2_3_4_5_6_7[13]), .in_22(_0_1_2_3_4_5_6_7[12]),
    .in_23(_0_1_2_3_4_5_6_7[11]), .in_24(_0_1_2_3_4_5_6_7[10]), .in_25(_0_1_2_3_4_5_6_7[9]),
    .in_26(_0_1_2_3_4_5_6_7[8]), .in_27(_0_1_2_3_4_5_6_7[7]), .in_28(_0_1_2_3_4_5_6_7[6]),
    .in_29(_0_1_2_3_4_5_6_7[5]), .in_32(_0_1_2_3_4_5_6_7[4]), .in_33(_0_1_2_3_4_5_6_7[3]),
    .in_34(_0_1_2_3_4_5_6_7[2]), .in_35(_0_1_2_3_4_5_6_7[1]), .in_36(_0_1_2_3_4_5_6_7[0]),
    .out_37(double_16key_1_out_37[0]), .out_38(double_16key_1_out_37[1]), .out_39(double_16key_1_out_37[2]),
    .out_40(double_16key_1_out_37[3]), .out_41(double_16key_1_out_37[4]), .out_42(double_16key_1_out_37[5]),
    .out_43(double_16key_1_out_37[6]), .out_44(double_16key_1_out_37[7]), .in_10(rom_3_data[12]),
    .in_11(rom_3_data[11]), .in_30(in_4), .in_31(in_5));
  LED led_1 (.in(double_16key_1_out_37[2]));
  LED led_2 (.in(double_16key_1_out_37[0]));
  LED led_3 (.in(double_16key_1_out_37[4]));
  LED led_4 (.in(double_16key_1_out_37[6]));
  LED led_5 (.in(double_16key_1_out_37[3]));
  LED led_6 (.in(double_16key_1_out_37[5]));
  LED led_7 (.in(double_16key_1_out_37[1]));
  LED led_8 (.in(double_16key_1_out_37[7]));
  // Probe on double_16key_1_out_37
  c8_plus c8_plus_1 (.in_1(double_16key_1_out_37), .out_3(c8_plus_1_out_3), .in_2(rom_3_data[10]));
  c8_plus c8_plus_2 (.in_1({4'b0000, rom_2_data_2}), .out_3(double_16key_1_out_37), .in_2(rom_3_data[1]));
  reg_plus reg_plus_1 (.in_1(reg_plus_2_out_3), .out_3(reg_plus_1_out_3), .in_2(choose2_1_u));
  c8_plus c8_plus_3 (.in_1(reg_plus_2_out_3), .out_3(double_16key_1_out_37), .in_2(rom_3_data[6]));
  reg_plus reg_plus_2 (.in_1(c8_plus_1_out_3), .out_3(reg_plus_2_out_3), .in_2(choose2_1_y));
  c8_plus c8_plus_4 (.in_1(\n8_8乘法器封装_1_out_3 ), .out_3(c8_plus_1_out_3), .in_2(rom_3_data[7]));
  c8_plus c8_plus_5 (.in_1(n8addplus_1_out_4), .out_3(c8_plus_1_out_3), .in_2(rom_3_data[8]));
  LED led_9 (.in(n8addplus_1_out_3));
  _8addPlus u_8addplus_1 (
    .out_3(n8addplus_1_out_3), .out_4(n8addplus_1_out_4), .in_1(reg_plus_1_out_3), .in_2(reg_plus_3_out_3));
  \_8_8乘法器封装  \u_8_8乘法器封装_1  (
    .in_1(reg_plus_1_out_3), .in_2(reg_plus_3_out_3), .out_3(\n8_8乘法器封装_1_out_3 ));  // open: out_4
  reg_plus reg_plus_3 (.in_1(reg_plus_2_out_3), .out_3(reg_plus_3_out_3), .in_2(choose2_1_z));
  Register register_1 (.D(double_16key_1_out_37), .Q(register_1_q), .clk(rom_3_data[14]));  // open: en, clr
  _2seg u_2seg_1 (
    .in_2(register_1_q[0]), .in_3(register_1_q[1]), .in_4(register_1_q[2]), .in_5(register_1_q[3]),
    .in_6(register_1_q[4]), .in_7(register_1_q[5]), .in_8(register_1_q[6]), .in_9(register_1_q[7]),
    .out_10(n2seg_1_out_10), .out_11(n2seg_1_out_11), .out_12(n2seg_1_out_12), .out_13(n2seg_1_out_13),
    .out_14(n2seg_1_out_14), .out_15(n2seg_1_out_15), .out_16(n2seg_1_out_16), .out_17(n2seg_1_out_17),
    .out_18(n2seg_1_out_18), .out_19(n2seg_1_out_19), .out_20(n2seg_1_out_20), .out_21(n2seg_1_out_21),
    .out_22(n2seg_1_out_22), .out_23(n2seg_1_out_23), .in_1(in_1));
  // Probe on {register_2_q, 3'b000}
  Register #(.width(4)) register_2 (.D(rom_2_data), .Q(register_2_q), .clk(rom_3_data[4]));  // open: en, clr
  Pull_Resistor pull_resistor_1 (.node(rom_3_data[3]));
  Pull_Resistor pull_resistor_2 (.node(rom_3_data[2]));
  or or_1 (or_1_out, rom_1_data[1], rom_3_data[3], rom_3_data[2]);
  Pull_Resistor pull_resistor_3 (.node(rom_1_data[1]));
  _7_Segment_Display #(.active("false")) u_7_segment_display_1 (
    .g(n2seg_1_out_16), .f(n2seg_1_out_15), .a(n2seg_1_out_10), .b(n2seg_1_out_11), .e(n2seg_1_out_14),
    .d(n2seg_1_out_13), .c(n2seg_1_out_12), .dp(1'b1));
  choose2 choose2_1 (
    .a(rom_2_data[3:2]), .x(choose2_1_x), .y(choose2_1_y), .z(choose2_1_z), .u(choose2_1_u),
    .c(rom_3_data[9]), .a_2(rom_2_data[1:0]));
  // Probe on counter_1_q_2
  assign controlled_buffer_1_out = rom_3_data[3] ? {register_3_q, 3'b000} : 7'bz;  // Controlled_Buffer controlled_buffer_1
  assign controlled_buffer_1_out = rom_1_data[1] ? {register_2_q, 3'b000} : 7'bz;  // Controlled_Buffer controlled_buffer_2
  assign controlled_buffer_1_out = rom_3_data[2] ? {rom_2_data, 3'b000} : 7'bz;  // Controlled_Buffer controlled_buffer_3
  D_Flip_Flop d_ff_1 (.Q(d_ff_1_q), .preset(rom_3_data[13]), .reset(rom_3_data[0]));  // open: clk, D, Qn, en
  _7_Segment_Display #(.active("false")) u_7_segment_display_2 (
    .g(n2seg_1_out_23), .f(n2seg_1_out_22), .a(n2seg_1_out_17), .b(n2seg_1_out_18), .e(n2seg_1_out_21),
    .d(n2seg_1_out_20), .c(n2seg_1_out_19), .dp(1'b1));
  Register #(.width(4)) register_3 (.D(counter_1_q_2), .Q(register_3_q), .clk(rom_1_data[2]));  // open: en, clr
  Counter #(.width(7), .max('h7f)) counter_1 (
    .load(or_1_out), .D(controlled_buffer_1_out), .count(not_2_out), .Q({counter_1_q_2, counter_1_q}),
    .clk(clock_1_out));  // open: carry, clr
  Clock clock_1 (.out(clock_1_out));
  not not_1 (not_1_out, counter_1_q[2]);
  not not_2 (not_2_out, or_1_out);
  not not_3 (not_3_out, d_ff_1_q);
  and and_1 (and_1_out, not_3_out, counter_1_q[2], d_ff_2_q);
  D_Flip_Flop d_ff_2 (.Q(d_ff_2_q), .preset(in_6), .reset(rom_3_data[0]));  // open: clk, D, Qn, en
  LED led_10 (.in(d_ff_2_q));
  // Probe on {counter_1_q_2, counter_1_q}
  assign controlled_buffer_4_out = not_1_out ? counter_1_q[1:0] : 2'bz;  // Controlled_Buffer controlled_buffer_4
  assign controlled_buffer_5_out = counter_1_q[2] ? counter_1_q[1:0] : 2'bz;  // Controlled_Buffer controlled_buffer_5
  // Probe on {rom_2_data_2, controlled_buffer_4_out}
  ROM #(.addrWidth(2), .dataWidth(3)) rom_1 (.addr(controlled_buffer_5_out), .data(rom_1_data), .sel(and_1_out));
  // Probe on rom_2_data_2
  // Probe on rom_1_data
  ROM #(.addrWidth(4)) rom_2 (.addr(counter_1_q_2), .data({rom_2_data_2, rom_2_data}));  // open: sel
  // Probe on {rom_2_data_2, rom_2_data}
  ROM #(.addrWidth(6), .dataWidth(15)) rom_3 (
    .addr({rom_2_data_2, controlled_buffer_4_out}), .data(rom_3_data), .sel(not_1_out));
  // Probe on rom_3_data

  // Notes on the sheet:
  //   0 1 2 3 4 5 6 7
  //   8 9 a b c d e f
  //   8 9 a b c d e f
  //   contents of rom_1 (hex, n*v repeats v):
  //   4 2 2 2
  //   contents of rom_2 (hex, n*v repeats v):
  //   0 69 1a 33 2a 31 4a 80 7d 90 ba 80 a0
  //   contents of rom_3 (hex, n*v repeats v):
  //   4*0 1000 1600 0 0 c00 e00 0 0 0 200 0 0 500 700 0 0 480 680 0 0 0 10 0 0 4*4 40 4040 0 0 0 2000 0 0
  //   1 8 0 0 402 602
endmodule

module _8addPlus (
  input  [7:0] in_1,
  input  [7:0] in_2,
  output out_3,
  output [7:0] out_4
);

  \_8加法  \u_8加法_1  (
    .in_1(in_1[7]), .in_2(in_1[6]), .in_3(in_1[5]), .in_4(in_1[4]), .in_5(in_1[3]), .in_6(in_1[2]),
    .in_7(in_1[1]), .in_8(in_1[0]), .in_9(in_2[7]), .in_10(in_2[6]), .in_11(in_2[5]), .in_12(in_2[4]),
    .in_13(in_2[3]), .in_14(in_2[2]), .in_15(in_2[1]), .in_16(in_2[0]), .out_17(out_3), .out_18(out_4[7]),
    .out_19(out_4[6]), .out_20(out_4[5]), .out_21(out_4[4]), .out_22(out_4[3]), .out_23(out_4[2]),
    .out_24(out_4[1]), .out_25(out_4[0]));
endmodule

module \二进制乘法器  (
  input  in_1,
  input  in_2,
  input  in_3,
  input  in_4,
  output out_5,
  output out_6
);

  wire and_1_out;

  and and_1 (and_1_out, in_3, in_4);
  \全加器  \u_全加器_1  (.c(in_1), .a(and_1_out), .b(in_2), .s(out_5), .c_2(out_6));
endmodule

module \二进制乘法器4  (
  input  in_1,
  input  in_2,
  input  in_3,
  input  in_4,
  input  in_5,
  input  in_6,
  input  in_7,
  input  in_8,
  input  in_9,
  input  in_10,
  output out_11,
  output out_12,
  output out_13,
  output out_14,
  output out_15
);

  wire and_1_out, and_2_out, and_3_out, and_4_out, \全加器_1_c_2 , \全加器_2_c_2 , \全加器_3_c_2 ;

  and and_1 (and_1_out, in_1, in_3);
  and and_2 (and_2_out, in_1, in_5);
  and and_3 (and_3_out, in_1, in_7);
  and and_4 (and_4_out, in_1, in_9);
  \全加器  \u_全加器_1  (.c(in_2), .a(and_1_out), .b(in_4), .s(out_11), .c_2(\全加器_1_c_2 ));
  \全加器  \u_全加器_2  (.c(\全加器_1_c_2 ), .a(and_2_out), .b(in_6), .s(out_12), .c_2(\全加器_2_c_2 ));
  \全加器  \u_全加器_3  (.c(\全加器_2_c_2 ), .a(and_3_out), .b(in_8), .s(out_13), .c_2(\全加器_3_c_2 ));
  \全加器  \u_全加器_4  (.c(\全加器_3_c_2 ), .a(and_4_out), .b(in_10), .s(out_14), .c_2(out_15));
endmodule

module \二进制乘法器4_4  (
  input  in_1,
  input  in_2,
  input  in_3,
  input  in_4,
  input  in_5,
  input  in_6,
  input  in_7,
  input  in_8,
  input  in_9,
  output out_10,
  output out_11,
  output out_12,
  output out_13
);

  wire and_1_out, and_2_out, and_3_out, and_4_out, pull_resistor_1_node, \二进制乘法器4_1_out_12 ,
       \二进制乘法器4_1_out_13 , \二进制乘法器4_1_out_14 , \二进制乘法器4_1_out_15 , \二进制乘法器4_2_out_12 , \二进制乘法器4_2_out_13 ,
       \二进制乘法器4_2_out_14 , \二进制乘法器4_2_out_15 , \二进制乘法器4_3_out_12 , \二进制乘法器4_3_out_13 , \二进制乘法器4_3_out_14 ,
       \二进制乘法器4_3_out_15 ;

  and and_1 (and_1_out, in_5, in_9);
  and and_2 (and_2_out, in_6, in_9);
  and and_3 (and_3_out, in_7, in_9);
  and and_4 (and_4_out, in_8, in_9);
  Pull_Resistor pull_resistor_1 (.node(pull_resistor_1_node));
  \二进制乘法器4  \u_二进制乘法器4_1  (
    .in_3(and_1_out), .in_4(pull_resistor_1_node), .in_5(and_2_out), .in_6(pull_resistor_1_node),
    .in_7(and_3_out), .in_8(pull_resistor_1_node), .in_9(and_4_out), .in_10(pull_resistor_1_node),
    .in_1(in_1), .in_2(pull_resistor_1_node), .out_11(out_10), .out_12(\二进制乘法器4_1_out_12 ),
    .out_13(\二进制乘法器4_1_out_13 ), .out_14(\二进制乘法器4_1_out_14 ), .out_15(\二进制乘法器4_1_out_15 ));
  \二进制乘法器4  \u_二进制乘法器4_2  (
    .in_3(and_1_out), .in_4(\二进制乘法器4_1_out_12 ), .in_5(and_2_out), .in_6(\二进制乘法器4_1_out_13 ),
    .in_7(and_3_out), .in_8(\二进制乘法器4_1_out_14 ), .in_9(and_4_out), .in_10(\二进制乘法器4_1_out_15 ), .in_1(in_2),
    .in_2(pull_resistor_1_node), .out_11(out_11), .out_12(\二进制乘法器4_2_out_12 ), .out_13(\二进制乘法器4_2_out_13 ),
    .out_14(\二进制乘法器4_2_out_14 ), .out_15(\二进制乘法器4_2_out_15 ));
  \二进制乘法器4  \u_二进制乘法器4_3  (
    .in_3(and_1_out), .in_4(\二进制乘法器4_2_out_12 ), .in_5(and_2_out), .in_6(\二进制乘法器4_2_out_13 ),
    .in_7(and_3_out), .in_8(\二进制乘法器4_2_out_14 ), .in_9(and_3_out), .in_10(\二进制乘法器4_2_out_15 ), .in_1(in_3),
    .in_2(pull_resistor_1_node), .out_11(out_12), .out_12(\二进制乘法器4_3_out_12 ), .out_13(\二进制乘法器4_3_out_13 ),
    .out_14(\二进制乘法器4_3_out_14 ), .out_15(\二进制乘法器4_3_out_15 ));
  \二进制乘法器4  \u_二进制乘法器4_4  (
    .in_3(and_1_out), .in_4(\二进制乘法器4_3_out_12 ), .in_5(and_2_out), .in_6(\二进制乘法器4_3_out_13 ),
    .in_7(and_3_out), .in_8(\二进制乘法器4_3_out_14 ), .in_9(and_4_out), .in_10(\二进制乘法器4_3_out_15 ), .in_1(in_4),
    .in_2(pull_resistor_1_node), .out_11(out_13));  // open: out_12, out_13, out_14, out_15
endmodule

module \二进制乘法器8  (
  input  in_1,
  input  in_2,
  input  in_3,
  input  in_4,
  input  in_5,
  input  in_6,
  input  in_7,
  input  in_8,
  input  in_9,
  input  in_10,
  input  in_11,
  input  in_12,
  input  in_13,
  input  in_14,
  input  in_15,
  input  in_16,
  input  in_17,
  input  in_18,
  output out_19,
  output out_20,
  output out_21,
  output out_22,
  output out_23,
  output out_24,
  output out_25,
  output out_26,
  output out_27
);

  wire and_1_out, and_2_out, and_3_out, and_4_out, and_5_out, and_6_out, and_7_out, and_8_out, \全加器_1_c_2 ,
       \全加器_2_c_2 , \全加器_3_c_2 , \全加器_4_c_2 , \全加器_5_c_2 , \全加器_6_c_2 , \全加器_7_c_2 ;

  and and_1 (and_1_out, in_1, in_3);
  and and_2 (and_2_out, in_1, in_5);
  and and_3 (and_3_out, in_1, in_7);
  and and_4 (and_4_out, in_1, in_9);
  and and_5 (and_5_out, in_1, in_11);
  and and_6 (and_6_out, in_1, in_13);
  and and_7 (and_7_out, in_1, in_15);
  and and_8 (and_8_out, in_1, in_17);
  \全加器  \u_全加器_1  (.c(in_2), .a(and_1_out), .b(in_4), .s(out_19), .c_2(\全加器_1_c_2 ));
  \全加器  \u_全加器_2  (.c(\全加器_1_c_2 ), .a(and_2_out), .b(in_6), .s(out_20), .c_2(\全加器_2_c_2 ));
  \全加器  \u_全加器_3  (.c(\全加器_2_c_2 ), .a(and_3_out), .b(in_8), .s(out_21), .c_2(\全加器_3_c_2 ));
  \全加器  \u_全加器_4  (.c(\全加器_3_c_2 ), .a(and_4_out), .b(in_10), .s(out_22), .c_2(\全加器_4_c_2 ));
  \全加器  \u_全加器_5  (.c(\全加器_4_c_2 ), .a(and_5_out), .b(in_12), .s(out_23), .c_2(\全加器_5_c_2 ));
  \全加器  \u_全加器_6  (.c(\全加器_5_c_2 ), .a(and_6_out), .b(in_14), .s(out_24), .c_2(\全加器_6_c_2 ));
  \全加器  \u_全加器_7  (.c(\全加器_6_c_2 ), .a(and_7_out), .b(in_16), .s(out_25), .c_2(\全加器_7_c_2 ));
  \全加器  \u_全加器_8  (.c(\全加器_7_c_2 ), .a(and_8_out), .b(in_18), .s(out_26), .c_2(out_27));
endmodule

module \二进制乘法器8_8  (
  input  in_1,
  input  in_2,
  input  in_3,
  input  in_4,
  input  in_5,
  input  in_6,
  input  in_7,
  input  in_8,
  input  in_9,
  input  in_10,
  input  in_11,
  input  in_12,
  input  in_13,
  input  in_14,
  input  in_15,
  input  in_16,
  input  in_17,
  output out_18,
  output out_19,
  output out_20,
  output out_21,
  output out_22,
  output out_23,
  output out_24,
  output out_25,
  output out_26,
  output out_27,
  output out_28,
  output out_29,
  output out_30,
  output out_31,
  output out_32,
  output out_33
);

  wire and_1_out, and_2_out, and_3_out, and_4_out, and_5_out, and_6_out, and_7_out, and_8_out,
       pull_resistor_1_node, undriven, undriven_2, undriven_3, undriven_4, undriven_5, undriven_6,
       undriven_7, undriven_8, undriven_9, undriven_10, undriven_11, undriven_12, undriven_13, undriven_14,
       undriven_15, undriven_16, \二进制乘法器8_1_out_20 , \二进制乘法器8_1_out_21 , \二进制乘法器8_1_out_22 ,
       \二进制乘法器8_1_out_23 , \二进制乘法器8_1_out_24 , \二进制乘法器8_1_out_25 , \二进制乘法器8_1_out_26 , \二进制乘法器8_1_out_27 ,
       \二进制乘法器8_3_out_20 , \二进制乘法器8_3_out_21 , \二进制乘法器8_3_out_22 , \二进制乘法器8_3_out_23 , \二进制乘法器8_3_out_24 ,
       \二进制乘法器8_3_out_25 , \二进制乘法器8_3_out_26 , \二进制乘法器8_3_out_27 , \二进制乘法器8_4_out_20 , \二进制乘法器8_4_out_21 ,
       \二进制乘法器8_4_out_22 , \二进制乘法器8_4_out_23 , \二进制乘法器8_4_out_24 , \二进制乘法器8_4_out_25 , \二进制乘法器8_4_out_26 ,
       \二进制乘法器8_4_out_27 , \二进制乘法器8_5_out_20 , \二进制乘法器8_5_out_21 , \二进制乘法器8_5_out_22 , \二进制乘法器8_5_out_23 ,
       \二进制乘法器8_5_out_24 , \二进制乘法器8_5_out_25 , \二进制乘法器8_5_out_26 , \二进制乘法器8_5_out_27 , \二进制乘法器8_6_out_20 ,
       \二进制乘法器8_6_out_21 , \二进制乘法器8_6_out_22 , \二进制乘法器8_6_out_23 , \二进制乘法器8_6_out_24 , \二进制乘法器8_6_out_25 ,
       \二进制乘法器8_6_out_26 , \二进制乘法器8_6_out_27 , \二进制乘法器8_7_out_20 , \二进制乘法器8_7_out_21 , \二进制乘法器8_7_out_22 ,
       \二进制乘法器8_7_out_23 , \二进制乘法器8_7_out_24 , \二进制乘法器8_7_out_25 , \二进制乘法器8_7_out_26 , \二进制乘法器8_7_out_27 ,
       \二进制乘法器8_8_out_20 , \二进制乘法器8_8_out_21 , \二进制乘法器8_8_out_22 , \二进制乘法器8_8_out_23 , \二进制乘法器8_8_out_24 ,
       \二进制乘法器8_8_out_25 , \二进制乘法器8_8_out_26 , \二进制乘法器8_8_out_27 ;

  and and_1 (and_1_out, in_9, in_17);
  and and_2 (and_2_out, in_10, in_17);
  and and_3 (and_3_out, in_11, in_17);
  and and_4 (and_4_out, in_12, in_17);
  and and_5 (and_5_out, in_13, in_17);
  and and_6 (and_6_out, in_14, in_17);
  and and_7 (and_7_out, in_15, in_17);
  and and_8 (and_8_out, in_16, in_17);
  Pull_Resistor pull_resistor_1 (.node(pull_resistor_1_node));
  \二进制乘法器8  \u_二进制乘法器8_1  (
    .in_3(and_1_out), .in_4(pull_resistor_1_node), .in_5(and_2_out), .in_6(pull_resistor_1_node),
    .in_7(and_3_out), .in_8(pull_resistor_1_node), .in_9(and_4_out), .in_10(pull_resistor_1_node),
    .in_11(and_5_out), .in_12(pull_resistor_1_node), .in_13(and_6_out), .in_14(pull_resistor_1_node),
    .in_15(and_7_out), .in_16(pull_resistor_1_node), .in_17(and_8_out), .in_18(pull_resistor_1_node),
    .in_1(in_1), .in_2(pull_resistor_1_node), .out_19(out_18), .out_20(\二进制乘法器8_1_out_20 ),
    .out_21(\二进制乘法器8_1_out_21 ), .out_22(\二进制乘法器8_1_out_22 ), .out_23(\二进制乘法器8_1_out_23 ),
    .out_24(\二进制乘法器8_1_out_24 ), .out_25(\二进制乘法器8_1_out_25 ), .out_26(\二进制乘法器8_1_out_26 ),
    .out_27(\二进制乘法器8_1_out_27 ));
  \二进制乘法器8  \u_二进制乘法器8_2  (
    .in_3(undriven_8), .in_4(undriven_9), .in_5(undriven_7), .in_6(undriven_10), .in_7(undriven_6),
    .in_8(undriven_11), .in_9(undriven_5), .in_10(undriven_12), .in_11(undriven_4), .in_12(undriven_13),
    .in_13(undriven_3), .in_14(undriven_14), .in_15(undriven_2), .in_16(undriven_15), .in_17(undriven),
    .in_18(undriven_16));  // open: in_1, in_2, out_19, out_20, out_21, out_22, out_23, out_24, out_25, out_26, out_27
  \二进制乘法器8  \u_二进制乘法器8_3  (
    .in_3(and_1_out), .in_4(\二进制乘法器8_1_out_20 ), .in_5(and_2_out), .in_6(\二进制乘法器8_1_out_21 ),
    .in_7(and_3_out), .in_8(\二进制乘法器8_1_out_22 ), .in_9(and_4_out), .in_10(\二进制乘法器8_1_out_23 ),
    .in_11(and_5_out), .in_12(\二进制乘法器8_1_out_24 ), .in_13(and_6_out), .in_14(\二进制乘法器8_1_out_25 ),
    .in_15(and_7_out), .in_16(\二进制乘法器8_1_out_26 ), .in_17(and_8_out), .in_18(\二进制乘法器8_1_out_27 ),
    .in_1(in_2), .in_2(pull_resistor_1_node), .out_19(out_19), .out_20(\二进制乘法器8_3_out_20 ),
    .out_21(\二进制乘法器8_3_out_21 ), .out_22(\二进制乘法器8_3_out_22 ), .out_23(\二进制乘法器8_3_out_23 ),
    .out_24(\二进制乘法器8_3_out_24 ), .out_25(\二进制乘法器8_3_out_25 ), .out_26(\二进制乘法器8_3_out_26 ),
    .out_27(\二进制乘法器8_3_out_27 ));
  \二进制乘法器8  \u_二进制乘法器8_4  (
    .in_3(and_1_out), .in_4(\二进制乘法器8_3_out_20 ), .in_5(and_2_out), .in_6(\二进制乘法器8_3_out_21 ),
    .in_7(and_3_out), .in_8(\二进制乘法器8_3_out_22 ), .in_9(and_4_out), .in_10(\二进制乘法器8_3_out_23 ),
    .in_11(and_5_out), .in_12(\二进制乘法器8_3_out_24 ), .in_13(and_6_out), .in_14(\二进制乘法器8_3_out_25 ),
    .in_15(and_7_out), .in_16(\二进制乘法器8_3_out_26 ), .in_17(and_8_out), .in_18(\二进制乘法器8_3_out_27 ),
    .in_1(in_3), .in_2(pull_resistor_1_node), .out_19(out_20), .out_20(\二进制乘法器8_4_out_20 ),
    .out_21(\二进制乘法器8_4_out_21 ), .out_22(\二进制乘法器8_4_out_22 ), .out_23(\二进制乘法器8_4_out_23 ),
    .out_24(\二进制乘法器8_4_out_24 ), .out_25(\二进制乘法器8_4_out_25 ), .out_26(\二进制乘法器8_4_out_26 ),
    .out_27(\二进制乘法器8_4_out_27 ));
  \二进制乘法器8  \u_二进制乘法器8_5  (
    .in_3(and_1_out), .in_4(\二进制乘法器8_4_out_20 ), .in_5(and_2_out), .in_6(\二进制乘法器8_4_out_21 ),
    .in_7(and_3_out), .in_8(\二进制乘法器8_4_out_22 ), .in_9(and_4_out), .in_10(\二进制乘法器8_4_out_23 ),
    .in_11(and_5_out), .in_12(\二进制乘法器8_4_out_24 ), .in_13(and_6_out), .in_14(\二进制乘法器8_4_out_25 ),
    .in_15(and_7_out), .in_16(\二进制乘法器8_4_out_26 ), .in_17(and_8_out), .in_18(\二进制乘法器8_4_out_27 ),
    .in_1(in_4), .in_2(pull_resistor_1_node), .out_19(out_21), .out_20(\二进制乘法器8_5_out_20 ),
    .out_21(\二进制乘法器8_5_out_21 ), .out_22(\二进制乘法器8_5_out_22 ), .out_23(\二进制乘法器8_5_out_23 ),
    .out_24(\二进制乘法器8_5_out_24 ), .out_25(\二进制乘法器8_5_out_25 ), .out_26(\二进制乘法器8_5_out_26 ),
    .out_27(\二进制乘法器8_5_out_27 ));
  \二进制乘法器8  \u_二进制乘法器8_6  (
    .in_3(and_1_out), .in_4(\二进制乘法器8_5_out_20 ), .in_5(and_2_out), .in_6(\二进制乘法器8_5_out_21 ),
    .in_7(and_3_out), .in_8(\二进制乘法器8_5_out_22 ), .in_9(and_4_out), .in_10(\二进制乘法器8_5_out_23 ),
    .in_11(and_5_out), .in_12(\二进制乘法器8_5_out_24 ), .in_13(and_6_out), .in_14(\二进制乘法器8_5_out_25 ),
    .in_15(and_7_out), .in_16(\二进制乘法器8_5_out_26 ), .in_17(and_8_out), .in_18(\二进制乘法器8_5_out_27 ),
    .in_1(in_5), .in_2(pull_resistor_1_node), .out_19(out_22), .out_20(\二进制乘法器8_6_out_20 ),
    .out_21(\二进制乘法器8_6_out_21 ), .out_22(\二进制乘法器8_6_out_22 ), .out_23(\二进制乘法器8_6_out_23 ),
    .out_24(\二进制乘法器8_6_out_24 ), .out_25(\二进制乘法器8_6_out_25 ), .out_26(\二进制乘法器8_6_out_26 ),
    .out_27(\二进制乘法器8_6_out_27 ));
  \二进制乘法器8  \u_二进制乘法器8_7  (
    .in_3(and_1_out), .in_4(\二进制乘法器8_6_out_20 ), .in_5(and_2_out), .in_6(\二进制乘法器8_6_out_21 ),
    .in_7(and_3_out), .in_8(\二进制乘法器8_6_out_22 ), .in_9(and_4_out), .in_10(\二进制乘法器8_6_out_23 ),
    .in_11(and_5_out), .in_12(\二进制乘法器8_6_out_24 ), .in_13(and_6_out), .in_14(\二进制乘法器8_6_out_25 ),
    .in_15(and_7_out), .in_16(\二进制乘法器8_6_out_26 ), .in_17(and_8_out), .in_18(\二进制乘法器8_6_out_27 ),
    .in_1(in_6), .in_2(pull_resistor_1_node), .out_19(out_23), .out_20(\二进制乘法器8_7_out_20 ),
    .out_21(\二进制乘法器8_7_out_21 ), .out_22(\二进制乘法器8_7_out_22 ), .out_23(\二进制乘法器8_7_out_23 ),
    .out_24(\二进制乘法器8_7_out_24 ), .out_25(\二进制乘法器8_7_out_25 ), .out_26(\二进制乘法器8_7_out_26 ),
    .out_27(\二进制乘法器8_7_out_27 ));
  \二进制乘法器8  \u_二进制乘法器8_8  (
    .in_3(and_1_out), .in_4(\二进制乘法器8_7_out_20 ), .in_5(and_2_out), .in_6(\二进制乘法器8_7_out_21 ),
    .in_7(and_3_out), .in_8(\二进制乘法器8_7_out_22 ), .in_9(and_4_out), .in_10(\二进制乘法器8_7_out_23 ),
    .in_11(and_5_out), .in_12(\二进制乘法器8_7_out_24 ), .in_13(and_6_out), .in_14(\二进制乘法器8_7_out_25 ),
    .in_15(and_7_out), .in_16(\二进制乘法器8_7_out_26 ), .in_17(and_8_out), .in_18(\二进制乘法器8_7_out_27 ),
    .in_1(in_7), .in_2(pull_resistor_1_node), .out_19(out_24), .out_20(\二进制乘法器8_8_out_20 ),
    .out_21(\二进制乘法器8_8_out_21 ), .out_22(\二进制乘法器8_8_out_22 ), .out_23(\二进制乘法器8_8_out_23 ),
    .out_24(\二进制乘法器8_8_out_24 ), .out_25(\二进制乘法器8_8_out_25 ), .out_26(\二进制乘法器8_8_out_26 ),
    .out_27(\二进制乘法器8_8_out_27 ));
  \二进制乘法器8  \u_二进制乘法器8_9  (
    .in_3(and_1_out), .in_4(\二进制乘法器8_8_out_20 ), .in_5(and_2_out), .in_6(\二进制乘法器8_8_out_21 ),
    .in_7(and_3_out), .in_8(\二进制乘法器8_8_out_22 ), .in_9(and_4_out), .in_10(\二进制乘法器8_8_out_23 ),
    .in_11(and_5_out), .in_12(\二进制乘法器8_8_out_24 ), .in_13(and_6_out), .in_14(\二进制乘法器8_8_out_25 ),
    .in_15(and_7_out), .in_16(\二进制乘法器8_8_out_26 ), .in_17(and_8_out), .in_18(\二进制乘法器8_8_out_27 ),
    .in_1(in_8), .in_2(pull_resistor_1_node), .out_19(out_25), .out_20(out_26), .out_21(out_27),
    .out_22(out_28), .out_23(out_29), .out_24(out_30), .out_25(out_31), .out_26(out_32), .out_27(out_33));
endmodule

module \_8_8乘法器封装  (
  input  [7:0] in_1,
  input  [7:0] in_2,
  output [7:0] out_3,
  output [15:0] out_4
);

  wire pull_resistor_1_node;

  // Probe on in_1
  // Probe on in_2
  Pull_Resistor #(.pull(1)) pull_resistor_1 (.node(pull_resistor_1_node));
  // Probe on out_3
  \二进制乘法器8_8  \u_二进制乘法器8_8_1  (
    .in_9(in_1[0]), .in_10(in_1[1]), .in_11(in_1[2]), .in_12(in_1[3]), .in_13(in_1[4]), .in_14(in_1[5]),
    .in_15(in_1[6]), .in_16(in_1[7]), .in_1(in_2[0]), .in_2(in_2[1]), .in_3(in_2[2]), .in_4(in_2[3]),
    .in_5(in_2[4]), .in_6(in_2[5]), .in_7(in_2[6]), .in_8(in_2[7]), .in_17(pull_resistor_1_node),
    .out_18(out_3[0]), .out_19(out_3[1]), .out_20(out_3[2]), .out_21(out_3[3]), .out_22(out_3[4]),
    .out_23(out_3[5]), .out_24(out_3[6]), .out_25(out_3[7]), .out_26(out_4[8]), .out_27(out_4[9]),
    .out_28(out_4[10]), .out_29(out_4[11]), .out_30(out_4[12]), .out_31(out_4[13]), .out_32(out_4[14]),
    .out_33(out_4[15]));
  // Probe on {out_4[15:8], out_3}

  assign out_4[7:0] = out_3;
endmodule

module choose (
  input  [1:0] a,
  input  c,
  output x,
  output y,
  output z,
  output u
);

  wire not_1_out, not_2_out, not_3_out, not_4_out;

  not not_1 (not_1_out, a[0]);
  not not_2 (not_2_out, a[1]);
  not not_3 (not_3_out, a[0]);
  not not_4 (not_4_out, a[1]);
  and and_1 (u, a[0], a[1], c);
  and and_2 (x, not_1_out, not_2_out, c);
  and and_3 (y, not_3_out, a[1], c);
  and and_4 (z, a[0], not_4_out, c);
endmodule

module choose2 (
  input  [1:0] a,
  input  [1:0] a_2,
  input  c,
  output x,
  output y,
  output z,
  output u
);

  wire and_1_out, and_2_out, and_3_out, and_4_out, and_5_out, and_6_out, and_7_out, and_8_out, not_1_out,
       not_2_out, not_3_out, not_4_out, not_5_out, not_6_out, not_7_out, not_8_out;

  not not_1 (not_1_out, a[0]);
  not not_2 (not_2_out, a[1]);
  not not_3 (not_3_out, a[0]);
  not not_4 (not_4_out, a[1]);
  and and_1 (and_1_out, a[0], a[1], c);
  not not_5 (not_5_out, a_2[0]);
  not not_6 (not_6_out, a_2[1]);
  not not_7 (not_7_out, a_2[0]);
  not not_8 (not_8_out, a_2[1]);
  and and_2 (and_2_out, a_2[0], a_2[1], c);
  and and_3 (and_3_out, not_1_out, not_2_out, c);
  and and_4 (and_4_out, not_3_out, a[1], c);
  and and_5 (and_5_out, a[0], not_4_out, c);
  and and_6 (and_6_out, not_5_out, not_6_out, c);
  and and_7 (and_7_out, not_7_out, a_2[1], c);
  and and_8 (and_8_out, a_2[0], not_8_out, c);
  or or_1 (x, and_3_out, and_6_out);
  or or_2 (y, and_4_out, and_7_out);
  or or_3 (z, and_5_out, and_8_out);
  or or_4 (u, and_1_out, and_2_out);
endmodule
