// Logisim project 多端口输入.circ as structural Verilog: 7 circuits, main circuit main
module main (
  input  in_1,
  input  in_2,
  input  in_3,
  input  in_4,
  input  in_5,
  input  in_6,
  input  in_7,
  input  in_8,
  input  in_9,
  output out_10,
  output out_11,
  output out_12,
  output out_13,
  output out_14,
  output out_15,
  output out_16,
  output out_17
);

  assign out_10 = in_1 ? in_2 : 1'bz;  // Controlled_Buffer controlled_buffer_1
  assign out_11 = in_1 ? in_3 : 1'bz;  // Controlled_Buffer controlled_buffer_2
  assign out_12 = in_1 ? in_4 : 1'bz;  // Controlled_Buffer controlled_buffer_3
  assign out_13 = in_1 ? in_5 : 1'bz;  // Controlled_Buffer controlled_buffer_4
  assign out_14 = in_1 ? in_6 : 1'bz;  // Controlled_Buffer controlled_buffer_5
  assign out_15 = in_1 ? in_7 : 1'bz;  // Controlled_Buffer controlled_buffer_6
  assign out_16 = in_1 ? in_8 : 1'bz;  // Controlled_Buffer controlled_buffer_7
  assign out_17 = in_1 ? in_9 : 1'bz;  // Controlled_Buffer controlled_buffer_8
endmodule

module C8 (
  input  in_1,
  input  in_2,
  input  in_3,
  input  in_4,
  input  in_5,
  input  in_6,
  input  in_7,
  input  in_8,
  input  in_9,
  output out_10,
  output out_11,
  output out_12,
  output out_13,
  output out_14,
  output out_15,
  output out_16,
  output out_17
);

  assign out_10 = in_1 ? in_2 : 1'bz;  // Controlled_Buffer controlled_buffer_1
  assign out_11 = in_1 ? in_3 : 1'bz;  // Controlled_Buffer controlled_buffer_2
  assign out_12 = in_1 ? in_4 : 1'bz;  // Controlled_Buffer controlled_buffer_3
  assign out_13 = in_1 ? in_5 : 1'bz;  // Controlled_Buffer controlled_buffer_4
  assign out_14 = in_1 ? in_6 : 1'bz;  // Controlled_Buffer controlled_buffer_5
  assign out_15 = in_1 ? in_7 : 1'bz;  // Controlled_Buffer controlled_buffer_6
  assign out_16 = in_1 ? in_8 : 1'bz;  // Controlled_Buffer controlled_buffer_7
  assign out_17 = in_1 ? in_9 : 1'bz;  // Controlled_Buffer controlled_buffer_8
endmodule

module _2seg (
  input  in_1,
  input  in_2,
  input  in_3,
  input  in_4,
  input  in_5,
  input  in_6,
  input  in_7,
  input  in_8,
  input  in_9,
  output out_10,
  output out_11,
  output out_12,
  output out_13,
  output out_14,
  output out_15,
  output out_16,
  output out_17,
  output out_18,
  output out_19,
  output out_20,
  output out_21,
  output out_22,
  output out_23
);

  wire c8_1_out_10, c8_1_out_11, c8_1_out_12, c8_1_out_13, c8_1_out_14, c8_1_out_15, c8_1_out_16, c8_1_out_17;

  C8 c8_1 (
    .in_2(in_2), .in_3(in_3), .in_4(in_4), .in_5(in_5), .in_6(in_6), .in_7(in_7), .in_8(in_8), .in_9(in_9),
    .out_10(c8_1_out_10), .out_11(c8_1_out_11), .out_12(c8_1_out_12), .out_13(c8_1_out_13),
    .out_14(c8_1_out_14), .out_15(c8_1_out_15), .out_16(c8_1_out_16), .out_17(c8_1_out_17), .in_1(in_1));
  Seg seg_1 (
    .in_1(c8_1_out_10), .in_2(c8_1_out_11), .in_3(c8_1_out_12), .in_4(c8_1_out_13), .out_5(out_10),
    .out_6(out_11), .out_7(out_12), .out_8(out_13), .out_9(out_14), .out_10(out_15), .out_11(out_16));
  Seg seg_2 (
    .in_1(c8_1_out_14), .in_2(c8_1_out_15), .in_3(c8_1_out_16), .in_4(c8_1_out_17), .out_5(out_17),
    .out_6(out_18), .out_7(out_19), .out_8(out_20), .out_9(out_21), .out_10(out_22), .out_11(out_23));
endmodule

module _16key (
  input  in_1,
  input  in_2,
  input  in_3,
  input  in_4,
  input  in_5,
  input  in_6,
  input  in_7,
  input  in_8,
  input  in_9,
  input  in_10,
  input  in_11,
  input  in_12,
  input  in_13,
  input  in_14,
  input  in_15,
  input  in_16,
  input  in_17,
  input  in_18,
  input  in_19,
  input  in_20,
  input  in_21,
  input  in_22,
  input  in_23,
  input  in_24,
  input  in_25,
  input  in_26,
  input  in_27,
  input  in_28,
  input  in_29,
  input  in_30,
  input  in_31,
  input  in_32,
  input  in_33,
  output out_34,
  output out_35,
  output out_36,
  output out_37,
  output out_38,
  output out_39,
  output out_40,
  output out_41
);

  wire \n16_4编码器_1_out_17 , \n16_4编码器_1_out_18 , \n16_4编码器_1_out_19 , \n16_4编码器_1_out_20 ,
       \n16_4编码器_2_out_17 , \n16_4编码器_2_out_18 , \n16_4编码器_2_out_19 , \n16_4编码器_2_out_20 ;

  \_16_4编码器  \u_16_4编码器_1  (
    .in_1(in_1), .in_2(in_2), .in_3(in_3), .in_4(in_4), .in_5(in_5), .in_6(in_6), .in_7(in_7), .in_8(in_8),
    .in_9(in_9), .in_10(in_11), .in_11(in_12), .in_12(in_13), .in_13(in_14), .in_14(in_15), .in_15(in_16),
    .in_16(in_17), .out_17(\n16_4编码器_1_out_17 ), .out_18(\n16_4编码器_1_out_18 ), .out_19(\n16_4编码器_1_out_19 ),
    .out_20(\n16_4编码器_1_out_20 ));
  \_16_4编码器  \u_16_4编码器_2  (
    .in_1(in_18), .in_2(in_19), .in_3(in_20), .in_4(in_21), .in_5(in_22), .in_6(in_23), .in_7(in_24),
    .in_8(in_25), .in_9(in_26), .in_10(in_27), .in_11(in_28), .in_12(in_29), .in_13(in_30), .in_14(in_31),
    .in_15(in_32), .in_16(in_33), .out_17(\n16_4编码器_2_out_17 ), .out_18(\n16_4编码器_2_out_18 ),
    .out_19(\n16_4编码器_2_out_19 ), .out_20(\n16_4编码器_2_out_20 ));
  C8 c8_1 (
    .in_2(\n16_4编码器_1_out_17 ), .in_3(\n16_4编码器_1_out_18 ), .in_4(\n16_4编码器_1_out_19 ),
    .in_5(\n16_4编码器_1_out_20 ), .in_6(\n16_4编码器_2_out_17 ), .in_7(\n16_4编码器_2_out_18 ),
    .in_8(\n16_4编码器_2_out_19 ), .in_9(\n16_4编码器_2_out_20 ), .out_10(out_34), .out_11(out_35),
    .out_12(out_36), .out_13(out_37), .out_14(out_38), .out_15(out_39), .out_16(out_40), .out_17(out_41),
    .in_1(in_10));
endmodule

module double_16key (
  input  in_1,
  input  in_2,
  input  in_3,
  input  in_4,
  input  in_5,
  input  in_6,
  input  in_7,
  input  in_8,
  input  in_9,
  input  in_10,
  input  in_11,
  input  in_12,
  input  in_13,
  input  in_14,
  input  in_15,
  input  in_16,
  input  in_17,
  input  in_18,
  input  in_19,
  input  in_20,
  input  in_21,
  input  in_22,
  input  in_23,
  input  in_24,
  input  in_25,
  input  in_26,
  input  in_27,
  input  in_28,
  input  in_29,
  input  in_30,
  input  in_31,
  input  in_32,
  input  in_33,
  input  in_34,
  input  in_35,
  input  in_36,
  output out_37,
  output out_38,
  output out_39,
  output out_40,
  output out_41,
  output out_42,
  output out_43,
  output out_44
);

  wire and_1_out, \n16_4编码器_1_out_17 , \n16_4编码器_1_out_18 , \n16_4编码器_1_out_19 , \n16_4编码器_1_out_20 ,
       \n16_4编码器_2_out_17 , \n16_4编码器_2_out_18 , \n16_4编码器_2_out_19 , \n16_4编码器_2_out_20 , reg8_1_out_10,
       reg8_1_out_11, reg8_1_out_12, reg8_1_out_13, reg8_1_out_14, reg8_1_out_15, reg8_1_out_16,
       reg8_1_out_17;

  \_16_4编码器  \u_16_4编码器_1  (
    .in_1(in_1), .in_2(in_2), .in_3(in_3), .in_4(in_4), .in_5(in_5), .in_6(in_6), .in_7(in_7), .in_8(in_8),
    .in_9(in_9), .in_10(in_12), .in_11(in_13), .in_12(in_14), .in_13(in_15), .in_14(in_16), .in_15(in_17),
    .in_16(in_18), .out_17(\n16_4编码器_1_out_17 ), .out_18(\n16_4编码器_1_out_18 ), .out_19(\n16_4编码器_1_out_19 ),
    .out_20(\n16_4编码器_1_out_20 ));
  \_16_4编码器  \u_16_4编码器_2  (
    .in_1(in_19), .in_2(in_20), .in_3(in_21), .in_4(in_22), .in_5(in_23), .in_6(in_24), .in_7(in_25),
    .in_8(in_26), .in_9(in_27), .in_10(in_28), .in_11(in_29), .in_12(in_32), .in_13(in_33), .in_14(in_34),
    .in_15(in_35), .in_16(in_36), .out_17(\n16_4编码器_2_out_17 ), .out_18(\n16_4编码器_2_out_18 ),
    .out_19(\n16_4编码器_2_out_19 ), .out_20(\n16_4编码器_2_out_20 ));
  C8 c8_1 (
    .in_2(\n16_4编码器_1_out_17 ), .in_3(\n16_4编码器_1_out_18 ), .in_4(\n16_4编码器_1_out_19 ),
    .in_5(\n16_4编码器_1_out_20 ), .in_6(\n16_4编码器_2_out_17 ), .in_7(\n16_4编码器_2_out_18 ),
    .in_8(\n16_4编码器_2_out_19 ), .in_9(\n16_4编码器_2_out_20 ), .out_10(out_37), .out_11(out_38),
    .out_12(out_39), .out_13(out_40), .out_14(out_41), .out_15(out_42), .out_16(out_43), .out_17(out_44),
    .in_1(in_10));
  reg8 reg8_1 (
    .in_1(\n16_4编码器_1_out_17 ), .in_2(\n16_4编码器_1_out_18 ), .in_3(\n16_4编码器_1_out_19 ),
    .in_4(\n16_4编码器_1_out_20 ), .in_5(\n16_4编码器_2_out_17 ), .in_6(\n16_4编码器_2_out_18 ),
    .in_7(\n16_4编码器_2_out_19 ), .in_9(\n16_4编码器_2_out_20 ), .in_8(in_30), .out_10(reg8_1_out_10),
    .out_11(reg8_1_out_11), .out_12(reg8_1_out_12), .out_13(reg8_1_out_13), .out_14(reg8_1_out_14),
    .out_15(reg8_1_out_15), .out_16(reg8_1_out_16), .out_17(reg8_1_out_17));
  C8 c8_2 (
    .in_2(and_1_out), .in_3(reg8_1_out_11), .in_4(reg8_1_out_12), .in_5(reg8_1_out_13), .in_6(reg8_1_out_14),
    .in_7(reg8_1_out_15), .in_8(reg8_1_out_16), .in_9(reg8_1_out_17), .out_10(out_37), .out_11(out_38),
    .out_12(out_39), .out_13(out_40), .out_14(out_41), .out_15(out_42), .out_16(out_43), .out_17(out_44),
    .in_1(in_11));
  and and_1 (and_1_out, reg8_1_out_10, in_31);
endmodule

module \验证  (
  input  in_1,
  input  in_2,
  input  in_3,
  input  in_4,
  input  in_5,
  input  in_6,
  input  in_7,
  input  in_8,
  input  in_9,
  input  in_10,
  input  in_11,
  input  in_12,
  input  in_13,
  input  in_14,
  input  in_15,
  input  in_16,
  input  in_17,
  input  in_18,
  input  in_19,
  input  in_20,
  input  in_21,
  input  in_22,
  input  in_23,
  input  in_24,
  input  in_25,
  input  in_26,
  input  in_27,
  input  in_28,
  input  in_29,
  input  in_30,
  input  in_31,
  input  in_32,
  input  in_33,
  input  in_34,
  input  in_35,
  input  in_36
);

  wire double_16key_1_out_37, double_16key_1_out_38, double_16key_1_out_39, double_16key_1_out_40,
       double_16key_1_out_41, double_16key_1_out_42, double_16key_1_out_43, double_16key_1_out_44;

  double_16key double_16key_1 (
    .in_1(in_1), .in_2(in_4), .in_3(in_5), .in_4(in_6), .in_5(in_7), .in_6(in_8), .in_7(in_9), .in_8(in_10),
    .in_9(in_11), .in_12(in_12), .in_13(in_13), .in_14(in_14), .in_15(in_15), .in_16(in_16), .in_17(in_17),
    .in_18(in_18), .in_19(in_19), .in_20(in_20), .in_21(in_21), .in_22(in_22), .in_23(in_23), .in_24(in_24),
    .in_25(in_25), .in_26(in_28), .in_27(in_29), .in_28(in_30), .in_29(in_31), .in_32(in_32), .in_33(in_33),
    .in_34(in_34), .in_35(in_35), .in_36(in_36), .out_37(double_16key_1_out_37),
    .out_38(double_16key_1_out_38), .out_39(double_16key_1_out_39), .out_40(double_16key_1_out_40),
    .out_41(double_16key_1_out_41), .out_42(double_16key_1_out_42), .out_43(double_16key_1_out_43),
    .out_44(double_16key_1_out_44), .in_10(in_2), .in_11(in_3), .in_30(in_26), .in_31(in_27));
  LED led_1 (.in(double_16key_1_out_37));
  LED led_2 (.in(double_16key_1_out_38));
  LED led_3 (.in(double_16key_1_out_41));
  LED led_4 (.in(double_16key_1_out_42));
  LED led_5 (.in(double_16key_1_out_39));
  LED led_6 (.in(double_16key_1_out_40));
  LED led_7 (.in(double_16key_1_out_43));
  LED led_8 (.in(double_16key_1_out_44));
endmodule

module \验证2  (
  input  in_1,
  input  in_2,
  input  in_3,
  input  in_4,
  input  in_5,
  input  in_6,
  input  in_7,
  input  in_8,
  input  in_9,
  input  in_10,
  input  in_11,
  input  in_12,
  input  in_13,
  input  in_14,
  input  in_15,
  input  in_16,
  input  in_17,
  input  in_18,
  input  in_19,
  input  in_20,
  input  in_21,
  input  in_22,
  input  in_23,
  input  in_24,
  input  in_25,
  input  in_26,
  input  in_27,
  input  in_28,
  input  in_29,
  input  in_30,
  input  in_31,
  input  in_32,
  input  in_33,
  input  in_34,
  input  in_35,
  input  in_36,
  input  in_37
);

  wire double_16key_1_out_37, double_16key_1_out_38, double_16key_1_out_39, double_16key_1_out_40,
       double_16key_1_out_41, double_16key_1_out_42, double_16key_1_out_43, double_16key_1_out_44,
       n2seg_1_out_10, n2seg_1_out_11, n2seg_1_out_12, n2seg_1_out_13, n2seg_1_out_14, n2seg_1_out_15,
       n2seg_1_out_16, n2seg_1_out_17, n2seg_1_out_18, n2seg_1_out_19, n2seg_1_out_20, n2seg_1_out_21,
       n2seg_1_out_22, n2seg_1_out_23;

  double_16key double_16key_1 (
    .in_1(in_2), .in_2(in_5), .in_3(in_6), .in_4(in_7), .in_5(in_8), .in_6(in_9), .in_7(in_10), .in_8(in_11),
    .in_9(in_12), .in_12(in_13), .in_13(in_14), .in_14(in_15), .in_15(in_16), .in_16(in_17), .in_17(in_18),
    .in_18(in_19), .in_19(in_20), .in_20(in_21), .in_21(in_22), .in_22(in_23), .in_23(in_24), .in_24(in_25),
    .in_25(in_26), .in_26(in_29), .in_27(in_30), .in_28(in_31), .in_29(in_32), .in_32(in_33), .in_33(in_34),
    .in_34(in_35), .in_35(in_36), .in_36(in_37), .out_37(double_16key_1_out_37),
    .out_38(double_16key_1_out_38), .out_39(double_16key_1_out_39), .out_40(double_16key_1_out_40),
    .out_41(double_16key_1_out_41), .out_42(double_16key_1_out_42), .out_43(double_16key_1_out_43),
    .out_44(double_16key_1_out_44), .in_10(in_3), .in_11(in_4), .in_30(in_27), .in_31(in_28));
  LED led_1 (.in(double_16key_1_out_37));
  LED led_2 (.in(double_16key_1_out_38));
  LED led_3 (.in(double_16key_1_out_41));
  LED led_4 (.in(double_16key_1_out_42));
  LED led_5 (.in(double_16key_1_out_39));
  LED led_6 (.in(double_16key_1_out_40));
  LED led_7 (.in(double_16key_1_out_43));
  LED led_8 (.in(double_16key_1_out_44));
  _2seg u_2seg_1 (
    .in_2(double_16key_1_out_37), .in_3(double_16key_1_out_38), .in_4(double_16key_1_out_39),
    .in_5(double_16key_1_out_40), .in_6(double_16key_1_out_41), .in_7(double_16key_1_out_42),
    .in_8(double_16key_1_out_43), .in_9(double_16key_1_out_44), .out_10(n2seg_1_out_10),
    .out_11(n2seg_1_out_11), .out_12(n2seg_1_out_12), .out_13(n2seg_1_out_13), .out_14(n2seg_1_out_14),
    .out_15(n2seg_1_out_15), .out_16(n2seg_1_out_16), .out_17(n2seg_1_out_17), .out_18(n2seg_1_out_18),
    .out_19(n2seg_1_out_19), .out_20(n2seg_1_out_20), .out_21(n2seg_1_out_21), .out_22(n2seg_1_out_22),
    .out_23(n2seg_1_out_23), .in_1(in_1));
  _7_Segment_Display #(.active("false")) u_7_segment_display_1 (
    .g(n2seg_1_out_16), .f(n2seg_1_out_15), .a(n2seg_1_out_10), .b(n2seg_1_out_11), .e(n2seg_1_out_14),
    .d(n2seg_1_out_13), .c(n2seg_1_out_12), .dp(1'b1));
  _7_Segment_Display #(.active("false")) u_7_segment_display_2 (
    .g(n2seg_1_out_23), .f(n2seg_1_out_22), .a(n2seg_1_out_17), .b(n2seg_1_out_18), .e(n2seg_1_out_21),
    .d(n2seg_1_out_20), .c(n2seg_1_out_19), .dp(1'b1));
endmodule
