// Logisim project 大二上.circ as structural Verilog: 40 circuits, main circuit main
module main (
);

  wire and_1_out, button_1_out, button_2_out, not_1_out, not_2_out;

  Button button_1 (.out(button_1_out));
  Button button_2 (.out(button_2_out));
  not not_1 (not_1_out, button_1_out);
  not not_2 (not_2_out, button_2_out);
  \锁存  \u_锁存_1  (.in_1(button_1_out), .in_2(and_1_out));  // open: out_3, out_4
  and and_1 (and_1_out, not_2_out, not_1_out);
endmodule

module \半加器  (
  input  in_1,
  input  in_2,
  output out_3,
  output out_4
);

  xor xor_1 (out_3, in_1, in_2);
  and and_1 (out_4, in_1, in_2);
endmodule

module \四位加法器  (
  input  in_1,
  input  in_2,
  input  in_3,
  input  in_4,
  input  in_5,
  input  in_6,
  input  in_7,
  input  in_8,
  output out_9,
  output out_10,
  output out_11,
  output out_12,
  output out_13
);

  wire \全加器_1_c_2 , \全加器_2_c_2 , \全加器_3_c_2 ;

  \全加器  \u_全加器_1  (.c(1'b0), .a(in_1), .b(in_2), .s(out_9), .c_2(\全加器_1_c_2 ));
  \全加器  \u_全加器_2  (.c(\全加器_1_c_2 ), .a(in_3), .b(in_4), .s(out_10), .c_2(\全加器_2_c_2 ));
  \全加器  \u_全加器_3  (.c(\全加器_2_c_2 ), .a(in_5), .b(in_6), .s(out_11), .c_2(\全加器_3_c_2 ));
  \全加器  \u_全加器_4  (.c(\全加器_3_c_2 ), .a(in_7), .b(in_8), .s(out_12), .c_2(out_13));
endmodule

module \全加器  (
  input  c,
  input  a,
  input  b,
  output s,
  output c_2
);

  wire \半加器_1_out_3 , \半加器_1_out_4 , \半加器_2_out_4 ;

  \半加器  \u_半加器_1  (.in_1(a), .in_2(b), .out_3(\半加器_1_out_3 ), .out_4(\半加器_1_out_4 ));
  \半加器  \u_半加器_2  (.in_1(c), .in_2(\半加器_1_out_3 ), .out_3(s), .out_4(\半加器_2_out_4 ));
  or or_1 (c_2, \半加器_2_out_4 , \半加器_1_out_4 );
endmodule

module \编码器  (
  input  in_1,
  input  in_2,
  input  in_3,
  input  in_4,
  input  in_5,
  input  in_6,
  input  in_7,
  input  in_8,
  output out_9,
  output out_10,
  output out_11
);

  or or_1 (out_9, in_5, in_6, in_7, in_8);
  or or_2 (out_10, in_4, in_3, in_7, in_8);
  or or_3 (out_11, in_6, in_4, in_8, in_2);
endmodule

module \_8_3优先编码器  (
  input  in_1,
  input  in_2,
  input  in_3,
  input  in_4,
  input  in_5,
  input  in_6,
  input  in_7,
  input  in_8,
  output out_9,
  output out_10,
  output out_11
);

  wire and_1_out, and_2_out, and_3_out, and_4_out, and_5_out, and_6_out, and_7_out, not_1_out, not_2_out,
       not_3_out, not_4_out, not_5_out, not_6_out, not_7_out;

  not not_1 (not_1_out, in_1);
  not not_2 (not_2_out, in_2);
  not not_3 (not_3_out, in_3);
  not not_4 (not_4_out, in_4);
  not not_5 (not_5_out, in_5);
  not not_6 (not_6_out, in_6);
  not not_7 (not_7_out, in_7);
  and and_1 (and_1_out, in_2, not_1_out);
  and and_2 (and_2_out, not_1_out, not_2_out, in_3);
  and and_3 (and_3_out, not_1_out, not_2_out, not_3_out, in_4);
  and and_4 (and_4_out, not_1_out, not_2_out, not_3_out, not_4_out, in_5);
  and and_5 (and_5_out, not_1_out, not_2_out, not_3_out, not_4_out, not_5_out, in_6);
  and and_6 (and_6_out, not_1_out, not_2_out, not_3_out, not_4_out, not_5_out, not_6_out, in_7);
  and and_7 (and_7_out, not_1_out, not_2_out, not_3_out, not_4_out, not_5_out, not_6_out, not_7_out, in_8);
  or or_1 (out_9, and_4_out, and_5_out, and_6_out, and_7_out);
  or or_2 (out_10, and_2_out, and_3_out, and_6_out, and_7_out);
  or or_3 (out_11, and_1_out, and_3_out, and_5_out, and_7_out);
endmodule

module \_16_4编码器  (
  input  in_1,
  input  in_2,
  input  in_3,
  input  in_4,
  input  in_5,
  input  in_6,
  input  in_7,
  input  in_8,
  input  in_9,
  input  in_10,
  input  in_11,
  input  in_12,
  input  in_13,
  input  in_14,
  input  in_15,
  input  in_16,
  output out_17,
  output out_18,
  output out_19,
  output out_20
);

  wire \n8_3优先编码器_1_out_9 , \n8_3优先编码器_1_out_10 , \n8_3优先编码器_1_out_11 , \n8_3优先编码器_2_out_9 ,
       \n8_3优先编码器_2_out_10 , \n8_3优先编码器_2_out_11 ;

  \_8_3优先编码器  \u_8_3优先编码器_1  (
    .in_1(in_1), .in_2(in_2), .in_3(in_3), .in_4(in_4), .in_5(in_5), .in_6(in_6), .in_7(in_7), .in_8(in_8),
    .out_9(\n8_3优先编码器_1_out_9 ), .out_10(\n8_3优先编码器_1_out_10 ), .out_11(\n8_3优先编码器_1_out_11 ));
  \_8_3优先编码器  \u_8_3优先编码器_2  (
    .in_1(in_9), .in_2(in_10), .in_3(in_11), .in_4(in_12), .in_5(in_13), .in_6(in_14), .in_7(in_15),
    .in_8(in_16), .out_9(\n8_3优先编码器_2_out_9 ), .out_10(\n8_3优先编码器_2_out_10 ), .out_11(\n8_3优先编码器_2_out_11 ));
  or or_1 (out_17, in_9, \n8_3优先编码器_2_out_9 , \n8_3优先编码器_2_out_10 , \n8_3优先编码器_2_out_11 );
  or or_2 (out_18, \n8_3优先编码器_1_out_9 , \n8_3优先编码器_2_out_9 );
  or or_3 (out_19, \n8_3优先编码器_1_out_10 , \n8_3优先编码器_2_out_10 );
  or or_4 (out_20, \n8_3优先编码器_1_out_11 , \n8_3优先编码器_2_out_11 );
endmodule

module \自锁电路  (
  input  a,
  input  b,
  input  c,
  input  d,
  input  e,
  input  f,
  input  g,
  input  h,
  output x,
  output y,
  output z
);

  wire not_1_out, not_2_out, not_3_out, not_4_out, not_5_out, not_6_out, not_7_out, not_8_out, not_9_out,
       not_10_out, not_11_out, not_12_out;

  not not_1 (not_1_out, a);
  not not_2 (not_2_out, b);
  not not_3 (not_3_out, c);
  not not_4 (not_4_out, d);
  not not_5 (not_5_out, a);
  not not_6 (not_6_out, b);
  not not_7 (not_7_out, e);
  not not_8 (not_8_out, f);
  not not_9 (not_9_out, a);
  not not_10 (not_10_out, c);
  not not_11 (not_11_out, e);
  not not_12 (not_12_out, g);
  and and_1 (x, not_1_out, not_2_out, not_3_out, not_4_out);
  and and_2 (y, not_5_out, not_6_out, not_7_out, not_8_out);
  and and_3 (z, not_9_out, not_10_out, not_11_out, not_12_out);
endmodule

module \_83编码器调用  (
  input  in_1,
  input  in_2,
  input  in_3,
  input  in_4,
  input  in_5,
  input  in_6,
  input  in_7,
  input  in_8,
  input  in_9,
  input  in_10,
  input  in_11,
  input  in_12,
  input  in_13,
  input  in_14,
  input  in_15,
  input  in_16,
  input  in_17,
  input  in_18,
  input  in_19,
  input  in_20,
  input  in_21,
  input  in_22,
  input  in_23,
  input  in_24,
  input  in_25,
  input  in_26,
  input  in_27,
  input  in_28,
  input  in_29,
  input  in_30,
  input  in_31,
  input  in_32,
  output out_33,
  output out_34,
  output out_35,
  output out_36,
  output out_37,
  output out_38,
  output out_39,
  output out_40,
  output out_41,
  output out_42
);

  \编码器  \u_编码器_1  (
    .in_1(in_1), .in_2(in_2), .in_3(in_3), .in_4(in_4), .in_5(in_5), .in_6(in_6), .in_7(in_7), .in_8(in_8),
    .out_9(out_33), .out_10(out_34), .out_11(out_35));
  \_8_3优先编码器  \u_8_3优先编码器_1  (
    .in_1(in_9), .in_2(in_10), .in_3(in_11), .in_4(in_12), .in_5(in_13), .in_6(in_14), .in_7(in_15),
    .in_8(in_16), .out_9(out_36), .out_10(out_37), .out_11(out_38));
  \_16_4编码器  \u_16_4编码器_1  (
    .in_1(in_17), .in_2(in_19), .in_3(in_21), .in_4(in_23), .in_5(in_25), .in_6(in_27), .in_7(in_29),
    .in_8(in_31), .in_9(in_18), .in_10(in_20), .in_11(in_22), .in_12(in_24), .in_13(in_26), .in_14(in_28),
    .in_15(in_30), .in_16(in_32), .out_17(out_39), .out_18(out_40), .out_19(out_41), .out_20(out_42));
endmodule

module \_3_8译码器  (
  input  in_1,
  input  in_2,
  input  in_3,
  input  in_4,
  output out_5,
  output out_6,
  output out_7,
  output out_8,
  output out_9,
  output out_10,
  output out_11,
  output out_12
);

  wire and_1_out, and_3_out, and_5_out, and_7_out, and_9_out, and_11_out, and_13_out, and_15_out, not_1_out,
       not_2_out, not_3_out, not_4_out;

  not not_1 (not_1_out, in_1);
  not not_2 (not_2_out, in_2);
  not not_3 (not_3_out, in_4);
  not not_4 (not_4_out, in_3);
  and and_1 (and_1_out, not_1_out, not_2_out, not_4_out);
  and and_2 (out_5, and_1_out, not_3_out);
  and and_3 (and_3_out, in_1, not_2_out, not_4_out);
  and and_4 (out_6, and_3_out, not_3_out);
  and and_5 (and_5_out, not_1_out, in_2, not_4_out);
  and and_6 (out_7, and_5_out, not_3_out);
  and and_7 (and_7_out, in_1, in_2, not_4_out);
  and and_8 (out_8, and_7_out, not_3_out);
  and and_9 (and_9_out, not_1_out, not_2_out, in_3);
  and and_10 (out_9, and_9_out, not_3_out);
  and and_11 (and_11_out, in_1, not_2_out, in_3);
  and and_12 (out_10, and_11_out, not_3_out);
  and and_13 (and_13_out, not_1_out, in_2, in_3);
  and and_14 (out_11, and_13_out, not_3_out);
  and and_15 (and_15_out, in_1, in_2, in_3);
  and and_16 (out_12, and_15_out, not_3_out);
endmodule

module \半减器  (
  input  in_1,
  input  in_2,
  input  in_3,
  output out_4,
  output out_5
);

  wire and_1_out, and_2_out, not_1_out, not_2_out, xor_1_out;

  not not_1 (not_1_out, in_1);
  xor xor_1 (xor_1_out, in_1, in_2);
  and and_1 (and_1_out, in_2, not_1_out);
  not not_2 (not_2_out, xor_1_out);
  and and_2 (and_2_out, in_3, not_2_out);
  xor xor_2 (out_4, in_3, xor_1_out);
  or or_1 (out_5, and_1_out, and_2_out);
endmodule

module \全减器  (
  input  in_1,
  input  in_2,
  input  in_3,
  input  in_4,
  input  in_5,
  input  in_6,
  input  in_7,
  input  in_8,
  input  in_9,
  input  in_10,
  input  in_11,
  output out_12,
  output out_13,
  output out_14,
  output out_15,
  output out_16,
  output out_17
);

  wire \半减器_1_out_5 , \半减器_2_out_5 , \半减器_3_out_5 , \半减器_4_out_5 ;

  \半减器  \u_半减器_1  (.in_1(in_2), .in_2(in_3), .in_3(in_1), .out_4(out_12), .out_5(\半减器_1_out_5 ));
  \半减器  \u_半减器_2  (.in_1(in_4), .in_2(in_5), .in_3(\半减器_1_out_5 ), .out_4(out_13), .out_5(\半减器_2_out_5 ));
  \半减器  \u_半减器_3  (.in_1(in_6), .in_2(in_7), .in_3(\半减器_2_out_5 ), .out_4(out_14), .out_5(\半减器_3_out_5 ));
  \半减器  \u_半减器_4  (.in_1(in_8), .in_2(in_9), .in_3(\半减器_3_out_5 ), .out_4(out_15), .out_5(\半减器_4_out_5 ));
  \半减器  \u_半减器_5  (.in_1(in_10), .in_2(in_11), .in_3(\半减器_4_out_5 ), .out_4(out_16), .out_5(out_17));
endmodule

module \_4_16译码器  (
  input  in_1,
  input  in_2,
  input  in_3,
  input  in_4,
  output out_5,
  output out_6,
  output out_7,
  output out_8,
  output out_9,
  output out_10,
  output out_11,
  output out_12,
  output out_13,
  output out_14,
  output out_15,
  output out_16,
  output out_17,
  output out_18,
  output out_19,
  output out_20
);

  wire not_1_out;

  not not_1 (not_1_out, in_4);
  \_3_8译码器  \u_3_8译码器_1  (
    .in_1(in_1), .in_2(in_2), .in_3(in_3), .out_5(out_5), .in_4(in_4), .out_6(out_6), .out_7(out_7),
    .out_8(out_8), .out_9(out_9), .out_10(out_10), .out_11(out_11), .out_12(out_12));
  \_3_8译码器  \u_3_8译码器_2  (
    .in_1(in_1), .in_2(in_2), .in_3(in_3), .out_5(out_13), .in_4(not_1_out), .out_6(out_14), .out_7(out_15),
    .out_8(out_16), .out_9(out_17), .out_10(out_18), .out_11(out_19), .out_12(out_20));
endmodule

module \译码器调用  (
  input  in_1,
  input  in_2,
  input  in_3,
  input  in_4,
  input  in_5,
  input  in_6,
  input  in_7,
  input  in_8,
  input  in_9,
  input  in_10,
  input  in_11,
  output out_12,
  output out_13,
  output out_14,
  output out_15,
  output out_16,
  output out_17,
  output out_18,
  output out_19,
  output out_20,
  output out_21,
  output out_22,
  output out_23,
  output out_24,
  output out_25,
  output out_26,
  output out_27,
  output out_28,
  output out_29
);

  wire and_1_out, \n4_16译码器_1_out_5 , \n4_16译码器_1_out_6 , \n4_16译码器_1_out_7 , \n4_16译码器_1_out_8 ,
       \n4_16译码器_1_out_9 , \n4_16译码器_1_out_10 , \n4_16译码器_1_out_11 , \n4_16译码器_1_out_12 ,
       \n4_16译码器_1_out_13 , \n4_16译码器_1_out_14 , \n4_16译码器_1_out_15 , \n4_16译码器_1_out_16 ,
       \n4_16译码器_1_out_17 , \n4_16译码器_1_out_18 , \n4_16译码器_1_out_19 , \n4_16译码器_1_out_20 ,
       \n16_4编码器_1_out_17 , \n16_4编码器_1_out_18 , \n16_4编码器_1_out_19 , \n16_4编码器_1_out_20 , or_1_out,
       pull_resistor_1_node, \数码管_1_s , \数码管_1_u , \数码管_1_v , \数码管_1_w , \数码管_1_x , \数码管_1_y , \数码管_1_z ;

  Pull_Resistor pull_resistor_1 (.node(pull_resistor_1_node));
  or or_1 (or_1_out, in_10, in_9);
  \_3_8译码器  \u_3_8译码器_1  (
    .in_1(in_5), .in_2(in_6), .in_3(in_7), .out_5(out_16), .in_4(pull_resistor_1_node), .out_6(out_18),
    .out_7(out_20), .out_8(out_22), .out_9(out_24), .out_10(out_26), .out_11(out_28), .out_12(out_29));
  \_4_16译码器  \u_4_16译码器_1  (
    .in_1(in_11), .in_2(in_10), .in_3(in_9), .in_4(in_8), .out_5(\n4_16译码器_1_out_5 ),
    .out_6(\n4_16译码器_1_out_6 ), .out_7(\n4_16译码器_1_out_7 ), .out_8(\n4_16译码器_1_out_8 ),
    .out_9(\n4_16译码器_1_out_9 ), .out_10(\n4_16译码器_1_out_10 ), .out_11(\n4_16译码器_1_out_11 ),
    .out_12(\n4_16译码器_1_out_12 ), .out_13(\n4_16译码器_1_out_13 ), .out_14(\n4_16译码器_1_out_14 ),
    .out_15(\n4_16译码器_1_out_15 ), .out_16(\n4_16译码器_1_out_16 ), .out_17(\n4_16译码器_1_out_17 ),
    .out_18(\n4_16译码器_1_out_18 ), .out_19(\n4_16译码器_1_out_19 ), .out_20(\n4_16译码器_1_out_20 ));
  and and_1 (and_1_out, or_1_out, in_8);
  \_16_4编码器  \u_16_4编码器_1  (
    .in_1(\n4_16译码器_1_out_5 ), .in_2(\n4_16译码器_1_out_6 ), .in_3(\n4_16译码器_1_out_7 ),
    .in_4(\n4_16译码器_1_out_8 ), .in_5(\n4_16译码器_1_out_9 ), .in_6(\n4_16译码器_1_out_10 ),
    .in_7(\n4_16译码器_1_out_11 ), .in_8(\n4_16译码器_1_out_12 ), .in_9(\n4_16译码器_1_out_13 ),
    .in_10(\n4_16译码器_1_out_14 ), .in_11(\n4_16译码器_1_out_15 ), .in_12(\n4_16译码器_1_out_16 ),
    .in_13(\n4_16译码器_1_out_17 ), .in_14(\n4_16译码器_1_out_18 ), .in_15(\n4_16译码器_1_out_19 ),
    .in_16(\n4_16译码器_1_out_20 ), .out_17(\n16_4编码器_1_out_17 ), .out_18(\n16_4编码器_1_out_18 ),
    .out_19(\n16_4编码器_1_out_19 ), .out_20(\n16_4编码器_1_out_20 ));
  \数码管  \u_数码管_1  (
    .a(\n16_4编码器_1_out_17 ), .b(\n16_4编码器_1_out_18 ), .x(\数码管_1_x ), .c(\n16_4编码器_1_out_19 ),
    .d(\n16_4编码器_1_out_20 ), .y(\数码管_1_y ), .z(\数码管_1_z ), .u(\数码管_1_u ), .v(\数码管_1_v ), .w(\数码管_1_w ),
    .s(\数码管_1_s ));
  \_2_10译码器  \u_2_10译码器_1  (
    .in_1(in_4), .in_2(in_3), .in_3(in_2), .in_4(in_1), .out_5(out_12), .out_6(out_13), .out_7(out_14),
    .out_8(out_15), .out_9(out_17), .out_10(out_19), .out_11(out_21), .out_12(out_23), .out_13(out_25),
    .out_14(out_27));
  _7_Segment_Display u_7_segment_display_1 (.b(and_1_out), .c(and_1_out));  // open: g, f, a, e, d, dp
  _7_Segment_Display u_7_segment_display_2 (
    .g(\数码管_1_s ), .f(\数码管_1_w ), .a(\数码管_1_x ), .b(\数码管_1_y ), .e(\数码管_1_v ), .d(\数码管_1_u ), .c(\数码管_1_z ));  // open: dp
endmodule

module \数码管  (
  input  a,
  input  b,
  input  c,
  input  d,
  output x,
  output y,
  output z,
  output u,
  output v,
  output w,
  output s
);

  wire and_1_out, and_2_out, and_3_out, and_4_out, and_5_out, and_6_out, and_7_out, and_8_out, and_9_out,
       and_10_out, and_11_out, and_12_out, and_13_out, and_14_out, and_15_out, and_16_out, and_17_out,
       and_18_out, and_19_out, and_20_out, and_21_out, and_22_out, and_23_out, and_24_out, and_25_out,
       and_26_out, and_27_out, and_28_out, and_29_out, and_30_out, and_31_out, not_1_out, not_2_out,
       not_3_out, not_4_out, not_5_out, not_6_out, not_7_out, not_8_out, not_9_out, not_10_out, not_11_out,
       not_12_out, not_13_out, not_14_out, not_15_out, not_16_out, not_17_out, not_18_out, not_19_out,
       not_20_out, not_21_out, not_22_out, not_23_out, not_24_out, not_25_out, not_26_out, not_27_out,
       not_28_out, not_29_out, not_30_out, not_31_out, not_32_out, not_33_out, not_34_out, not_35_out,
       not_36_out, not_37_out, not_38_out, not_39_out, not_40_out, not_41_out, not_42_out, not_43_out;

  not not_1 (not_1_out, b);
  and and_1 (and_1_out, not_1_out, not_2_out);
  not not_2 (not_2_out, d);
  not not_3 (not_3_out, a);
  and and_2 (and_2_out, not_3_out, c);
  and and_3 (and_3_out, b, d);
  and and_4 (and_4_out, a, not_4_out);
  not not_4 (not_4_out, c);
  not not_5 (not_5_out, b);
  not not_6 (not_6_out, c);
  and and_5 (and_5_out, not_6_out, not_7_out);
  not not_7 (not_7_out, d);
  not not_8 (not_8_out, a);
  and and_6 (and_6_out, not_8_out, c, d);
  and and_7 (and_7_out, a, not_9_out);
  not not_9 (not_9_out, c);
  and and_8 (and_8_out, a, not_10_out);
  not not_10 (not_10_out, d);
  not not_11 (not_11_out, a);
  and and_9 (and_9_out, not_11_out, not_12_out);
  not not_12 (not_12_out, c);
  and and_10 (and_10_out, b, c);
  and and_11 (and_11_out, a, not_13_out);
  not not_13 (not_13_out, b);
  not not_14 (not_14_out, b);
  and and_12 (and_12_out, not_14_out, not_15_out);
  not not_15 (not_15_out, d);
  not not_16 (not_16_out, a);
  and and_13 (and_13_out, not_16_out, not_17_out, c);
  not not_17 (not_17_out, b);
  not not_18 (not_18_out, a);
  and and_14 (and_14_out, not_18_out, c, not_19_out);
  not not_19 (not_19_out, d);
  and and_15 (and_15_out, b, not_20_out, d);
  not not_20 (not_20_out, c);
  and and_16 (and_16_out, a, not_21_out);
  not not_21 (not_21_out, c);
  and and_17 (and_17_out, a, b, d);
  not not_22 (not_22_out, b);
  and and_18 (and_18_out, not_22_out, not_23_out);
  not not_23 (not_23_out, d);
  not not_24 (not_24_out, a);
  and and_19 (and_19_out, not_24_out, c, not_25_out);
  not not_25 (not_25_out, d);
  not not_26 (not_26_out, c);
  and and_20 (and_20_out, a, not_26_out, not_27_out);
  not not_27 (not_27_out, d);
  not not_28 (not_28_out, a);
  not not_29 (not_29_out, c);
  and and_21 (and_21_out, not_28_out, not_29_out, not_30_out);
  not not_30 (not_30_out, d);
  not not_31 (not_31_out, a);
  and and_22 (and_22_out, not_31_out, b, not_32_out);
  not not_32 (not_32_out, c);
  not not_33 (not_33_out, a);
  and and_23 (and_23_out, not_33_out, b, not_34_out);
  not not_34 (not_34_out, d);
  and and_24 (and_24_out, a, not_35_out, not_36_out);
  not not_35 (not_35_out, b);
  not not_36 (not_36_out, c);
  and and_25 (and_25_out, a, not_37_out, not_38_out);
  not not_37 (not_37_out, b);
  not not_38 (not_38_out, d);
  and and_26 (and_26_out, a, b, c);
  not not_39 (not_39_out, a);
  and and_27 (and_27_out, not_39_out, not_40_out, c);
  not not_40 (not_40_out, b);
  and and_28 (and_28_out, b, not_41_out);
  not not_41 (not_41_out, c);
  and and_29 (and_29_out, b, not_42_out);
  not not_42 (not_42_out, d);
  and and_30 (and_30_out, a, not_43_out);
  not not_43 (not_43_out, c);
  and and_31 (and_31_out, a, b);
  or or_1 (x, and_1_out, and_2_out, and_3_out, and_4_out);
  or or_2 (y, not_5_out, and_5_out, and_6_out, and_7_out, and_8_out);
  or or_3 (z, and_9_out, d, and_10_out, and_11_out);
  or or_4 (v, and_18_out, and_19_out, and_20_out);
  or or_5 (s, and_27_out, and_28_out, and_29_out, and_30_out, and_31_out);
  or or_6 (u, and_12_out, and_13_out, and_14_out, and_15_out, and_16_out, and_17_out);
  or or_7 (w, and_21_out, and_22_out, and_23_out, and_24_out, and_25_out, and_26_out);
endmodule

module \_2_10译码器  (
  input  in_1,
  input  in_2,
  input  in_3,
  input  in_4,
  output out_5,
  output out_6,
  output out_7,
  output out_8,
  output out_9,
  output out_10,
  output out_11,
  output out_12,
  output out_13,
  output out_14
);

  wire not_1_out;

  not not_1 (not_1_out, in_4);
  \_3_8译码器  \u_3_8译码器_1  (
    .in_1(in_1), .in_2(in_2), .in_3(in_3), .out_5(out_5), .in_4(in_4), .out_6(out_6), .out_7(out_7),
    .out_8(out_8), .out_9(out_9), .out_10(out_10), .out_11(out_11), .out_12(out_12));
  \_3_8译码器  \u_3_8译码器_2  (
    .in_1(in_1), .in_2(in_2), .in_3(in_3), .out_5(out_13), .in_4(not_1_out), .out_6(out_14));  // open: out_7, out_8, out_9, out_10, out_11, out_12
endmodule

module _16_4to4_16 (
  input  in_1,
  input  in_2,
  input  in_3,
  input  in_4,
  input  in_5,
  input  in_6,
  input  in_7,
  input  in_8,
  input  in_9,
  input  in_10,
  input  in_11,
  input  in_12,
  input  in_13,
  input  in_14,
  input  in_15,
  input  in_16,
  output out_17,
  output out_18,
  output out_19,
  output out_20,
  output out_21,
  output out_22,
  output out_23,
  output out_24,
  output out_25,
  output out_26,
  output out_27,
  output out_28,
  output out_29,
  output out_30,
  output out_31,
  output out_32
);

  wire and_1_out, \n16_4编码器_1_out_17 , \n16_4编码器_1_out_18 , \n16_4编码器_1_out_19 , \n16_4编码器_1_out_20 ,
       or_1_out, \数码管_1_s , \数码管_1_u , \数码管_1_v , \数码管_1_w , \数码管_1_x , \数码管_1_y , \数码管_1_z ;

  \_16_4编码器  \u_16_4编码器_1  (
    .in_1(in_1), .in_2(in_2), .in_3(in_3), .in_4(in_4), .in_5(in_5), .in_6(in_6), .in_7(in_7), .in_8(in_8),
    .in_9(in_9), .in_10(in_10), .in_11(in_11), .in_12(in_12), .in_13(in_13), .in_14(in_14), .in_15(in_15),
    .in_16(in_16), .out_17(\n16_4编码器_1_out_17 ), .out_18(\n16_4编码器_1_out_18 ), .out_19(\n16_4编码器_1_out_19 ),
    .out_20(\n16_4编码器_1_out_20 ));
  or or_1 (or_1_out, \n16_4编码器_1_out_19 , \n16_4编码器_1_out_18 );
  \_4_16译码器  \u_4_16译码器_1  (
    .in_1(\n16_4编码器_1_out_20 ), .in_2(\n16_4编码器_1_out_19 ), .in_3(\n16_4编码器_1_out_18 ),
    .in_4(\n16_4编码器_1_out_17 ), .out_5(out_17), .out_6(out_18), .out_7(out_19), .out_8(out_20),
    .out_9(out_21), .out_10(out_22), .out_11(out_23), .out_12(out_24), .out_13(out_25), .out_14(out_26),
    .out_15(out_27), .out_16(out_28), .out_17(out_29), .out_18(out_30), .out_19(out_31), .out_20(out_32));
  \数码管  \u_数码管_1  (
    .a(\n16_4编码器_1_out_17 ), .b(\n16_4编码器_1_out_18 ), .x(\数码管_1_x ), .c(\n16_4编码器_1_out_19 ),
    .d(\n16_4编码器_1_out_20 ), .y(\数码管_1_y ), .z(\数码管_1_z ), .u(\数码管_1_u ), .v(\数码管_1_v ), .w(\数码管_1_w ),
    .s(\数码管_1_s ));
  and and_1 (and_1_out, or_1_out, \n16_4编码器_1_out_17 );
  _7_Segment_Display u_7_segment_display_1 (.b(and_1_out), .c(and_1_out));  // open: g, f, a, e, d, dp
  _7_Segment_Display u_7_segment_display_2 (
    .g(\数码管_1_s ), .f(\数码管_1_w ), .a(\数码管_1_x ), .b(\数码管_1_y ), .e(\数码管_1_v ), .d(\数码管_1_u ), .c(\数码管_1_z ));  // open: dp
endmodule

module \锁存  (
  input  in_1,
  input  in_2,
  output out_3,
  output out_4
);

  nand nand_1 (out_3, in_1, out_4);
  nand nand_2 (out_4, out_3, in_2);
endmodule

module \数码管调用  (
  input  in_1,
  input  in_2,
  input  in_3,
  input  in_4
);

  wire \数码管_1_s , \数码管_1_u , \数码管_1_v , \数码管_1_w , \数码管_1_x , \数码管_1_y , \数码管_1_z ;

  \数码管  \u_数码管_1  (
    .a(in_1), .b(in_2), .x(\数码管_1_x ), .c(in_3), .d(in_4), .y(\数码管_1_y ), .z(\数码管_1_z ), .u(\数码管_1_u ),
    .v(\数码管_1_v ), .w(\数码管_1_w ), .s(\数码管_1_s ));
  _7_Segment_Display u_7_segment_display_1 (
    .g(\数码管_1_s ), .f(\数码管_1_w ), .a(\数码管_1_x ), .b(\数码管_1_y ), .e(\数码管_1_v ), .d(\数码管_1_u ), .c(\数码管_1_z ));  // open: dp
endmodule

module \总线1  (
  input  in_1,
  input  in_2,
  input  in_3,
  input  in_4,
  input  in_5,
  input  in_6,
  input  in_7,
  input  in_8,
  output out_9,
  output out_10,
  output out_11,
  output out_12,
  output out_13,
  output out_14,
  output out_15
);

  wire \n8_3优先编码器_1_out_9 , \n8_3优先编码器_1_out_10 , \n8_3优先编码器_1_out_11 , pull_resistor_1_node,
       pull_resistor_2_node, \数码管_1_s , \数码管_1_u , \数码管_1_v , \数码管_1_w , \数码管_1_x , \数码管_1_y , \数码管_1_z ;

  \_8_3优先编码器  \u_8_3优先编码器_1  (
    .in_1(in_1), .in_2(in_2), .in_3(in_3), .in_4(in_4), .in_5(in_5), .in_6(in_6), .in_7(in_7), .in_8(in_8),
    .out_9(\n8_3优先编码器_1_out_9 ), .out_10(\n8_3优先编码器_1_out_10 ), .out_11(\n8_3优先编码器_1_out_11 ));
  LED led_1 (.in(\n8_3优先编码器_1_out_9 ));
  LED led_2 (.in(\n8_3优先编码器_1_out_10 ));
  LED led_3 (.in(\n8_3优先编码器_1_out_11 ));
  \数码管  \u_数码管_1  (
    .a(\n8_3优先编码器_1_out_9 ), .b(\n8_3优先编码器_1_out_10 ), .x(\数码管_1_x ), .c(\n8_3优先编码器_1_out_11 ),
    .d(pull_resistor_1_node), .y(\数码管_1_y ), .z(\数码管_1_z ), .u(\数码管_1_u ), .v(\数码管_1_v ), .w(\数码管_1_w ),
    .s(\数码管_1_s ));
  Pull_Resistor pull_resistor_1 (.node(pull_resistor_1_node));
  Pull_Resistor pull_resistor_2 (.node(pull_resistor_2_node));
  \_3_8译码器  \u_3_8译码器_1  (
    .in_1(\n8_3优先编码器_1_out_11 ), .in_2(\n8_3优先编码器_1_out_10 ), .in_3(\n8_3优先编码器_1_out_9 ), .out_5(out_9),
    .in_4(pull_resistor_2_node), .out_6(out_10), .out_7(out_11), .out_8(out_12), .out_9(out_13),
    .out_10(out_14), .out_11(out_15));  // open: out_12
  _7_Segment_Display u_7_segment_display_1 (
    .g(\数码管_1_s ), .f(\数码管_1_w ), .a(\数码管_1_x ), .b(\数码管_1_y ), .e(\数码管_1_v ), .d(\数码管_1_u ), .c(\数码管_1_z ));  // open: dp
endmodule

module \三位控制器  (
  input  in_1,
  input  in_2,
  input  in_3,
  input  in_4,
  output out_5,
  output out_6,
  output out_7
);

  assign out_5 = in_1 ? in_2 : 1'bz;  // Controlled_Buffer controlled_buffer_1
  assign out_6 = in_1 ? in_3 : 1'bz;  // Controlled_Buffer controlled_buffer_2
  assign out_7 = in_1 ? in_4 : 1'bz;  // Controlled_Buffer controlled_buffer_3
endmodule

module \总线2  (
  input  in_1,
  input  in_2,
  input  in_3,
  input  in_4,
  input  in_5,
  input  in_6,
  input  in_7,
  input  in_8,
  input  in_9,
  input  in_10,
  input  in_11,
  input  in_12,
  input  in_13,
  input  in_14,
  input  in_15,
  input  in_16,
  input  in_17,
  input  in_18,
  output out_19,
  output out_20,
  output out_21,
  output out_22,
  output out_23,
  output out_24,
  output out_25
);

  wire \n8_3优先编码器_1_out_9 , \n8_3优先编码器_1_out_10 , \n8_3优先编码器_1_out_11 , \n8_3优先编码器_2_out_9 ,
       \n8_3优先编码器_2_out_10 , \n8_3优先编码器_2_out_11 , pull_resistor_1_node, pull_resistor_2_node,
       \三位控制器_1_out_5 , \三位控制器_1_out_6 , \三位控制器_1_out_7 , \数码管_1_s , \数码管_1_u , \数码管_1_v , \数码管_1_w ,
       \数码管_1_x , \数码管_1_y , \数码管_1_z ;

  \_8_3优先编码器  \u_8_3优先编码器_1  (
    .in_1(in_2), .in_2(in_3), .in_3(in_4), .in_4(in_5), .in_5(in_6), .in_6(in_7), .in_7(in_8), .in_8(in_9),
    .out_9(\n8_3优先编码器_1_out_9 ), .out_10(\n8_3优先编码器_1_out_10 ), .out_11(\n8_3优先编码器_1_out_11 ));
  \_8_3优先编码器  \u_8_3优先编码器_2  (
    .in_1(in_11), .in_2(in_12), .in_3(in_13), .in_4(in_14), .in_5(in_15), .in_6(in_16), .in_7(in_17),
    .in_8(in_18), .out_9(\n8_3优先编码器_2_out_9 ), .out_10(\n8_3优先编码器_2_out_10 ), .out_11(\n8_3优先编码器_2_out_11 ));
  \三位控制器  \u_三位控制器_1  (
    .in_2(\n8_3优先编码器_1_out_11 ), .in_3(\n8_3优先编码器_1_out_10 ), .in_4(\n8_3优先编码器_1_out_9 ), .in_1(in_1),
    .out_5(\三位控制器_1_out_5 ), .out_6(\三位控制器_1_out_6 ), .out_7(\三位控制器_1_out_7 ));
  \三位控制器  \u_三位控制器_2  (
    .in_2(\n8_3优先编码器_2_out_11 ), .in_3(\n8_3优先编码器_2_out_10 ), .in_4(\n8_3优先编码器_2_out_9 ), .in_1(in_10),
    .out_5(\三位控制器_1_out_5 ), .out_6(\三位控制器_1_out_6 ), .out_7(\三位控制器_1_out_7 ));
  LED led_1 (.in(\三位控制器_1_out_7 ));
  LED led_2 (.in(\三位控制器_1_out_5 ));
  LED led_3 (.in(\三位控制器_1_out_6 ));
  \数码管  \u_数码管_1  (
    .a(\三位控制器_1_out_7 ), .b(\三位控制器_1_out_6 ), .x(\数码管_1_x ), .c(\三位控制器_1_out_5 ), .d(pull_resistor_1_node),
    .y(\数码管_1_y ), .z(\数码管_1_z ), .u(\数码管_1_u ), .v(\数码管_1_v ), .w(\数码管_1_w ), .s(\数码管_1_s ));
  Pull_Resistor pull_resistor_1 (.node(pull_resistor_1_node));
  Pull_Resistor pull_resistor_2 (.node(pull_resistor_2_node));
  \_3_8译码器  \u_3_8译码器_1  (
    .in_1(\三位控制器_1_out_5 ), .in_2(\三位控制器_1_out_6 ), .in_3(\三位控制器_1_out_7 ), .out_5(out_19),
    .in_4(pull_resistor_2_node), .out_6(out_20), .out_7(out_21), .out_8(out_22), .out_9(out_23),
    .out_10(out_24), .out_11(out_25));  // open: out_12
  _7_Segment_Display u_7_segment_display_1 (
    .g(\数码管_1_s ), .f(\数码管_1_w ), .a(\数码管_1_x ), .b(\数码管_1_y ), .e(\数码管_1_v ), .d(\数码管_1_u ), .c(\数码管_1_z ));  // open: dp
endmodule

module \实验3验收  (
  input  in_1,
  input  in_2,
  input  in_3,
  input  in_4,
  input  in_5,
  input  in_6,
  input  in_7,
  input  in_8,
  input  in_9,
  input  in_10,
  input  in_11,
  input  in_12,
  input  in_13,
  input  in_14,
  input  in_15,
  input  in_16,
  input  in_17,
  input  in_18,
  input  in_19,
  input  in_20,
  input  in_21,
  input  in_22,
  input  in_23,
  input  in_24,
  input  in_25,
  input  in_26,
  input  in_27,
  output out_28,
  output out_29,
  output out_30,
  output out_31,
  output out_32,
  output out_33,
  output out_34,
  output out_35,
  output out_36,
  output out_37,
  output out_38,
  output out_39,
  output out_40,
  output out_41,
  output out_42,
  output out_43,
  output out_44,
  output out_45,
  output out_46,
  output out_47,
  output out_48,
  output out_49,
  output out_50,
  output out_51,
  output out_52,
  output out_53,
  output out_54,
  output out_55,
  output out_56,
  output out_57,
  output out_58,
  output out_59,
  output out_60,
  output out_61
);

  wire and_1_out, and_2_out, \n4_16译码器_1_out_5 , \n4_16译码器_1_out_6 , \n4_16译码器_1_out_7 , \n4_16译码器_1_out_8 ,
       \n4_16译码器_1_out_9 , \n4_16译码器_1_out_10 , \n4_16译码器_1_out_11 , \n4_16译码器_1_out_12 ,
       \n4_16译码器_1_out_13 , \n4_16译码器_1_out_14 , \n4_16译码器_1_out_15 , \n4_16译码器_1_out_16 ,
       \n4_16译码器_1_out_17 , \n4_16译码器_1_out_18 , \n4_16译码器_1_out_19 , \n4_16译码器_1_out_20 ,
       \n16_4编码器_1_out_17 , \n16_4编码器_1_out_18 , \n16_4编码器_1_out_19 , \n16_4编码器_1_out_20 ,
       \n16_4编码器_2_out_17 , \n16_4编码器_2_out_18 , \n16_4编码器_2_out_19 , \n16_4编码器_2_out_20 , or_1_out,
       or_2_out, pull_resistor_1_node, \数码管_1_s , \数码管_1_u , \数码管_1_v , \数码管_1_w , \数码管_1_x , \数码管_1_y ,
       \数码管_1_z , \数码管_2_s , \数码管_2_u , \数码管_2_v , \数码管_2_w , \数码管_2_x , \数码管_2_y , \数码管_2_z ;

  Pull_Resistor pull_resistor_1 (.node(pull_resistor_1_node));
  or or_1 (or_1_out, in_10, in_9);
  \_3_8译码器  \u_3_8译码器_1  (
    .in_1(in_5), .in_2(in_6), .in_3(in_7), .out_5(out_32), .in_4(pull_resistor_1_node), .out_6(out_34),
    .out_7(out_36), .out_8(out_38), .out_9(out_40), .out_10(out_42), .out_11(out_44), .out_12(out_45));
  \_4_16译码器  \u_4_16译码器_1  (
    .in_1(in_11), .in_2(in_10), .in_3(in_9), .in_4(in_8), .out_5(\n4_16译码器_1_out_5 ),
    .out_6(\n4_16译码器_1_out_6 ), .out_7(\n4_16译码器_1_out_7 ), .out_8(\n4_16译码器_1_out_8 ),
    .out_9(\n4_16译码器_1_out_9 ), .out_10(\n4_16译码器_1_out_10 ), .out_11(\n4_16译码器_1_out_11 ),
    .out_12(\n4_16译码器_1_out_12 ), .out_13(\n4_16译码器_1_out_13 ), .out_14(\n4_16译码器_1_out_14 ),
    .out_15(\n4_16译码器_1_out_15 ), .out_16(\n4_16译码器_1_out_16 ), .out_17(\n4_16译码器_1_out_17 ),
    .out_18(\n4_16译码器_1_out_18 ), .out_19(\n4_16译码器_1_out_19 ), .out_20(\n4_16译码器_1_out_20 ));
  and and_1 (and_1_out, or_1_out, in_8);
  \_16_4编码器  \u_16_4编码器_1  (
    .in_1(\n4_16译码器_1_out_5 ), .in_2(\n4_16译码器_1_out_6 ), .in_3(\n4_16译码器_1_out_7 ),
    .in_4(\n4_16译码器_1_out_8 ), .in_5(\n4_16译码器_1_out_9 ), .in_6(\n4_16译码器_1_out_10 ),
    .in_7(\n4_16译码器_1_out_11 ), .in_8(\n4_16译码器_1_out_12 ), .in_9(\n4_16译码器_1_out_13 ),
    .in_10(\n4_16译码器_1_out_14 ), .in_11(\n4_16译码器_1_out_15 ), .in_12(\n4_16译码器_1_out_16 ),
    .in_13(\n4_16译码器_1_out_17 ), .in_14(\n4_16译码器_1_out_18 ), .in_15(\n4_16译码器_1_out_19 ),
    .in_16(\n4_16译码器_1_out_20 ), .out_17(\n16_4编码器_1_out_17 ), .out_18(\n16_4编码器_1_out_18 ),
    .out_19(\n16_4编码器_1_out_19 ), .out_20(\n16_4编码器_1_out_20 ));
  \_16_4编码器  \u_16_4编码器_2  (
    .in_1(in_12), .in_2(in_13), .in_3(in_14), .in_4(in_15), .in_5(in_16), .in_6(in_17), .in_7(in_18),
    .in_8(in_19), .in_9(in_20), .in_10(in_21), .in_11(in_22), .in_12(in_23), .in_13(in_24), .in_14(in_25),
    .in_15(in_26), .in_16(in_27), .out_17(\n16_4编码器_2_out_17 ), .out_18(\n16_4编码器_2_out_18 ),
    .out_19(\n16_4编码器_2_out_19 ), .out_20(\n16_4编码器_2_out_20 ));
  or or_2 (or_2_out, \n16_4编码器_2_out_19 , \n16_4编码器_2_out_18 );
  \数码管  \u_数码管_1  (
    .a(\n16_4编码器_1_out_17 ), .b(\n16_4编码器_1_out_18 ), .x(\数码管_1_x ), .c(\n16_4编码器_1_out_19 ),
    .d(\n16_4编码器_1_out_20 ), .y(\数码管_1_y ), .z(\数码管_1_z ), .u(\数码管_1_u ), .v(\数码管_1_v ), .w(\数码管_1_w ),
    .s(\数码管_1_s ));
  \_4_16译码器  \u_4_16译码器_2  (
    .in_1(\n16_4编码器_2_out_20 ), .in_2(\n16_4编码器_2_out_19 ), .in_3(\n16_4编码器_2_out_18 ),
    .in_4(\n16_4编码器_2_out_17 ), .out_5(out_46), .out_6(out_47), .out_7(out_48), .out_8(out_49),
    .out_9(out_50), .out_10(out_51), .out_11(out_52), .out_12(out_53), .out_13(out_54), .out_14(out_55),
    .out_15(out_56), .out_16(out_57), .out_17(out_58), .out_18(out_59), .out_19(out_60), .out_20(out_61));
  \数码管  \u_数码管_2  (
    .a(\n16_4编码器_2_out_17 ), .b(\n16_4编码器_2_out_18 ), .x(\数码管_2_x ), .c(\n16_4编码器_2_out_19 ),
    .d(\n16_4编码器_2_out_20 ), .y(\数码管_2_y ), .z(\数码管_2_z ), .u(\数码管_2_u ), .v(\数码管_2_v ), .w(\数码管_2_w ),
    .s(\数码管_2_s ));
  and and_2 (and_2_out, or_2_out, \n16_4编码器_2_out_17 );
  _7_Segment_Display u_7_segment_display_1 (.b(and_2_out), .c(and_2_out));  // open: g, f, a, e, d, dp
  \_2_10译码器  \u_2_10译码器_1  (
    .in_1(in_4), .in_2(in_3), .in_3(in_2), .in_4(in_1), .out_5(out_28), .out_6(out_29), .out_7(out_30),
    .out_8(out_31), .out_9(out_33), .out_10(out_35), .out_11(out_37), .out_12(out_39), .out_13(out_41),
    .out_14(out_43));
  _7_Segment_Display u_7_segment_display_2 (.b(and_1_out), .c(and_1_out));  // open: g, f, a, e, d, dp
  _7_Segment_Display u_7_segment_display_3 (
    .g(\数码管_2_s ), .f(\数码管_2_w ), .a(\数码管_2_x ), .b(\数码管_2_y ), .e(\数码管_2_v ), .d(\数码管_2_u ), .c(\数码管_2_z ));  // open: dp
  _7_Segment_Display u_7_segment_display_4 (
    .g(\数码管_1_s ), .f(\数码管_1_w ), .a(\数码管_1_x ), .b(\数码管_1_y ), .e(\数码管_1_v ), .d(\数码管_1_u ), .c(\数码管_1_z ));  // open: dp
endmodule

module \实验4验收  (
  input  in_1,
  input  in_2,
  input  in_3,
  input  in_4,
  input  in_5,
  input  in_6,
  input  in_7,
  input  in_8,
  input  in_9,
  input  in_10,
  input  in_11,
  input  in_12,
  input  in_13,
  input  in_14,
  input  in_15,
  input  in_16,
  input  in_17,
  input  in_18,
  input  in_19,
  input  in_20,
  output out_21,
  output out_22,
  output out_23,
  output out_24,
  output out_25,
  output out_26,
  output out_27,
  output out_28,
  output out_29,
  output out_30,
  output out_31,
  output out_32,
  output out_33,
  output out_34,
  output out_35,
  output out_36
);

  wire and_1_out, \n16_4编码器_1_out_17 , \n16_4编码器_1_out_18 , \n16_4编码器_1_out_19 , \n16_4编码器_1_out_20 ,
       or_1_out, \数码管_1_s , \数码管_1_u , \数码管_1_v , \数码管_1_w , \数码管_1_x , \数码管_1_y , \数码管_1_z , \数码管_2_s ,
       \数码管_2_u , \数码管_2_v , \数码管_2_w , \数码管_2_x , \数码管_2_y , \数码管_2_z , \翻转器_1_out_9 , \翻转器_1_out_10 ,
       \翻转器_1_out_12 , \翻转器_1_out_13 ;

  \数码管  \u_数码管_1  (
    .a(in_1), .b(in_2), .x(\数码管_1_x ), .c(in_3), .d(in_4), .y(\数码管_1_y ), .z(\数码管_1_z ), .u(\数码管_1_u ),
    .v(\数码管_1_v ), .w(\数码管_1_w ), .s(\数码管_1_s ));
  \_16_4编码器  \u_16_4编码器_1  (
    .in_1(in_5), .in_2(in_6), .in_3(in_7), .in_4(in_8), .in_5(in_9), .in_6(in_10), .in_7(in_11),
    .in_8(in_12), .in_9(in_13), .in_10(in_14), .in_11(in_15), .in_12(in_16), .in_13(in_17), .in_14(in_18),
    .in_15(in_19), .in_16(in_20), .out_17(\n16_4编码器_1_out_17 ), .out_18(\n16_4编码器_1_out_18 ),
    .out_19(\n16_4编码器_1_out_19 ), .out_20(\n16_4编码器_1_out_20 ));
  _7_Segment_Display u_7_segment_display_1 (
    .g(\数码管_1_s ), .f(\数码管_1_w ), .a(\数码管_1_x ), .b(\数码管_1_y ), .e(\数码管_1_v ), .d(\数码管_1_u ), .c(\数码管_1_z ));  // open: dp
  \翻转器  \u_翻转器_1  (
    .in_2(\n16_4编码器_1_out_17 ), .in_3(\n16_4编码器_1_out_18 ), .in_5(\n16_4编码器_1_out_19 ),
    .in_6(\n16_4编码器_1_out_20 ), .out_9(\翻转器_1_out_9 ), .out_10(\翻转器_1_out_10 ), .out_12(\翻转器_1_out_12 ),
    .out_13(\翻转器_1_out_13 ));  // open: in_1, in_4, in_7, out_8, out_11, out_14
  \数码管  \u_数码管_2  (
    .a(\n16_4编码器_1_out_17 ), .b(\n16_4编码器_1_out_18 ), .x(\数码管_2_x ), .c(\n16_4编码器_1_out_19 ),
    .d(\n16_4编码器_1_out_20 ), .y(\数码管_2_y ), .z(\数码管_2_z ), .u(\数码管_2_u ), .v(\数码管_2_v ), .w(\数码管_2_w ),
    .s(\数码管_2_s ));
  or or_1 (or_1_out, \n16_4编码器_1_out_19 , \n16_4编码器_1_out_18 );
  and and_1 (and_1_out, or_1_out, \n16_4编码器_1_out_17 );
  _7_Segment_Display u_7_segment_display_2 (.b(and_1_out), .c(and_1_out));  // open: g, f, a, e, d, dp
  \_4_16译码器  \u_4_16译码器_1  (
    .in_1(\翻转器_1_out_9 ), .in_2(\翻转器_1_out_10 ), .in_3(\翻转器_1_out_12 ), .in_4(\翻转器_1_out_13 ),
    .out_5(out_21), .out_6(out_22), .out_7(out_23), .out_8(out_24), .out_9(out_25), .out_10(out_26),
    .out_11(out_27), .out_12(out_28), .out_13(out_29), .out_14(out_30), .out_15(out_31), .out_16(out_32),
    .out_17(out_33), .out_18(out_34), .out_19(out_35), .out_20(out_36));
  _7_Segment_Display u_7_segment_display_3 (
    .g(\数码管_2_s ), .f(\数码管_2_w ), .a(\数码管_2_x ), .b(\数码管_2_y ), .e(\数码管_2_v ), .d(\数码管_2_u ), .c(\数码管_2_z ));  // open: dp
endmodule

module \实验5验收  (
  input  in_1,
  input  in_2,
  input  in_3,
  input  in_4,
  input  in_5,
  input  in_6,
  input  in_7,
  input  in_8,
  input  in_9,
  input  in_10,
  input  in_11,
  input  in_12,
  input  in_13,
  input  in_14,
  input  in_15,
  input  in_16,
  input  in_17,
  input  in_18,
  output out_19,
  output out_20,
  output out_21,
  output out_22,
  output out_23,
  output out_24,
  output out_25
);

  wire \n8_3优先编码器_1_out_9 , \n8_3优先编码器_1_out_10 , \n8_3优先编码器_1_out_11 , \n8_3优先编码器_2_out_9 ,
       \n8_3优先编码器_2_out_10 , \n8_3优先编码器_2_out_11 , pull_resistor_1_node, pull_resistor_2_node,
       \三位控制器_1_out_5 , \三位控制器_1_out_6 , \三位控制器_1_out_7 , \数码管_1_s , \数码管_1_u , \数码管_1_v , \数码管_1_w ,
       \数码管_1_x , \数码管_1_y , \数码管_1_z , \翻转器_1_out_10 , \翻转器_1_out_11 , \翻转器_1_out_12 , \翻转器_2_out_10 ,
       \翻转器_2_out_11 , \翻转器_2_out_12 ;

  \翻转器  \u_翻转器_1  (
    .in_3(\n8_3优先编码器_1_out_9 ), .in_4(\n8_3优先编码器_1_out_10 ), .in_5(\n8_3优先编码器_1_out_11 ),
    .out_10(\翻转器_1_out_10 ), .out_11(\翻转器_1_out_11 ), .out_12(\翻转器_1_out_12 ));  // open: in_1, in_2, in_6, in_7, out_8, out_9, out_13, out_14
  \_8_3优先编码器  \u_8_3优先编码器_1  (
    .in_1(in_2), .in_2(in_3), .in_3(in_4), .in_4(in_5), .in_5(in_6), .in_6(in_7), .in_7(in_8), .in_8(in_9),
    .out_9(\n8_3优先编码器_1_out_9 ), .out_10(\n8_3优先编码器_1_out_10 ), .out_11(\n8_3优先编码器_1_out_11 ));
  \翻转器  \u_翻转器_2  (
    .in_3(\n8_3优先编码器_2_out_9 ), .in_4(\n8_3优先编码器_2_out_10 ), .in_5(\n8_3优先编码器_2_out_11 ),
    .out_10(\翻转器_2_out_10 ), .out_11(\翻转器_2_out_11 ), .out_12(\翻转器_2_out_12 ));  // open: in_1, in_2, in_6, in_7, out_8, out_9, out_13, out_14
  \_8_3优先编码器  \u_8_3优先编码器_2  (
    .in_1(in_11), .in_2(in_12), .in_3(in_13), .in_4(in_14), .in_5(in_15), .in_6(in_16), .in_7(in_17),
    .in_8(in_18), .out_9(\n8_3优先编码器_2_out_9 ), .out_10(\n8_3优先编码器_2_out_10 ), .out_11(\n8_3优先编码器_2_out_11 ));
  \三位控制器  \u_三位控制器_1  (
    .in_2(\翻转器_1_out_10 ), .in_3(\翻转器_1_out_11 ), .in_4(\翻转器_1_out_12 ), .in_1(in_1),
    .out_5(\三位控制器_1_out_5 ), .out_6(\三位控制器_1_out_6 ), .out_7(\三位控制器_1_out_7 ));
  \三位控制器  \u_三位控制器_2  (
    .in_2(\翻转器_2_out_10 ), .in_3(\翻转器_2_out_11 ), .in_4(\翻转器_2_out_12 ), .in_1(in_10),
    .out_5(\三位控制器_1_out_5 ), .out_6(\三位控制器_1_out_6 ), .out_7(\三位控制器_1_out_7 ));
  LED led_1 (.in(\三位控制器_1_out_7 ));
  LED led_2 (.in(\三位控制器_1_out_6 ));
  LED led_3 (.in(\三位控制器_1_out_5 ));
  Pull_Resistor pull_resistor_1 (.node(pull_resistor_1_node));
  \数码管  \u_数码管_1  (
    .a(pull_resistor_1_node), .b(\三位控制器_1_out_7 ), .x(\数码管_1_x ), .c(\三位控制器_1_out_6 ), .d(\三位控制器_1_out_5 ),
    .y(\数码管_1_y ), .z(\数码管_1_z ), .u(\数码管_1_u ), .v(\数码管_1_v ), .w(\数码管_1_w ), .s(\数码管_1_s ));
  Pull_Resistor pull_resistor_2 (.node(pull_resistor_2_node));
  \_3_8译码器  \u_3_8译码器_1  (
    .in_1(\三位控制器_1_out_5 ), .in_2(\三位控制器_1_out_6 ), .in_3(\三位控制器_1_out_7 ), .out_5(out_19),
    .in_4(pull_resistor_2_node), .out_6(out_20), .out_7(out_21), .out_8(out_22), .out_9(out_23),
    .out_10(out_24), .out_11(out_25));  // open: out_12
  _7_Segment_Display u_7_segment_display_1 (
    .g(\数码管_1_s ), .f(\数码管_1_w ), .a(\数码管_1_x ), .b(\数码管_1_y ), .e(\数码管_1_v ), .d(\数码管_1_u ), .c(\数码管_1_z ));  // open: dp
endmodule

module \翻转器  (
  input  in_1,
  input  in_2,
  input  in_3,
  input  in_4,
  input  in_5,
  input  in_6,
  input  in_7,
  output out_8,
  output out_9,
  output out_10,
  output out_11,
  output out_12,
  output out_13,
  output out_14
);


  assign out_8 = in_7;
  assign out_9 = in_6;
  assign out_10 = in_5;
  assign out_11 = in_4;
  assign out_12 = in_3;
  assign out_13 = in_2;
  assign out_14 = in_1;
endmodule

module \数码管打包3  (
  input  in_1,
  input  in_2,
  input  in_3,
  input  in_4,
  input  in_5,
  input  in_6,
  input  in_7,
  output out_8,
  output out_9,
  output out_10,
  output out_11,
  output out_12,
  output out_13,
  output out_14,
  output out_15
);


  assign out_8 = in_7;
  assign out_9 = in_6;
  assign out_10 = in_1;
  assign out_11 = in_2;
  assign out_12 = in_5;
  assign out_13 = in_4;
  assign out_14 = in_3;
  assign out_15 = 1'b0;
endmodule

module \数码管plus  (
  input  in_1,
  input  in_2,
  input  in_3,
  input  in_4,
  input  in_5
);

  wire adder_1_out, \数码管_1_s , \数码管_1_u , \数码管_1_v , \数码管_1_w , \数码管_1_x , \数码管_1_y , \数码管_1_z ;

  Adder #(.width(1)) adder_1 (.a(1'b1), .b(1'b1), .out(adder_1_out));  // open: cin, cout
  \数码管  \u_数码管_1  (
    .a(in_4), .b(in_3), .x(\数码管_1_x ), .c(in_2), .d(in_1), .y(\数码管_1_y ), .z(\数码管_1_z ), .u(\数码管_1_u ),
    .v(\数码管_1_v ), .w(\数码管_1_w ), .s(\数码管_1_s ));
  _7_Segment_Display u_7_segment_display_1 (
    .g(\数码管_1_s ), .f(\数码管_1_w ), .a(\数码管_1_x ), .b(\数码管_1_y ), .e(\数码管_1_v ), .d(\数码管_1_u ), .c(\数码管_1_z ));  // open: dp
endmodule

module \实验五验收plus  (
  input  in_1,
  input  in_2,
  input  in_3,
  input  in_4,
  input  in_5,
  input  in_6,
  input  in_7,
  input  in_8,
  input  in_9,
  input  in_10,
  input  in_11,
  input  in_12,
  input  in_13,
  input  in_14,
  input  in_15,
  input  in_16,
  input  in_17,
  input  in_18,
  input  in_19,
  input  in_20,
  input  in_21,
  input  in_22,
  input  in_23,
  input  in_24,
  input  in_25,
  input  in_26,
  input  in_27,
  input  in_28,
  input  in_29,
  input  in_30,
  input  in_31,
  input  in_32,
  input  in_33,
  input  in_34,
  output out_35,
  output out_36,
  output out_37,
  output out_38,
  output out_39,
  output out_40,
  output out_41,
  output out_42,
  output out_43,
  output out_44,
  output out_45,
  output out_46,
  output out_47,
  output out_48,
  output out_49,
  output out_50
);

  wire and_1_out, \n16_4编码器_1_out_17 , \n16_4编码器_1_out_18 , \n16_4编码器_1_out_19 , \n16_4编码器_1_out_20 ,
       \n16_4编码器_2_out_17 , \n16_4编码器_2_out_18 , \n16_4编码器_2_out_19 , \n16_4编码器_2_out_20 , not_1_out,
       or_1_out, pull_resistor_1_node, \四位控制器_1_out_6 , \四位控制器_1_out_7 , \四位控制器_1_out_8 , \四位控制器_1_out_9 ,
       \数码管_1_s , \数码管_1_u , \数码管_1_v , \数码管_1_w , \数码管_1_x , \数码管_1_y , \数码管_1_z , \翻转器_1_out_9 ,
       \翻转器_1_out_10 , \翻转器_1_out_12 , \翻转器_1_out_13 , \翻转器_2_out_9 , \翻转器_2_out_10 , \翻转器_2_out_12 ,
       \翻转器_2_out_13 ;

  \_16_4编码器  \u_16_4编码器_1  (
    .in_1(in_1), .in_2(in_2), .in_3(in_3), .in_4(in_4), .in_5(in_6), .in_6(in_7), .in_7(in_8), .in_8(in_9),
    .in_9(in_10), .in_10(in_11), .in_11(in_12), .in_12(in_13), .in_13(in_14), .in_14(in_15), .in_15(in_16),
    .in_16(in_17), .out_17(\n16_4编码器_1_out_17 ), .out_18(\n16_4编码器_1_out_18 ), .out_19(\n16_4编码器_1_out_19 ),
    .out_20(\n16_4编码器_1_out_20 ));
  \_16_4编码器  \u_16_4编码器_2  (
    .in_1(in_18), .in_2(in_19), .in_3(in_20), .in_4(in_21), .in_5(in_23), .in_6(in_24), .in_7(in_25),
    .in_8(in_26), .in_9(in_27), .in_10(in_28), .in_11(in_29), .in_12(in_30), .in_13(in_31), .in_14(in_32),
    .in_15(in_33), .in_16(in_34), .out_17(\n16_4编码器_2_out_17 ), .out_18(\n16_4编码器_2_out_18 ),
    .out_19(\n16_4编码器_2_out_19 ), .out_20(\n16_4编码器_2_out_20 ));
  \翻转器  \u_翻转器_1  (
    .in_2(\n16_4编码器_1_out_17 ), .in_3(\n16_4编码器_1_out_18 ), .in_5(\n16_4编码器_1_out_19 ),
    .in_6(\n16_4编码器_1_out_20 ), .out_9(\翻转器_1_out_9 ), .out_10(\翻转器_1_out_10 ), .out_12(\翻转器_1_out_12 ),
    .out_13(\翻转器_1_out_13 ));  // open: in_1, in_4, in_7, out_8, out_11, out_14
  \翻转器  \u_翻转器_2  (
    .in_2(\n16_4编码器_2_out_17 ), .in_3(\n16_4编码器_2_out_18 ), .in_5(\n16_4编码器_2_out_19 ),
    .in_6(\n16_4编码器_2_out_20 ), .out_9(\翻转器_2_out_9 ), .out_10(\翻转器_2_out_10 ), .out_12(\翻转器_2_out_12 ),
    .out_13(\翻转器_2_out_13 ));  // open: in_1, in_4, in_7, out_8, out_11, out_14
  \四位控制器  \u_四位控制器_1  (
    .in_2(\翻转器_1_out_9 ), .in_3(\翻转器_1_out_10 ), .in_4(\翻转器_1_out_12 ), .in_5(\翻转器_1_out_13 ),
    .out_6(\四位控制器_1_out_6 ), .out_7(\四位控制器_1_out_7 ), .out_8(\四位控制器_1_out_8 ), .out_9(\四位控制器_1_out_9 ),
    .in_1(in_5));
  \四位控制器  \u_四位控制器_2  (
    .in_2(\翻转器_2_out_9 ), .in_3(\翻转器_2_out_10 ), .in_4(\翻转器_2_out_12 ), .in_5(\翻转器_2_out_13 ),
    .out_6(\四位控制器_1_out_6 ), .out_7(\四位控制器_1_out_7 ), .out_8(\四位控制器_1_out_8 ), .out_9(\四位控制器_1_out_9 ),
    .in_1(in_22));
  LED led_1 (.in(\四位控制器_1_out_6 ));
  LED led_2 (.in(\四位控制器_1_out_8 ));
  LED led_3 (.in(\四位控制器_1_out_7 ));
  LED led_4 (.in(\四位控制器_1_out_9 ));
  \_4_16译码器  \u_4_16译码器_1  (
    .in_1(\四位控制器_1_out_6 ), .in_2(\四位控制器_1_out_7 ), .in_3(\四位控制器_1_out_8 ), .in_4(\四位控制器_1_out_9 ),
    .out_5(out_35), .out_6(out_36), .out_7(out_37), .out_8(out_38), .out_9(out_39), .out_10(out_40),
    .out_11(out_41), .out_12(out_42), .out_13(out_43), .out_14(out_44), .out_15(out_45), .out_16(out_46),
    .out_17(out_47), .out_18(out_48), .out_19(out_49), .out_20(out_50));
  \数码管  \u_数码管_1  (
    .a(\四位控制器_1_out_9 ), .b(\四位控制器_1_out_8 ), .x(\数码管_1_x ), .c(\四位控制器_1_out_7 ), .d(\四位控制器_1_out_6 ),
    .y(\数码管_1_y ), .z(\数码管_1_z ), .u(\数码管_1_u ), .v(\数码管_1_v ), .w(\数码管_1_w ), .s(\数码管_1_s ));
  or or_1 (or_1_out, \四位控制器_1_out_7 , \四位控制器_1_out_8 );
  and and_1 (and_1_out, or_1_out, \四位控制器_1_out_9 );
  not not_1 (not_1_out, and_1_out);
  _7_Segment_Display u_7_segment_display_1 (
    .f(not_1_out), .a(not_1_out), .b(pull_resistor_1_node), .e(not_1_out), .d(not_1_out),
    .c(pull_resistor_1_node));  // open: g, dp
  Pull_Resistor #(.pull(1)) pull_resistor_1 (.node(pull_resistor_1_node));
  _7_Segment_Display u_7_segment_display_2 (
    .g(\数码管_1_s ), .f(\数码管_1_w ), .a(\数码管_1_x ), .b(\数码管_1_y ), .e(\数码管_1_v ), .d(\数码管_1_u ), .c(\数码管_1_z ));  // open: dp
endmodule

module \四位控制器  (
  input  in_1,
  input  in_2,
  input  in_3,
  input  in_4,
  input  in_5,
  output out_6,
  output out_7,
  output out_8,
  output out_9
);

  assign out_6 = in_1 ? in_2 : 1'bz;  // Controlled_Buffer controlled_buffer_1
  assign out_7 = in_1 ? in_3 : 1'bz;  // Controlled_Buffer controlled_buffer_2
  assign out_8 = in_1 ? in_4 : 1'bz;  // Controlled_Buffer controlled_buffer_3
  assign out_9 = in_1 ? in_5 : 1'bz;  // Controlled_Buffer controlled_buffer_4
endmodule

module \_3位D触发器  (
  input  in_1,
  input  in_2,
  input  in_3,
  input  in_4,
  input  in_5,
  input  in_6,
  output out_7,
  output out_8,
  output out_9,
  output out_10,
  output out_11
);

  D_Flip_Flop d_ff_1 (.clk(in_6), .D(in_1), .Q(out_7));  // open: Qn, preset, en, reset
  D_Flip_Flop d_ff_2 (.clk(in_6), .D(in_2), .Q(out_8));  // open: Qn, preset, en, reset
  D_Flip_Flop d_ff_3 (.clk(in_6), .D(in_3), .Q(out_9));  // open: Qn, preset, en, reset
  D_Flip_Flop d_ff_4 (.clk(in_6), .D(in_4), .Q(out_10));  // open: Qn, preset, en, reset
  D_Flip_Flop d_ff_5 (.clk(in_6), .D(in_5), .Q(out_11));  // open: Qn, preset, en, reset
endmodule

module \实验5  (
  input  in_1,
  input  in_2,
  input  in_3,
  input  in_4,
  input  in_5,
  input  in_6,
  input  in_7,
  input  in_8,
  input  in_9,
  input  in_10,
  input  in_11,
  input  in_12,
  input  in_13,
  input  in_14,
  input  in_15,
  input  in_16,
  input  in_17,
  input  in_18,
  input  in_19,
  input  in_20,
  input  in_21,
  input  in_22,
  input  in_23,
  input  in_24,
  input  in_25,
  input  in_26,
  input  in_27,
  input  in_28,
  input  in_29,
  input  in_30,
  input  in_31,
  input  in_32,
  input  in_33,
  input  in_34,
  input  in_35,
  input  in_36,
  input  in_37,
  output out_38,
  output out_39,
  output out_40,
  output out_41,
  output out_42,
  output out_43,
  output out_44,
  output out_45,
  output out_46,
  output out_47,
  output out_48,
  output out_49,
  output out_50,
  output out_51,
  output out_52,
  output out_53
);

  wire \n3位d触发器_1_out_7 , \n3位d触发器_1_out_8 , \n3位d触发器_1_out_9 , \n3位d触发器_1_out_10 , \n3位d触发器_2_out_7 ,
       \n3位d触发器_2_out_8 , \n3位d触发器_2_out_9 , \n3位d触发器_2_out_10 , \n16_4编码器_1_out_17 , \n16_4编码器_1_out_18 ,
       \n16_4编码器_1_out_19 , \n16_4编码器_1_out_20 , \n16_4编码器_2_out_17 , \n16_4编码器_2_out_18 ,
       \n16_4编码器_2_out_19 , \n16_4编码器_2_out_20 , pull_resistor_1_node, pull_resistor_2_node, \四位加法器_1_out_9 ,
       \四位加法器_1_out_10 , \四位加法器_1_out_11 , \四位加法器_1_out_12 , \四位加法器_1_out_13 , \四位控制器_1_out_6 ,
       \四位控制器_1_out_7 , \四位控制器_1_out_8 , \四位控制器_1_out_9 , \数码管_1_s , \数码管_1_u , \数码管_1_v , \数码管_1_w ,
       \数码管_1_x , \数码管_1_y , \数码管_1_z , \数码管_2_s , \数码管_2_u , \数码管_2_v , \数码管_2_w , \数码管_2_x , \数码管_2_y ,
       \数码管_2_z , \数码管高位_1_out_6 , \数码管高位_1_out_7 , \数码管高位_1_out_8 , \数码管高位_1_out_9 , \数码管高位_1_out_10 ,
       \数码管高位_1_out_11 , \数码管高位_1_out_12 , \翻转器_1_out_9 , \翻转器_1_out_10 , \翻转器_1_out_12 , \翻转器_1_out_13 ,
       \翻转器_2_out_9 , \翻转器_2_out_10 , \翻转器_2_out_12 , \翻转器_2_out_13 ;

  \_16_4编码器  \u_16_4编码器_1  (
    .in_1(in_1), .in_2(in_2), .in_3(in_3), .in_4(in_4), .in_5(in_6), .in_6(in_7), .in_7(in_8), .in_8(in_9),
    .in_9(in_10), .in_10(in_11), .in_11(in_12), .in_12(in_14), .in_13(in_15), .in_14(in_16), .in_15(in_17),
    .in_16(in_18), .out_17(\n16_4编码器_1_out_17 ), .out_18(\n16_4编码器_1_out_18 ), .out_19(\n16_4编码器_1_out_19 ),
    .out_20(\n16_4编码器_1_out_20 ));
  \_16_4编码器  \u_16_4编码器_2  (
    .in_1(in_19), .in_2(in_20), .in_3(in_22), .in_4(in_23), .in_5(in_25), .in_6(in_26), .in_7(in_27),
    .in_8(in_28), .in_9(in_30), .in_10(in_31), .in_11(in_32), .in_12(in_33), .in_13(in_34), .in_14(in_35),
    .in_15(in_36), .in_16(in_37), .out_17(\n16_4编码器_2_out_17 ), .out_18(\n16_4编码器_2_out_18 ),
    .out_19(\n16_4编码器_2_out_19 ), .out_20(\n16_4编码器_2_out_20 ));
  \翻转器  \u_翻转器_1  (
    .in_2(\n16_4编码器_1_out_17 ), .in_3(\n16_4编码器_1_out_18 ), .in_5(\n16_4编码器_1_out_19 ),
    .in_6(\n16_4编码器_1_out_20 ), .out_9(\翻转器_1_out_9 ), .out_10(\翻转器_1_out_10 ), .out_12(\翻转器_1_out_12 ),
    .out_13(\翻转器_1_out_13 ));  // open: in_1, in_4, in_7, out_8, out_11, out_14
  \四位控制器  \u_四位控制器_1  (
    .in_2(\翻转器_1_out_9 ), .in_3(\翻转器_1_out_10 ), .in_4(\翻转器_1_out_12 ), .in_5(\翻转器_1_out_13 ),
    .out_6(\四位控制器_1_out_6 ), .out_7(\四位控制器_1_out_7 ), .out_8(\四位控制器_1_out_8 ), .out_9(\四位控制器_1_out_9 ),
    .in_1(in_5));
  \翻转器  \u_翻转器_2  (
    .in_2(\n16_4编码器_2_out_17 ), .in_3(\n16_4编码器_2_out_18 ), .in_5(\n16_4编码器_2_out_19 ),
    .in_6(\n16_4编码器_2_out_20 ), .out_9(\翻转器_2_out_9 ), .out_10(\翻转器_2_out_10 ), .out_12(\翻转器_2_out_12 ),
    .out_13(\翻转器_2_out_13 ));  // open: in_1, in_4, in_7, out_8, out_11, out_14
  \四位控制器  \u_四位控制器_2  (
    .in_2(\翻转器_2_out_9 ), .in_3(\翻转器_2_out_10 ), .in_4(\翻转器_2_out_12 ), .in_5(\翻转器_2_out_13 ),
    .out_6(\四位控制器_1_out_6 ), .out_7(\四位控制器_1_out_7 ), .out_8(\四位控制器_1_out_8 ), .out_9(\四位控制器_1_out_9 ),
    .in_1(in_24));
  LED led_1 (.in(\四位控制器_1_out_6 ));
  LED led_2 (.in(\四位控制器_1_out_8 ));
  LED led_3 (.in(pull_resistor_1_node));
  LED led_4 (.in(\四位控制器_1_out_7 ));
  LED led_5 (.in(\四位控制器_1_out_9 ));
  Pull_Resistor pull_resistor_1 (.node(pull_resistor_1_node));
  \_4_16译码器  \u_4_16译码器_1  (
    .in_1(\四位控制器_1_out_6 ), .in_2(\四位控制器_1_out_7 ), .in_3(\四位控制器_1_out_8 ), .in_4(\四位控制器_1_out_9 ),
    .out_5(out_38), .out_6(out_39), .out_7(out_40), .out_8(out_41), .out_9(out_42), .out_10(out_43),
    .out_11(out_44), .out_12(out_45), .out_13(out_46), .out_14(out_47), .out_15(out_48), .out_16(out_49),
    .out_17(out_50), .out_18(out_51), .out_19(out_52), .out_20(out_53));
  \_3位D触发器  \u_3位d触发器_1  (
    .in_1(\四位控制器_1_out_6 ), .in_2(\四位控制器_1_out_7 ), .in_3(\四位控制器_1_out_8 ), .in_4(\四位控制器_1_out_9 ),
    .out_7(\n3位d触发器_1_out_7 ), .out_8(\n3位d触发器_1_out_8 ), .out_9(\n3位d触发器_1_out_9 ),
    .out_10(\n3位d触发器_1_out_10 ), .in_6(in_21));  // open: in_5, out_11
  \_3位D触发器  \u_3位d触发器_2  (
    .in_1(\四位控制器_1_out_6 ), .in_2(\四位控制器_1_out_7 ), .in_3(\四位控制器_1_out_8 ), .in_4(\四位控制器_1_out_9 ),
    .out_7(\n3位d触发器_2_out_7 ), .out_8(\n3位d触发器_2_out_8 ), .out_9(\n3位d触发器_2_out_9 ),
    .out_10(\n3位d触发器_2_out_10 ), .in_6(in_29));  // open: in_5, out_11
  \数码管高位  \u_数码管高位_1  (
    .in_1(pull_resistor_1_node), .in_2(\四位控制器_1_out_9 ), .in_3(\四位控制器_1_out_8 ), .in_4(\四位控制器_1_out_7 ),
    .in_5(\四位控制器_1_out_6 ), .out_6(\数码管高位_1_out_6 ), .out_7(\数码管高位_1_out_7 ), .out_8(\数码管高位_1_out_8 ),
    .out_9(\数码管高位_1_out_9 ), .out_10(\数码管高位_1_out_10 ), .out_11(\数码管高位_1_out_11 ), .out_12(\数码管高位_1_out_12 ));
  \四位加法器  \u_四位加法器_1  (
    .in_1(\n3位d触发器_1_out_7 ), .in_2(\n3位d触发器_2_out_7 ), .in_3(\n3位d触发器_1_out_8 ), .in_4(\n3位d触发器_2_out_8 ),
    .in_5(\n3位d触发器_1_out_9 ), .in_6(\n3位d触发器_2_out_9 ), .in_7(\n3位d触发器_1_out_10 ), .in_8(\n3位d触发器_2_out_10 ),
    .out_9(\四位加法器_1_out_9 ), .out_10(\四位加法器_1_out_10 ), .out_11(\四位加法器_1_out_11 ), .out_12(\四位加法器_1_out_12 ),
    .out_13(\四位加法器_1_out_13 ));
  \数码管  \u_数码管_1  (
    .a(\数码管高位_1_out_9 ), .b(\数码管高位_1_out_10 ), .x(\数码管_1_x ), .c(\数码管高位_1_out_11 ), .d(\数码管高位_1_out_12 ),
    .y(\数码管_1_y ), .z(\数码管_1_z ), .u(\数码管_1_u ), .v(\数码管_1_v ), .w(\数码管_1_w ), .s(\数码管_1_s ));
  Pull_Resistor pull_resistor_2 (.node(pull_resistor_2_node));
  \数码管  \u_数码管_2  (
    .a(pull_resistor_2_node), .b(\数码管高位_1_out_6 ), .x(\数码管_2_x ), .c(\数码管高位_1_out_7 ), .d(\数码管高位_1_out_8 ),
    .y(\数码管_2_y ), .z(\数码管_2_z ), .u(\数码管_2_u ), .v(\数码管_2_v ), .w(\数码管_2_w ), .s(\数码管_2_s ));
  \四位控制器  \u_四位控制器_3  (
    .in_2(\四位加法器_1_out_12 ), .in_3(\四位加法器_1_out_11 ), .in_4(\四位加法器_1_out_10 ), .in_5(\四位加法器_1_out_9 ),
    .out_6(\四位控制器_1_out_9 ), .out_7(\四位控制器_1_out_8 ), .out_8(\四位控制器_1_out_7 ), .out_9(\四位控制器_1_out_6 ),
    .in_1(in_13));
  \四位控制器  \u_四位控制器_4  (
    .in_2(\四位加法器_1_out_13 ), .out_6(pull_resistor_1_node), .in_1(in_13));  // open: in_3, in_4, in_5, out_7, out_8, out_9
  _7_Segment_Display u_7_segment_display_1 (
    .g(\数码管_1_s ), .f(\数码管_1_w ), .a(\数码管_1_x ), .b(\数码管_1_y ), .e(\数码管_1_v ), .d(\数码管_1_u ), .c(\数码管_1_z ));  // open: dp
  _7_Segment_Display u_7_segment_display_2 (
    .g(\数码管_2_s ), .f(\数码管_2_w ), .a(\数码管_2_x ), .b(\数码管_2_y ), .e(\数码管_2_v ), .d(\数码管_2_u ), .c(\数码管_2_z ));  // open: dp
endmodule

module \数码管高位  (
  input  in_1,
  input  in_2,
  input  in_3,
  input  in_4,
  input  in_5,
  output out_6,
  output out_7,
  output out_8,
  output out_9,
  output out_10,
  output out_11,
  output out_12
);

  wire and_1_out, and_2_out, and_3_out, and_4_out, \n5位数码管_1_out_6 , \n5位数码管_1_out_7 , \n5位数码管_1_out_8 ,
       \n5位数码管_1_out_9 , \n5位数码管_1_out_10 , \n5位数码管_1_out_11 , \n5位数码管_2_out_6 , \n5位数码管_2_out_7 ,
       \n5位数码管_2_out_8 , \n5位数码管_2_out_9 , \n5位数码管_2_out_10 , \n5位数码管_2_out_11 , \n5位数码管_3_out_6 ,
       \n5位数码管_3_out_8 , \n5位数码管_3_out_9 , \n5位数码管_3_out_10 , \n5位数码管_3_out_11 , not_1_out, not_2_out,
       not_3_out, not_4_out, not_5_out, not_6_out;

  \四位控制器  \u_四位控制器_1  (
    .in_2(in_2), .in_3(in_3), .in_4(in_4), .in_5(in_5), .out_6(out_9), .out_7(out_10), .out_8(out_11),
    .out_9(out_12), .in_1(and_1_out));
  \_5位数码管  \u_5位数码管_1  (
    .in_1(in_1), .in_2(in_2), .in_3(in_3), .in_4(in_4), .in_5(in_5), .out_7(\n5位数码管_1_out_7 ),
    .out_8(\n5位数码管_1_out_8 ), .out_9(\n5位数码管_1_out_9 ), .out_10(\n5位数码管_1_out_10 ),
    .out_11(\n5位数码管_1_out_11 ), .out_6(\n5位数码管_1_out_6 ));
  \_5位数码管  \u_5位数码管_2  (
    .in_1(\n5位数码管_1_out_7 ), .in_2(\n5位数码管_1_out_8 ), .in_3(\n5位数码管_1_out_9 ), .in_4(\n5位数码管_1_out_10 ),
    .in_5(\n5位数码管_1_out_11 ), .out_7(\n5位数码管_2_out_7 ), .out_8(\n5位数码管_2_out_8 ), .out_9(\n5位数码管_2_out_9 ),
    .out_10(\n5位数码管_2_out_10 ), .out_11(\n5位数码管_2_out_11 ), .out_6(\n5位数码管_2_out_6 ));
  \四位控制器  \u_四位控制器_2  (
    .in_2(\n5位数码管_1_out_8 ), .in_3(\n5位数码管_1_out_9 ), .in_4(\n5位数码管_1_out_10 ), .in_5(\n5位数码管_1_out_11 ),
    .out_6(out_9), .out_7(out_10), .out_8(out_11), .out_9(out_12), .in_1(and_2_out));
  \_5位数码管  \u_5位数码管_3  (
    .in_1(\n5位数码管_2_out_7 ), .in_2(\n5位数码管_2_out_8 ), .in_3(\n5位数码管_2_out_9 ), .in_4(\n5位数码管_2_out_10 ),
    .in_5(\n5位数码管_2_out_11 ), .out_8(\n5位数码管_3_out_8 ), .out_9(\n5位数码管_3_out_9 ), .out_10(\n5位数码管_3_out_10 ),
    .out_11(\n5位数码管_3_out_11 ), .out_6(\n5位数码管_3_out_6 ));  // open: out_7
  \四位控制器  \u_四位控制器_3  (
    .in_2(\n5位数码管_2_out_8 ), .in_3(\n5位数码管_2_out_9 ), .in_4(\n5位数码管_2_out_10 ), .in_5(\n5位数码管_2_out_11 ),
    .out_6(out_9), .out_7(out_10), .out_8(out_11), .out_9(out_12), .in_1(and_3_out));
  not not_1 (not_1_out, \n5位数码管_1_out_6 );
  and and_1 (and_1_out, not_1_out, not_2_out, not_3_out);
  not not_2 (not_2_out, \n5位数码管_2_out_6 );
  not not_3 (not_3_out, \n5位数码管_3_out_6 );
  and and_2 (and_2_out, \n5位数码管_1_out_6 , not_4_out, not_5_out);
  not not_4 (not_4_out, \n5位数码管_2_out_6 );
  not not_5 (not_5_out, \n5位数码管_3_out_6 );
  not not_6 (not_6_out, \n5位数码管_3_out_6 );
  and and_3 (and_3_out, not_6_out, \n5位数码管_2_out_6 , \n5位数码管_1_out_6 );
  and and_4 (and_4_out, \n5位数码管_3_out_6 , \n5位数码管_2_out_6 , \n5位数码管_1_out_6 );
  \四位控制器  \u_四位控制器_4  (
    .in_2(\n5位数码管_3_out_8 ), .in_3(\n5位数码管_3_out_9 ), .in_4(\n5位数码管_3_out_10 ), .in_5(\n5位数码管_3_out_11 ),
    .out_6(out_9), .out_7(out_10), .out_8(out_11), .out_9(out_12), .in_1(and_4_out));
  \_8_3优先编码器  \u_8_3优先编码器_1  (
    .in_1(and_1_out), .in_2(and_2_out), .in_3(and_3_out), .in_4(and_4_out), .out_9(out_6), .out_10(out_7),
    .out_11(out_8));  // open: in_5, in_6, in_7, in_8
endmodule

module \_5位数码管  (
  input  in_1,
  input  in_2,
  input  in_3,
  input  in_4,
  input  in_5,
  output out_6,
  output out_7,
  output out_8,
  output out_9,
  output out_10,
  output out_11
);

  wire and_1_out, not_1_out, or_1_out, pull_resistor_1_node, pull_resistor_2_node, \全减器_1_out_12 ,
       \全减器_1_out_13 , \全减器_1_out_14 , \全减器_1_out_15 , \全减器_1_out_16 , \翻转器_1_out_9 , \翻转器_1_out_10 ,
       \翻转器_1_out_11 , \翻转器_1_out_12 , \翻转器_1_out_13 ;

  or or_1 (or_1_out, in_3, in_4);
  \翻转器  \u_翻转器_1  (
    .in_2(in_1), .in_3(in_2), .in_4(in_3), .in_5(in_4), .in_6(in_5), .out_9(\翻转器_1_out_9 ),
    .out_10(\翻转器_1_out_10 ), .out_11(\翻转器_1_out_11 ), .out_12(\翻转器_1_out_12 ), .out_13(\翻转器_1_out_13 ));  // open: in_1, in_7, out_8, out_14
  and and_1 (and_1_out, or_1_out, in_2);
  Pull_Resistor pull_resistor_1 (.node(pull_resistor_1_node));
  Pull_Resistor #(.pull(1)) pull_resistor_2 (.node(pull_resistor_2_node));
  or or_2 (out_6, and_1_out, in_1);
  \全减器  \u_全减器_1  (
    .in_1(pull_resistor_1_node), .in_2(\翻转器_1_out_9 ), .in_3(pull_resistor_1_node), .in_4(\翻转器_1_out_10 ),
    .in_5(pull_resistor_2_node), .in_6(\翻转器_1_out_11 ), .in_7(pull_resistor_1_node), .in_8(\翻转器_1_out_12 ),
    .in_9(pull_resistor_2_node), .in_10(\翻转器_1_out_13 ), .in_11(pull_resistor_1_node),
    .out_12(\全减器_1_out_12 ), .out_13(\全减器_1_out_13 ), .out_14(\全减器_1_out_14 ), .out_15(\全减器_1_out_15 ),
    .out_16(\全减器_1_out_16 ));  // open: out_17
  \四位控制器  \u_四位控制器_1  (
    .in_2(\全减器_1_out_16 ), .out_6(out_7), .in_1(out_6));  // open: in_3, in_4, in_5, out_7, out_8, out_9
  \四位控制器  \u_四位控制器_2  (
    .in_2(\全减器_1_out_12 ), .in_3(\全减器_1_out_13 ), .in_4(\全减器_1_out_14 ), .in_5(\全减器_1_out_15 ),
    .out_6(out_11), .out_7(out_10), .out_8(out_9), .out_9(out_8), .in_1(out_6));
  not not_1 (not_1_out, out_6);
  \四位控制器  \u_四位控制器_3  (
    .in_2(pull_resistor_1_node), .in_3(pull_resistor_1_node), .in_4(pull_resistor_1_node),
    .in_5(pull_resistor_1_node), .out_6(out_8), .out_7(out_9), .out_8(out_10), .out_9(out_7), .in_1(not_1_out));
  \四位控制器  \u_四位控制器_4  (
    .in_2(pull_resistor_1_node), .in_3(pull_resistor_1_node), .in_4(pull_resistor_1_node),
    .in_5(pull_resistor_1_node), .out_6(out_11), .in_1(not_1_out));  // open: out_7, out_8, out_9
endmodule

module \实验6验收  (
  input  in_1,
  input  in_2,
  input  in_3,
  input  in_4,
  input  in_5,
  input  in_6,
  input  in_7,
  input  in_8,
  input  in_9,
  input  in_10,
  input  in_11,
  input  in_12,
  input  in_13,
  input  in_14,
  input  in_15,
  input  in_16,
  input  in_17,
  input  in_18,
  input  in_19,
  input  in_20,
  input  in_21,
  input  in_22,
  input  in_23,
  input  in_24,
  input  in_25,
  input  in_26,
  input  in_27,
  input  in_28,
  input  in_29,
  input  in_30,
  input  in_31,
  input  in_32,
  input  in_33,
  input  in_34,
  input  in_35,
  output out_36,
  output out_37,
  output out_38,
  output out_39,
  output out_40,
  output out_41,
  output out_42,
  output out_43,
  output out_44,
  output out_45,
  output out_46,
  output out_47,
  output out_48,
  output out_49,
  output out_50,
  output out_51
);

  wire button_1_out, button_2_out, \n3位d触发器_1_out_7 , \n3位d触发器_1_out_8 , \n3位d触发器_1_out_9 ,
       \n3位d触发器_1_out_10 , \n3位d触发器_2_out_7 , \n3位d触发器_2_out_8 , \n3位d触发器_2_out_9 , \n3位d触发器_2_out_10 ,
       \n16_4编码器_1_out_17 , \n16_4编码器_1_out_18 , \n16_4编码器_1_out_19 , \n16_4编码器_1_out_20 ,
       \n16_4编码器_2_out_17 , \n16_4编码器_2_out_18 , \n16_4编码器_2_out_19 , \n16_4编码器_2_out_20 ,
       pull_resistor_1_node, pull_resistor_2_node, \四位加法器_1_out_9 , \四位加法器_1_out_10 , \四位加法器_1_out_11 ,
       \四位加法器_1_out_12 , \四位加法器_1_out_13 , \四位控制器_1_out_6 , \四位控制器_1_out_7 , \四位控制器_1_out_8 ,
       \四位控制器_1_out_9 , \数码管_1_s , \数码管_1_u , \数码管_1_v , \数码管_1_w , \数码管_1_x , \数码管_1_y , \数码管_1_z ,
       \数码管_2_s , \数码管_2_u , \数码管_2_v , \数码管_2_w , \数码管_2_x , \数码管_2_y , \数码管_2_z , \数码管高位_1_out_6 ,
       \数码管高位_1_out_7 , \数码管高位_1_out_8 , \数码管高位_1_out_9 , \数码管高位_1_out_10 , \数码管高位_1_out_11 ,
       \数码管高位_1_out_12 , \翻转器_1_out_9 , \翻转器_1_out_10 , \翻转器_1_out_12 , \翻转器_1_out_13 , \翻转器_2_out_9 ,
       \翻转器_2_out_10 , \翻转器_2_out_12 , \翻转器_2_out_13 ;

  \_16_4编码器  \u_16_4编码器_1  (
    .in_1(in_1), .in_2(in_2), .in_3(in_3), .in_4(in_4), .in_5(in_6), .in_6(in_7), .in_7(in_8), .in_8(in_9),
    .in_9(in_10), .in_10(in_11), .in_11(in_12), .in_12(in_14), .in_13(in_15), .in_14(in_16), .in_15(in_17),
    .in_16(in_18), .out_17(\n16_4编码器_1_out_17 ), .out_18(\n16_4编码器_1_out_18 ), .out_19(\n16_4编码器_1_out_19 ),
    .out_20(\n16_4编码器_1_out_20 ));
  \_16_4编码器  \u_16_4编码器_2  (
    .in_1(in_19), .in_2(in_20), .in_3(in_21), .in_4(in_22), .in_5(in_24), .in_6(in_25), .in_7(in_26),
    .in_8(in_27), .in_9(in_28), .in_10(in_29), .in_11(in_30), .in_12(in_31), .in_13(in_32), .in_14(in_33),
    .in_15(in_34), .in_16(in_35), .out_17(\n16_4编码器_2_out_17 ), .out_18(\n16_4编码器_2_out_18 ),
    .out_19(\n16_4编码器_2_out_19 ), .out_20(\n16_4编码器_2_out_20 ));
  \翻转器  \u_翻转器_1  (
    .in_2(\n16_4编码器_1_out_17 ), .in_3(\n16_4编码器_1_out_18 ), .in_5(\n16_4编码器_1_out_19 ),
    .in_6(\n16_4编码器_1_out_20 ), .out_9(\翻转器_1_out_9 ), .out_10(\翻转器_1_out_10 ), .out_12(\翻转器_1_out_12 ),
    .out_13(\翻转器_1_out_13 ));  // open: in_1, in_4, in_7, out_8, out_11, out_14
  \四位控制器  \u_四位控制器_1  (
    .in_2(\翻转器_1_out_9 ), .in_3(\翻转器_1_out_10 ), .in_4(\翻转器_1_out_12 ), .in_5(\翻转器_1_out_13 ),
    .out_6(\四位控制器_1_out_6 ), .out_7(\四位控制器_1_out_7 ), .out_8(\四位控制器_1_out_8 ), .out_9(\四位控制器_1_out_9 ),
    .in_1(in_5));
  \翻转器  \u_翻转器_2  (
    .in_2(\n16_4编码器_2_out_17 ), .in_3(\n16_4编码器_2_out_18 ), .in_5(\n16_4编码器_2_out_19 ),
    .in_6(\n16_4编码器_2_out_20 ), .out_9(\翻转器_2_out_9 ), .out_10(\翻转器_2_out_10 ), .out_12(\翻转器_2_out_12 ),
    .out_13(\翻转器_2_out_13 ));  // open: in_1, in_4, in_7, out_8, out_11, out_14
  \四位控制器  \u_四位控制器_2  (
    .in_2(\翻转器_2_out_9 ), .in_3(\翻转器_2_out_10 ), .in_4(\翻转器_2_out_12 ), .in_5(\翻转器_2_out_13 ),
    .out_6(\四位控制器_1_out_6 ), .out_7(\四位控制器_1_out_7 ), .out_8(\四位控制器_1_out_8 ), .out_9(\四位控制器_1_out_9 ),
    .in_1(in_23));
  LED led_1 (.in(pull_resistor_1_node));
  LED led_2 (.in(\四位控制器_1_out_6 ));
  LED led_3 (.in(\四位控制器_1_out_8 ));
  LED led_4 (.in(\四位控制器_1_out_7 ));
  LED led_5 (.in(\四位控制器_1_out_9 ));
  Pull_Resistor pull_resistor_1 (.node(pull_resistor_1_node));
  \_4_16译码器  \u_4_16译码器_1  (
    .in_1(\四位控制器_1_out_6 ), .in_2(\四位控制器_1_out_7 ), .in_3(\四位控制器_1_out_8 ), .in_4(\四位控制器_1_out_9 ),
    .out_5(out_36), .out_6(out_37), .out_7(out_38), .out_8(out_39), .out_9(out_40), .out_10(out_41),
    .out_11(out_42), .out_12(out_43), .out_13(out_44), .out_14(out_45), .out_15(out_46), .out_16(out_47),
    .out_17(out_48), .out_18(out_49), .out_19(out_50), .out_20(out_51));
  Button button_1 (.out(button_1_out));
  Button button_2 (.out(button_2_out));
  \_3位D触发器  \u_3位d触发器_1  (
    .in_1(\四位控制器_1_out_6 ), .in_2(\四位控制器_1_out_7 ), .in_3(\四位控制器_1_out_8 ), .in_4(\四位控制器_1_out_9 ),
    .out_7(\n3位d触发器_1_out_7 ), .out_8(\n3位d触发器_1_out_8 ), .out_9(\n3位d触发器_1_out_9 ),
    .out_10(\n3位d触发器_1_out_10 ), .in_6(button_1_out));  // open: in_5, out_11
  \_3位D触发器  \u_3位d触发器_2  (
    .in_1(\四位控制器_1_out_6 ), .in_2(\四位控制器_1_out_7 ), .in_3(\四位控制器_1_out_8 ), .in_4(\四位控制器_1_out_9 ),
    .out_7(\n3位d触发器_2_out_7 ), .out_8(\n3位d触发器_2_out_8 ), .out_9(\n3位d触发器_2_out_9 ),
    .out_10(\n3位d触发器_2_out_10 ), .in_6(button_2_out));  // open: in_5, out_11
  \数码管高位  \u_数码管高位_1  (
    .in_1(pull_resistor_1_node), .in_2(\四位控制器_1_out_9 ), .in_3(\四位控制器_1_out_8 ), .in_4(\四位控制器_1_out_7 ),
    .in_5(\四位控制器_1_out_6 ), .out_6(\数码管高位_1_out_6 ), .out_7(\数码管高位_1_out_7 ), .out_8(\数码管高位_1_out_8 ),
    .out_9(\数码管高位_1_out_9 ), .out_10(\数码管高位_1_out_10 ), .out_11(\数码管高位_1_out_11 ), .out_12(\数码管高位_1_out_12 ));
  \四位加法器  \u_四位加法器_1  (
    .in_1(\n3位d触发器_1_out_7 ), .in_2(\n3位d触发器_2_out_7 ), .in_3(\n3位d触发器_1_out_8 ), .in_4(\n3位d触发器_2_out_8 ),
    .in_5(\n3位d触发器_1_out_9 ), .in_6(\n3位d触发器_2_out_9 ), .in_7(\n3位d触发器_1_out_10 ), .in_8(\n3位d触发器_2_out_10 ),
    .out_9(\四位加法器_1_out_9 ), .out_10(\四位加法器_1_out_10 ), .out_11(\四位加法器_1_out_11 ), .out_12(\四位加法器_1_out_12 ),
    .out_13(\四位加法器_1_out_13 ));
  Pull_Resistor pull_resistor_2 (.node(pull_resistor_2_node));
  \四位控制器  \u_四位控制器_3  (
    .in_2(\四位加法器_1_out_12 ), .in_3(\四位加法器_1_out_11 ), .in_4(\四位加法器_1_out_10 ), .in_5(\四位加法器_1_out_9 ),
    .out_6(\四位控制器_1_out_9 ), .out_7(\四位控制器_1_out_8 ), .out_8(\四位控制器_1_out_7 ), .out_9(\四位控制器_1_out_6 ),
    .in_1(in_13));
  \四位控制器  \u_四位控制器_4  (
    .in_2(\四位加法器_1_out_13 ), .out_6(pull_resistor_1_node), .in_1(in_13));  // open: in_3, in_4, in_5, out_7, out_8, out_9
  \数码管  \u_数码管_1  (
    .a(\数码管高位_1_out_9 ), .b(\数码管高位_1_out_10 ), .x(\数码管_1_x ), .c(\数码管高位_1_out_11 ), .d(\数码管高位_1_out_12 ),
    .y(\数码管_1_y ), .z(\数码管_1_z ), .u(\数码管_1_u ), .v(\数码管_1_v ), .w(\数码管_1_w ), .s(\数码管_1_s ));
  \数码管  \u_数码管_2  (
    .a(pull_resistor_2_node), .b(\数码管高位_1_out_6 ), .x(\数码管_2_x ), .c(\数码管高位_1_out_7 ), .d(\数码管高位_1_out_8 ),
    .y(\数码管_2_y ), .z(\数码管_2_z ), .u(\数码管_2_u ), .v(\数码管_2_v ), .w(\数码管_2_w ), .s(\数码管_2_s ));
  _7_Segment_Display u_7_segment_display_1 (
    .g(\数码管_2_s ), .f(\数码管_2_w ), .a(\数码管_2_x ), .b(\数码管_2_y ), .e(\数码管_2_v ), .d(\数码管_2_u ), .c(\数码管_2_z ));  // open: dp
  _7_Segment_Display u_7_segment_display_2 (
    .g(\数码管_1_s ), .f(\数码管_1_w ), .a(\数码管_1_x ), .b(\数码管_1_y ), .e(\数码管_1_v ), .d(\数码管_1_u ), .c(\数码管_1_z ));  // open: dp
endmodule

module \计数器  (
  input  in_1,
  output out_2,
  output out_3,
  output out_4,
  output out_5
);

  wire clock_1_out;

  Clock clock_1 (.out(clock_1_out));
  T_Flip_Flop t_ff_1 (.clk(out_3), .T(in_1), .Q(out_2));  // open: Qn, preset, reset, en
  T_Flip_Flop t_ff_2 (.clk(out_4), .T(in_1), .Q(out_3));  // open: Qn, preset, reset, en
  T_Flip_Flop t_ff_3 (.clk(out_5), .T(in_1), .Q(out_4));  // open: Qn, preset, reset, en
  T_Flip_Flop t_ff_4 (.clk(clock_1_out), .T(in_1), .Q(out_5));  // open: Qn, preset, reset, en
endmodule

module \实验7验收  (
  input  in_1
);

  wire \n4_16译码器_1_out_5 , \n4_16译码器_1_out_6 , \n4_16译码器_1_out_7 , \n4_16译码器_1_out_8 , \n4_16译码器_1_out_9 ,
       \n4_16译码器_1_out_10 , \n4_16译码器_1_out_11 , \n4_16译码器_1_out_12 , \n4_16译码器_1_out_13 ,
       \n4_16译码器_1_out_14 , \n4_16译码器_1_out_15 , \n4_16译码器_1_out_16 , \n4_16译码器_1_out_17 ,
       \n4_16译码器_1_out_18 , \n4_16译码器_1_out_19 , \n4_16译码器_1_out_20 , \计数器_1_out_2 , \计数器_1_out_3 ,
       \计数器_1_out_4 , \计数器_1_out_5 ;

  \计数器  \u_计数器_1  (
    .out_2(\计数器_1_out_2 ), .out_3(\计数器_1_out_3 ), .out_4(\计数器_1_out_4 ), .out_5(\计数器_1_out_5 ), .in_1(in_1));
  \_4_16译码器  \u_4_16译码器_1  (
    .in_1(\计数器_1_out_5 ), .in_2(\计数器_1_out_4 ), .in_3(\计数器_1_out_3 ), .in_4(\计数器_1_out_2 ),
    .out_5(\n4_16译码器_1_out_5 ), .out_6(\n4_16译码器_1_out_6 ), .out_7(\n4_16译码器_1_out_7 ),
    .out_8(\n4_16译码器_1_out_8 ), .out_9(\n4_16译码器_1_out_9 ), .out_10(\n4_16译码器_1_out_10 ),
    .out_11(\n4_16译码器_1_out_11 ), .out_12(\n4_16译码器_1_out_12 ), .out_13(\n4_16译码器_1_out_13 ),
    .out_14(\n4_16译码器_1_out_14 ), .out_15(\n4_16译码器_1_out_15 ), .out_16(\n4_16译码器_1_out_16 ),
    .out_17(\n4_16译码器_1_out_17 ), .out_18(\n4_16译码器_1_out_18 ), .out_19(\n4_16译码器_1_out_19 ),
    .out_20(\n4_16译码器_1_out_20 ));
  LED led_1 (.in(\n4_16译码器_1_out_5 ));
  LED led_2 (.in(\n4_16译码器_1_out_6 ));
  LED led_3 (.in(\n4_16译码器_1_out_7 ));
  LED led_4 (.in(\n4_16译码器_1_out_8 ));
  LED led_5 (.in(\n4_16译码器_1_out_9 ));
  LED led_6 (.in(\n4_16译码器_1_out_10 ));
  LED led_7 (.in(\n4_16译码器_1_out_11 ));
  LED led_8 (.in(\n4_16译码器_1_out_12 ));
  LED led_9 (.in(\n4_16译码器_1_out_13 ));
  LED led_10 (.in(\n4_16译码器_1_out_14 ));
  LED led_11 (.in(\n4_16译码器_1_out_15 ));
  LED led_12 (.in(\n4_16译码器_1_out_16 ));
  LED led_13 (.in(\n4_16译码器_1_out_17 ));
  LED led_14 (.in(\n4_16译码器_1_out_18 ));
  LED led_15 (.in(\n4_16译码器_1_out_19 ));
  LED led_16 (.in(\n4_16译码器_1_out_20 ));
endmodule

module \实验8  (
  input  in_1,
  input  in_2,
  input  in_3,
  input  in_4,
  input  in_5,
  input  in_6,
  input  in_7,
  input  in_8,
  input  in_9,
  input  in_10,
  input  in_11,
  input  in_12,
  input  in_13,
  input  in_14,
  input  in_15,
  input  in_16,
  input  in_17,
  input  in_18,
  input  in_19,
  input  in_20,
  input  in_21,
  input  in_22,
  input  in_23,
  input  in_24,
  input  in_25,
  input  in_26,
  input  in_27,
  input  in_28,
  input  in_29,
  input  in_30,
  input  in_31,
  input  in_32,
  input  in_33,
  output out_34,
  output out_35,
  output out_36,
  output out_37,
  output out_38,
  output out_39,
  output out_40,
  output out_41,
  output out_42,
  output out_43,
  output out_44,
  output out_45,
  output out_46,
  output out_47,
  output out_48,
  output out_49
);

  wire clock_1_out, \n3_8译码器_1_out_5 , \n3_8译码器_1_out_6 , \n3_8译码器_1_out_7 , \n3_8译码器_1_out_8 ,
       \n3_8译码器_1_out_9 , \n3_8译码器_1_out_10 , \n3_8译码器_1_out_11 , \n3_8译码器_1_out_12 , \n3位d触发器_1_out_7 ,
       \n3位d触发器_1_out_8 , \n3位d触发器_1_out_9 , \n3位d触发器_1_out_10 , \n3位d触发器_2_out_7 , \n3位d触发器_2_out_8 ,
       \n3位d触发器_2_out_9 , \n3位d触发器_2_out_10 , \n16_4编码器_1_out_17 , \n16_4编码器_1_out_18 , \n16_4编码器_1_out_19 ,
       \n16_4编码器_1_out_20 , \n16_4编码器_2_out_17 , \n16_4编码器_2_out_18 , \n16_4编码器_2_out_19 ,
       \n16_4编码器_2_out_20 , or_1_out, or_2_out, or_3_out, or_4_out, or_5_out, pull_resistor_1_node,
       pull_resistor_2_node, pull_resistor_3_node, \加减法器_1_out_10 , \加减法器_1_out_11 , \加减法器_1_out_12 ,
       \加减法器_1_out_13 , \加减法器_1_out_14 , \四位控制器_1_out_6 , \四位控制器_1_out_7 , \四位控制器_1_out_8 , \四位控制器_1_out_9 ,
       \数码管_1_s , \数码管_1_u , \数码管_1_v , \数码管_1_w , \数码管_1_x , \数码管_1_y , \数码管_1_z , \数码管_2_s , \数码管_2_u ,
       \数码管_2_v , \数码管_2_w , \数码管_2_x , \数码管_2_y , \数码管_2_z , \数码管高位_1_out_6 , \数码管高位_1_out_7 ,
       \数码管高位_1_out_8 , \数码管高位_1_out_9 , \数码管高位_1_out_10 , \数码管高位_1_out_11 , \数码管高位_1_out_12 , \翻转器_1_out_9 ,
       \翻转器_1_out_10 , \翻转器_1_out_12 , \翻转器_1_out_13 , \翻转器_2_out_9 , \翻转器_2_out_10 , \翻转器_2_out_12 ,
       \翻转器_2_out_13 , \计数器3_1_out_3 , \计数器3_1_out_4 , \计数器3_1_out_5 ;

  \_16_4编码器  \u_16_4编码器_1  (
    .in_1(in_1), .in_2(in_2), .in_3(in_3), .in_4(in_4), .in_5(in_5), .in_6(in_6), .in_7(in_7), .in_8(in_8),
    .in_9(in_9), .in_10(in_10), .in_11(in_11), .in_12(in_12), .in_13(in_13), .in_14(in_14), .in_15(in_15),
    .in_16(in_16), .out_17(\n16_4编码器_1_out_17 ), .out_18(\n16_4编码器_1_out_18 ), .out_19(\n16_4编码器_1_out_19 ),
    .out_20(\n16_4编码器_1_out_20 ));
  \_16_4编码器  \u_16_4编码器_2  (
    .in_1(in_17), .in_2(in_18), .in_3(in_19), .in_4(in_20), .in_5(in_21), .in_6(in_22), .in_7(in_23),
    .in_8(in_24), .in_9(in_25), .in_10(in_26), .in_11(in_27), .in_12(in_28), .in_13(in_29), .in_14(in_30),
    .in_15(in_32), .in_16(in_33), .out_17(\n16_4编码器_2_out_17 ), .out_18(\n16_4编码器_2_out_18 ),
    .out_19(\n16_4编码器_2_out_19 ), .out_20(\n16_4编码器_2_out_20 ));
  \翻转器  \u_翻转器_1  (
    .in_2(\n16_4编码器_1_out_17 ), .in_3(\n16_4编码器_1_out_18 ), .in_5(\n16_4编码器_1_out_19 ),
    .in_6(\n16_4编码器_1_out_20 ), .out_9(\翻转器_1_out_9 ), .out_10(\翻转器_1_out_10 ), .out_12(\翻转器_1_out_12 ),
    .out_13(\翻转器_1_out_13 ));  // open: in_1, in_4, in_7, out_8, out_11, out_14
  \四位控制器  \u_四位控制器_1  (
    .in_2(\翻转器_1_out_9 ), .in_3(\翻转器_1_out_10 ), .in_4(\翻转器_1_out_12 ), .in_5(\翻转器_1_out_13 ),
    .out_6(\四位控制器_1_out_6 ), .out_7(\四位控制器_1_out_7 ), .out_8(\四位控制器_1_out_8 ), .out_9(\四位控制器_1_out_9 ),
    .in_1(or_2_out));
  \翻转器  \u_翻转器_2  (
    .in_2(\n16_4编码器_2_out_17 ), .in_3(\n16_4编码器_2_out_18 ), .in_5(\n16_4编码器_2_out_19 ),
    .in_6(\n16_4编码器_2_out_20 ), .out_9(\翻转器_2_out_9 ), .out_10(\翻转器_2_out_10 ), .out_12(\翻转器_2_out_12 ),
    .out_13(\翻转器_2_out_13 ));  // open: in_1, in_4, in_7, out_8, out_11, out_14
  \四位控制器  \u_四位控制器_2  (
    .in_2(\翻转器_2_out_9 ), .in_3(\翻转器_2_out_10 ), .in_4(\翻转器_2_out_12 ), .in_5(\翻转器_2_out_13 ),
    .out_6(\四位控制器_1_out_6 ), .out_7(\四位控制器_1_out_7 ), .out_8(\四位控制器_1_out_8 ), .out_9(\四位控制器_1_out_9 ),
    .in_1(or_1_out));
  LED led_1 (.in(\四位控制器_1_out_6 ));
  LED led_2 (.in(pull_resistor_1_node));
  LED led_3 (.in(\四位控制器_1_out_8 ));
  LED led_4 (.in(\四位控制器_1_out_9 ));
  LED led_5 (.in(\四位控制器_1_out_7 ));
  Pull_Resistor pull_resistor_1 (.node(pull_resistor_1_node));
  Clock clock_1 (.out(clock_1_out));
  \_4_16译码器  \u_4_16译码器_1  (
    .in_1(\四位控制器_1_out_6 ), .in_2(\四位控制器_1_out_7 ), .in_3(\四位控制器_1_out_8 ), .in_4(\四位控制器_1_out_9 ),
    .out_5(out_34), .out_6(out_35), .out_7(out_36), .out_8(out_37), .out_9(out_38), .out_10(out_39),
    .out_11(out_40), .out_12(out_41), .out_13(out_42), .out_14(out_43), .out_15(out_44), .out_16(out_45),
    .out_17(out_46), .out_18(out_47), .out_19(out_48), .out_20(out_49));
  \计数器3  \u_计数器3_1  (
    .in_2(clock_1_out), .in_1(in_31), .out_3(\计数器3_1_out_3 ), .out_4(\计数器3_1_out_4 ), .out_5(\计数器3_1_out_5 ));
  Pull_Resistor pull_resistor_2 (.node(pull_resistor_2_node));
  \_3_8译码器  \u_3_8译码器_1  (
    .in_1(\计数器3_1_out_5 ), .in_2(\计数器3_1_out_4 ), .in_3(\计数器3_1_out_3 ), .out_5(\n3_8译码器_1_out_5 ),
    .in_4(pull_resistor_2_node), .out_6(\n3_8译码器_1_out_6 ), .out_7(\n3_8译码器_1_out_7 ),
    .out_8(\n3_8译码器_1_out_8 ), .out_9(\n3_8译码器_1_out_9 ), .out_10(\n3_8译码器_1_out_10 ),
    .out_11(\n3_8译码器_1_out_11 ), .out_12(\n3_8译码器_1_out_12 ));
  \_3位D触发器  \u_3位d触发器_1  (
    .in_1(\四位控制器_1_out_6 ), .in_2(\四位控制器_1_out_7 ), .in_3(\四位控制器_1_out_8 ), .in_4(\四位控制器_1_out_9 ),
    .out_7(\n3位d触发器_1_out_7 ), .out_8(\n3位d触发器_1_out_8 ), .out_9(\n3位d触发器_1_out_9 ),
    .out_10(\n3位d触发器_1_out_10 ), .in_6(\n3_8译码器_1_out_11 ));  // open: in_5, out_11
  \_3位D触发器  \u_3位d触发器_2  (
    .in_1(\四位控制器_1_out_6 ), .in_2(\四位控制器_1_out_7 ), .in_3(\四位控制器_1_out_8 ), .in_4(\四位控制器_1_out_9 ),
    .out_7(\n3位d触发器_2_out_7 ), .out_8(\n3位d触发器_2_out_8 ), .out_9(\n3位d触发器_2_out_9 ),
    .out_10(\n3位d触发器_2_out_10 ), .in_6(\n3_8译码器_1_out_9 ));  // open: in_5, out_11
  or or_1 (or_1_out, \n3_8译码器_1_out_9 , \n3_8译码器_1_out_10 );
  or or_2 (or_2_out, \n3_8译码器_1_out_11 , \n3_8译码器_1_out_12 );
  \数码管高位  \u_数码管高位_1  (
    .in_1(pull_resistor_1_node), .in_2(\四位控制器_1_out_9 ), .in_3(\四位控制器_1_out_8 ), .in_4(\四位控制器_1_out_7 ),
    .in_5(\四位控制器_1_out_6 ), .out_6(\数码管高位_1_out_6 ), .out_7(\数码管高位_1_out_7 ), .out_8(\数码管高位_1_out_8 ),
    .out_9(\数码管高位_1_out_9 ), .out_10(\数码管高位_1_out_10 ), .out_11(\数码管高位_1_out_11 ), .out_12(\数码管高位_1_out_12 ));
  \加减法器  \u_加减法器_1  (
    .in_2(\n3位d触发器_1_out_7 ), .in_3(\n3位d触发器_1_out_8 ), .in_4(\n3位d触发器_1_out_9 ), .in_5(\n3位d触发器_1_out_10 ),
    .in_6(\n3位d触发器_2_out_7 ), .in_7(\n3位d触发器_2_out_8 ), .in_8(\n3位d触发器_2_out_9 ), .in_9(\n3位d触发器_2_out_10 ),
    .out_10(\加减法器_1_out_10 ), .out_11(\加减法器_1_out_11 ), .out_12(\加减法器_1_out_12 ), .out_13(\加减法器_1_out_13 ),
    .out_14(\加减法器_1_out_14 ), .in_1(or_4_out));
  Pull_Resistor pull_resistor_3 (.node(pull_resistor_3_node));
  \四位控制器  \u_四位控制器_3  (
    .in_2(\加减法器_1_out_13 ), .in_3(\加减法器_1_out_12 ), .in_4(\加减法器_1_out_11 ), .in_5(\加减法器_1_out_10 ),
    .out_6(\四位控制器_1_out_9 ), .out_7(\四位控制器_1_out_8 ), .out_8(\四位控制器_1_out_7 ), .out_9(\四位控制器_1_out_6 ),
    .in_1(or_5_out));
  \四位控制器  \u_四位控制器_4  (
    .in_2(\加减法器_1_out_14 ), .out_6(pull_resistor_1_node), .in_1(or_5_out));  // open: in_3, in_4, in_5, out_7, out_8, out_9
  \数码管  \u_数码管_1  (
    .a(\数码管高位_1_out_9 ), .b(\数码管高位_1_out_10 ), .x(\数码管_1_x ), .c(\数码管高位_1_out_11 ), .d(\数码管高位_1_out_12 ),
    .y(\数码管_1_y ), .z(\数码管_1_z ), .u(\数码管_1_u ), .v(\数码管_1_v ), .w(\数码管_1_w ), .s(\数码管_1_s ));
  \数码管  \u_数码管_2  (
    .a(pull_resistor_3_node), .b(\数码管高位_1_out_6 ), .x(\数码管_2_x ), .c(\数码管高位_1_out_7 ), .d(\数码管高位_1_out_8 ),
    .y(\数码管_2_y ), .z(\数码管_2_z ), .u(\数码管_2_u ), .v(\数码管_2_v ), .w(\数码管_2_w ), .s(\数码管_2_s ));
  or or_3 (or_3_out, \n3_8译码器_1_out_6 , \n3_8译码器_1_out_5 );
  or or_4 (or_4_out, \n3_8译码器_1_out_7 , \n3_8译码器_1_out_8 );
  or or_5 (or_5_out, or_3_out, or_4_out);
  _7_Segment_Display u_7_segment_display_1 (
    .g(\数码管_1_s ), .f(\数码管_1_w ), .a(\数码管_1_x ), .b(\数码管_1_y ), .e(\数码管_1_v ), .d(\数码管_1_u ), .c(\数码管_1_z ));  // open: dp
  _7_Segment_Display u_7_segment_display_2 (
    .g(\数码管_2_s ), .f(\数码管_2_w ), .a(\数码管_2_x ), .b(\数码管_2_y ), .e(\数码管_2_v ), .d(\数码管_2_u ), .c(\数码管_2_z ));  // open: dp
endmodule

module \计数器3  (
  input  in_1,
  input  in_2,
  output out_3,
  output out_4,
  output out_5
);

  T_Flip_Flop t_ff_1 (.clk(out_4), .T(in_1), .Q(out_3));  // open: Qn, preset, reset, en
  T_Flip_Flop t_ff_2 (.clk(out_5), .T(in_1), .Q(out_4));  // open: Qn, preset, reset, en
  T_Flip_Flop t_ff_3 (.clk(in_2), .T(in_1), .Q(out_5));  // open: Qn, preset, reset, en
endmodule

module \加减法器  (
  input  in_1,
  input  in_2,
  input  in_3,
  input  in_4,
  input  in_5,
  input  in_6,
  input  in_7,
  input  in_8,
  input  in_9,
  output out_10,
  output out_11,
  output out_12,
  output out_13,
  output out_14
);

  wire not_1_out, pull_resistor_1_node, \全减器_1_out_12 , \全减器_1_out_13 , \全减器_1_out_14 , \全减器_1_out_15 ,
       \四位加法器_1_out_9 , \四位加法器_1_out_10 , \四位加法器_1_out_11 , \四位加法器_1_out_12 , \四位加法器_1_out_13 ;

  Pull_Resistor pull_resistor_1 (.node(pull_resistor_1_node));
  \四位加法器  \u_四位加法器_1  (
    .in_1(in_2), .in_2(in_6), .in_3(in_3), .in_4(in_7), .in_5(in_4), .in_6(in_8), .in_7(in_5), .in_8(in_9),
    .out_9(\四位加法器_1_out_9 ), .out_10(\四位加法器_1_out_10 ), .out_11(\四位加法器_1_out_11 ), .out_12(\四位加法器_1_out_12 ),
    .out_13(\四位加法器_1_out_13 ));
  \全减器  \u_全减器_1  (
    .in_1(pull_resistor_1_node), .in_2(in_2), .in_3(in_6), .in_4(in_3), .in_5(in_7), .in_6(in_4),
    .in_7(in_8), .in_8(in_5), .in_9(in_9), .in_10(pull_resistor_1_node), .in_11(pull_resistor_1_node),
    .out_12(\全减器_1_out_12 ), .out_13(\全减器_1_out_13 ), .out_14(\全减器_1_out_14 ), .out_15(\全减器_1_out_15 ));  // open: out_16, out_17
  \四位控制器  \u_四位控制器_1  (
    .in_2(\四位加法器_1_out_9 ), .in_3(\四位加法器_1_out_10 ), .in_4(\四位加法器_1_out_11 ), .in_5(\四位加法器_1_out_12 ),
    .out_6(out_10), .out_7(out_11), .out_8(out_12), .out_9(out_13), .in_1(in_1));
  \四位控制器  \u_四位控制器_2  (
    .in_2(\四位加法器_1_out_13 ), .out_6(out_14), .in_1(in_1));  // open: in_3, in_4, in_5, out_7, out_8, out_9
  not not_1 (not_1_out, in_1);
  \四位控制器  \u_四位控制器_3  (
    .in_2(\全减器_1_out_12 ), .in_3(\全减器_1_out_13 ), .in_4(\全减器_1_out_14 ), .in_5(\全减器_1_out_15 ),
    .out_6(out_10), .out_7(out_11), .out_8(out_12), .out_9(out_13), .in_1(not_1_out));
  \四位控制器  \u_四位控制器_4  (
    .in_2(pull_resistor_1_node), .out_6(out_14), .in_1(not_1_out));  // open: in_3, in_4, in_5, out_7, out_8, out_9
endmodule
