// Logisim project 汉明码电路.circ as structural Verilog: 9 circuits, main circuit main
module main (
  input  [3:0] in_1,
  input  [6:0] in_2,
  output P4,
  output P2,
  output P1
);

  wire \数码管译码器_1_out_2 , \数码管译码器_1_out_3 , \数码管译码器_1_out_4 , \数码管译码器_1_out_5 , \数码管译码器_1_out_6 ,
       \数码管译码器_1_out_7 , \数码管译码器_1_out_8 , \数码管译码器_1_out_9 ;
  wire [3:0] \汉明码解码器_1_out_2 ;
  wire [6:0] \汉明编码器_1_out_2 , \随机干扰器_1_out_3 ;

  // Probe on in_1
  \汉明编码器  \u_汉明编码器_1  (.out_2(\汉明编码器_1_out_2 ), .in_1(in_1));
  // Probe on \汉明编码器_1_out_2 
  // Probe on \随机干扰器_1_out_3 
  \随机干扰器  \u_随机干扰器_1  (.in_1(\汉明编码器_1_out_2 ), .out_3(\随机干扰器_1_out_3 ), .in_2(in_2));
  \汉明码检测器  \u_汉明码检测器_1  (.in_1(\随机干扰器_1_out_3 ), .P4(P4), .P2(P2), .P1(P1));
  \数码管译码器  \u_数码管译码器_1  (
    .in_1(\汉明码解码器_1_out_2 ), .out_2(\数码管译码器_1_out_2 ), .out_3(\数码管译码器_1_out_3 ), .out_4(\数码管译码器_1_out_4 ),
    .out_5(\数码管译码器_1_out_5 ), .out_6(\数码管译码器_1_out_6 ), .out_7(\数码管译码器_1_out_7 ), .out_8(\数码管译码器_1_out_8 ),
    .out_9(\数码管译码器_1_out_9 ));
  \汉明码解码器  \u_汉明码解码器_1  (.in_1(\随机干扰器_1_out_3 ), .out_2(\汉明码解码器_1_out_2 ));
  _7_Segment_Display u_7_segment_display_1 (
    .g(\数码管译码器_1_out_2 ), .f(\数码管译码器_1_out_3 ), .a(\数码管译码器_1_out_4 ), .b(\数码管译码器_1_out_5 ),
    .e(\数码管译码器_1_out_6 ), .d(\数码管译码器_1_out_7 ), .c(\数码管译码器_1_out_8 ), .dp(\数码管译码器_1_out_9 ));
endmodule

module \数码管译码器  (
  input  [3:0] in_1,
  output out_2,
  output out_3,
  output out_4,
  output out_5,
  output out_6,
  output out_7,
  output out_8,
  output out_9
);

  \数码管输出  \u_数码管输出_1  (
    .I1(in_1[3]), .I2(in_1[2]), .I3(in_1[1]), .I4(in_1[0]), .O1(out_2), .O2(out_3), .O3(out_4), .O4(out_5),
    .O5(out_6), .O6(out_7), .O7(out_8), .O8(out_9));
endmodule

module \数码管输出  (
  input  I1,
  input  I2,
  input  I3,
  input  I4,
  output O1,
  output O2,
  output O3,
  output O4,
  output O5,
  output O6,
  output O7,
  output O8
);

  wire nand_1_out, nand_2_out, nand_3_out, nand_4_out, nand_5_out, nand_6_out, nand_7_out, nand_8_out,
       nand_9_out, nand_10_out, nand_11_out, nand_12_out, nand_13_out, nand_14_out, nand_15_out, nand_16_out,
       nand_17_out, nand_18_out, nand_19_out, nand_20_out, nand_21_out, nand_22_out, nand_23_out,
       nand_24_out, nand_25_out, nand_26_out, nand_27_out, nand_28_out, nand_29_out, nand_30_out,
       nand_31_out, nand_32_out, nand_33_out, nand_34_out, nand_35_out, nand_36_out, nand_37_out,
       nand_38_out, nand_39_out, nand_40_out, nand_41_out, nand_42_out, nand_43_out, nand_44_out,
       nand_45_out, nand_46_out, nand_47_out, nand_48_out, nand_49_out, nand_50_out, nand_51_out,
       nand_52_out, nand_53_out, nand_54_out, nand_55_out, nand_56_out, nand_57_out, nand_58_out,
       nand_59_out, nand_60_out, nand_61_out, nand_62_out, nand_63_out, nand_64_out, nand_65_out,
       nand_66_out, nand_67_out, nand_68_out, nand_69_out, nand_70_out, nand_71_out, nand_72_out,
       nand_73_out, nand_74_out, nand_75_out, nand_76_out, nand_77_out, nand_78_out, nand_79_out,
       nand_80_out, nand_81_out, nand_82_out, nand_83_out, nand_84_out, nand_85_out, nand_86_out,
       nand_87_out, nand_88_out, nand_89_out, nand_90_out, nand_91_out, nand_92_out, nand_93_out,
       nand_94_out, nand_95_out, nand_96_out, nand_97_out, nand_98_out, nand_99_out, nand_100_out,
       nand_101_out, nand_103_out, nand_104_out, nand_105_out, nand_106_out, nand_107_out, nand_108_out,
       nand_109_out, nand_110_out, nand_111_out, nand_112_out, nand_113_out, nand_114_out, nand_115_out,
       nand_116_out, nand_117_out, nand_118_out, nand_119_out, nand_120_out, nand_121_out, nand_122_out,
       nand_123_out, nand_124_out, nand_125_out, nand_126_out, nand_127_out, nand_128_out, nand_129_out,
       nand_130_out, nand_132_out, nand_133_out, nand_134_out, nand_135_out, nand_136_out, nand_137_out,
       nand_138_out, nand_139_out, nand_141_out, nand_142_out, nand_143_out, nand_144_out, nand_145_out,
       nand_146_out, nand_147_out, nand_148_out;

  nand nand_1 (nand_1_out, I2, I2);
  nand nand_2 (nand_2_out, I4, I4);
  nand nand_3 (nand_3_out, I1, I1);
  nand nand_4 (nand_4_out, I1, I1);
  nand nand_5 (nand_5_out, I2, I2);
  nand nand_6 (nand_6_out, I1, I1);
  nand nand_7 (nand_7_out, I3, I3);
  nand nand_8 (nand_8_out, I2, I2);
  nand nand_9 (nand_9_out, I4, I4);
  nand nand_10 (nand_10_out, I4, I4);
  nand nand_11 (nand_11_out, I1, I1);
  nand nand_12 (nand_12_out, I2, I2);
  nand nand_13 (nand_13_out, I2, I2);
  nand nand_14 (nand_14_out, I1, I1);
  nand nand_15 (nand_15_out, I3, I3);
  nand nand_16 (nand_16_out, I1, I1);
  nand nand_17 (nand_17_out, nand_1_out, I3);
  nand nand_18 (nand_18_out, I3, nand_2_out);
  nand nand_19 (nand_19_out, nand_3_out, I2);
  nand nand_20 (nand_20_out, nand_4_out, I2);
  nand nand_21 (nand_21_out, I1, nand_5_out);
  nand nand_22 (nand_22_out, nand_6_out, nand_7_out);
  nand nand_23 (nand_23_out, nand_8_out, nand_9_out);
  nand nand_24 (nand_24_out, I3, nand_10_out);
  nand nand_25 (nand_25_out, I1, I3);
  nand nand_26 (nand_26_out, I1, I2);
  nand nand_27 (nand_27_out, nand_11_out, nand_12_out);
  nand nand_28 (nand_28_out, nand_13_out, I3);
  nand nand_29 (nand_29_out, nand_14_out, nand_15_out);
  nand nand_30 (nand_30_out, nand_16_out, I4);
  nand nand_31 (nand_31_out, nand_17_out, nand_18_out);
  nand nand_32 (nand_32_out, nand_19_out, nand_19_out);
  nand nand_33 (nand_33_out, I3, I3);
  nand nand_34 (nand_34_out, I2, I2);
  nand nand_35 (nand_35_out, I3, I3);
  nand nand_36 (nand_36_out, I4, I4);
  nand nand_37 (nand_37_out, nand_20_out, nand_20_out);
  nand nand_38 (nand_38_out, I3, I3);
  nand nand_39 (nand_39_out, I2, I2);
  nand nand_40 (nand_40_out, I4, I4);
  nand nand_41 (nand_41_out, I1, I1);
  nand nand_42 (nand_42_out, I1, I1);
  nand nand_43 (nand_43_out, nand_21_out, nand_21_out);
  nand nand_44 (nand_44_out, I3, I3);
  nand nand_45 (nand_45_out, I1, I1);
  nand nand_46 (nand_46_out, I2, I2);
  nand nand_47 (nand_47_out, nand_22_out, nand_22_out);
  nand nand_48 (nand_48_out, I4, I4);
  nand nand_49 (nand_49_out, I1, I1);
  nand nand_50 (nand_50_out, I3, I3);
  nand nand_51 (nand_51_out, nand_23_out, nand_24_out);
  nand nand_52 (nand_52_out, nand_25_out, nand_26_out);
  nand nand_53 (nand_53_out, nand_27_out, nand_27_out);
  nand nand_54 (nand_54_out, I4, I4);
  nand nand_55 (nand_55_out, nand_28_out, nand_28_out);
  nand nand_56 (nand_56_out, I3, I3);
  nand nand_57 (nand_57_out, I3, I3);
  nand nand_58 (nand_58_out, nand_29_out, nand_30_out);
  nand nand_59 (nand_59_out, I3, I3);
  nand nand_60 (nand_60_out, I1, I1);
  nand nand_61 (nand_61_out, I2, I2);
  nand nand_62 (nand_62_out, nand_31_out, nand_31_out);
  nand nand_63 (nand_63_out, nand_32_out, nand_33_out);
  nand nand_64 (nand_64_out, I1, nand_34_out);
  nand nand_65 (nand_65_out, I1, I4);
  nand nand_66 (nand_66_out, nand_35_out, nand_36_out);
  nand nand_67 (nand_67_out, nand_37_out, nand_38_out);
  nand nand_68 (nand_68_out, nand_39_out, nand_40_out);
  nand nand_69 (nand_69_out, nand_41_out, I3);
  nand nand_70 (nand_70_out, nand_42_out, I2);
  nand nand_71 (nand_71_out, I2, I3);
  nand nand_72 (nand_72_out, nand_43_out, nand_44_out);
  nand nand_73 (nand_73_out, nand_45_out, nand_46_out);
  nand nand_74 (nand_74_out, nand_47_out, nand_48_out);
  nand nand_75 (nand_75_out, nand_49_out, I3);
  nand nand_76 (nand_76_out, I1, nand_50_out);
  nand nand_77 (nand_77_out, nand_51_out, nand_51_out);
  nand nand_78 (nand_78_out, nand_52_out, nand_52_out);
  nand nand_79 (nand_79_out, nand_53_out, nand_54_out);
  nand nand_80 (nand_80_out, nand_55_out, I4);
  nand nand_81 (nand_81_out, I2, nand_56_out);
  nand nand_82 (nand_82_out, I2, I3);
  nand nand_83 (nand_83_out, I1, nand_57_out);
  nand nand_84 (nand_84_out, nand_58_out, nand_58_out);
  nand nand_85 (nand_85_out, nand_59_out, I4);
  nand nand_86 (nand_86_out, nand_60_out, I2);
  nand nand_87 (nand_87_out, I1, nand_61_out);
  nand nand_88 (nand_88_out, nand_62_out, nand_63_out);
  nand nand_89 (nand_89_out, nand_64_out, nand_65_out);
  nand nand_90 (nand_90_out, nand_66_out, nand_67_out);
  nand nand_91 (nand_91_out, I4, I4);
  nand nand_92 (nand_92_out, I2, I2);
  nand nand_93 (nand_93_out, nand_68_out, nand_69_out);
  nand nand_94 (nand_94_out, nand_70_out, nand_70_out);
  nand nand_95 (nand_95_out, nand_71_out, nand_72_out);
  nand nand_96 (nand_96_out, I4, I4);
  nand nand_97 (nand_97_out, nand_73_out, nand_74_out);
  nand nand_98 (nand_98_out, I2, I2);
  nand nand_99 (nand_99_out, I4, I4);
  nand nand_100 (nand_100_out, nand_75_out, nand_75_out);
  nand nand_101 (nand_101_out, nand_76_out, nand_76_out);
  nand nand_102 (O5, nand_77_out, nand_78_out);
  nand nand_103 (nand_103_out, nand_79_out, nand_80_out);
  nand nand_104 (nand_104_out, nand_81_out, nand_81_out);
  nand nand_105 (nand_105_out, nand_82_out, nand_82_out);
  nand nand_106 (nand_106_out, I4, I4);
  nand nand_107 (nand_107_out, nand_83_out, nand_83_out);
  nand nand_108 (nand_108_out, I4, I4);
  nand nand_109 (nand_109_out, nand_84_out, nand_85_out);
  nand nand_110 (nand_110_out, nand_86_out, nand_87_out);
  nand nand_111 (nand_111_out, nand_88_out, nand_88_out);
  nand nand_112 (nand_112_out, nand_89_out, nand_89_out);
  nand nand_113 (nand_113_out, nand_90_out, nand_90_out);
  nand nand_114 (nand_114_out, I2, nand_91_out);
  nand nand_115 (nand_115_out, I1, nand_92_out);
  nand nand_116 (nand_116_out, I1, I3);
  nand nand_117 (nand_117_out, nand_93_out, nand_93_out);
  nand nand_118 (nand_118_out, nand_94_out, I4);
  nand nand_119 (nand_119_out, nand_95_out, nand_95_out);
  nand nand_120 (nand_120_out, I1, nand_96_out);
  nand nand_121 (nand_121_out, nand_97_out, nand_97_out);
  nand nand_122 (nand_122_out, nand_98_out, nand_99_out);
  nand nand_123 (nand_123_out, nand_100_out, I4);
  nand nand_124 (nand_124_out, nand_101_out, I4);
  nand nand_125 (nand_125_out, nand_103_out, nand_103_out);
  nand nand_126 (nand_126_out, nand_104_out, I4);
  nand nand_127 (nand_127_out, nand_105_out, nand_106_out);
  nand nand_128 (nand_128_out, nand_107_out, nand_108_out);
  nand nand_129 (nand_129_out, nand_109_out, nand_109_out);
  nand nand_130 (nand_130_out, nand_110_out, nand_110_out);
  nand nand_131 (O1, nand_111_out, nand_112_out);
  nand nand_132 (nand_132_out, nand_113_out, nand_114_out);
  nand nand_133 (nand_133_out, nand_115_out, nand_116_out);
  nand nand_134 (nand_134_out, nand_117_out, nand_118_out);
  nand nand_135 (nand_135_out, nand_119_out, nand_120_out);
  nand nand_136 (nand_136_out, nand_121_out, nand_122_out);
  nand nand_137 (nand_137_out, nand_123_out, nand_124_out);
  nand nand_138 (nand_138_out, nand_125_out, nand_126_out);
  nand nand_139 (nand_139_out, nand_127_out, nand_128_out);
  nand nand_140 (O7, nand_129_out, nand_130_out);
  nand nand_141 (nand_141_out, nand_132_out, nand_132_out);
  nand nand_142 (nand_142_out, nand_133_out, nand_133_out);
  nand nand_143 (nand_143_out, nand_134_out, nand_134_out);
  nand nand_144 (nand_144_out, nand_135_out, nand_135_out);
  nand nand_145 (nand_145_out, nand_136_out, nand_136_out);
  nand nand_146 (nand_146_out, nand_137_out, nand_137_out);
  nand nand_147 (nand_147_out, nand_138_out, nand_138_out);
  nand nand_148 (nand_148_out, nand_139_out, nand_139_out);
  nand nand_149 (O2, nand_141_out, nand_142_out);
  nand nand_150 (O3, nand_143_out, nand_144_out);
  nand nand_151 (O4, nand_145_out, nand_146_out);
  nand nand_152 (O6, nand_147_out, nand_148_out);

  assign O8 = 1'b0;
endmodule

module \汉明编码器  (
  input  [3:0] in_1,
  output [6:0] out_2
);

  wire xor_1_out, xor_2_out, xor_3_out;

  xor xor_1 (xor_1_out, in_1[3], in_1[2]);
  xor xor_2 (xor_2_out, in_1[3], in_1[1]);
  xor xor_3 (xor_3_out, in_1[2], in_1[1]);
  xor xor_4 (out_2[6], xor_1_out, in_1[0]);
  xor xor_5 (out_2[5], xor_2_out, in_1[0]);
  xor xor_6 (out_2[3], xor_3_out, in_1[0]);

  assign {out_2[4], out_2[2:0]} = in_1;
endmodule

module \随机干扰器  (
  input  [6:0] in_1,
  input  [6:0] in_2,
  output [6:0] out_3
);

  xor xor_1 (out_3[0], in_1[0], in_2[0]);
  xor xor_2 (out_3[1], in_1[1], in_2[1]);
  xor xor_3 (out_3[2], in_1[2], in_2[2]);
  xor xor_4 (out_3[3], in_1[3], in_2[3]);
  xor xor_5 (out_3[4], in_1[4], in_2[4]);
  xor xor_6 (out_3[5], in_1[5], in_2[5]);
  xor xor_7 (out_3[6], in_1[6], in_2[6]);
endmodule

module \二路译码器  (
  input  I1,
  input  I2,
  output O1,
  output O2,
  output O3,
  output O4
);

  wire not_1_out, not_2_out, not_3_out, not_4_out;

  not not_1 (not_1_out, I1);
  not not_2 (not_2_out, I2);
  not not_3 (not_3_out, I1);
  not not_4 (not_4_out, I2);
  and and_1 (O4, I1, I2);
  and and_2 (O1, not_1_out, not_2_out);
  and and_3 (O2, not_3_out, I2);
  and and_4 (O3, I1, not_4_out);
endmodule

module \汉明码检测器  (
  input  [6:0] in_1,
  output P4,
  output P2,
  output P1
);

  wire xor_1_out, xor_2_out, xor_3_out, xor_4_out, xor_5_out, xor_6_out;

  xor xor_1 (xor_1_out, in_1[3], in_1[2]);
  xor xor_2 (xor_2_out, in_1[1], in_1[0]);
  xor xor_3 (xor_3_out, in_1[5], in_1[4]);
  xor xor_4 (xor_4_out, in_1[1], in_1[0]);
  xor xor_5 (xor_5_out, in_1[6], in_1[4]);
  xor xor_6 (xor_6_out, in_1[2], in_1[0]);
  xor xor_7 (P4, xor_1_out, xor_2_out);
  xor xor_8 (P2, xor_3_out, xor_4_out);
  xor xor_9 (P1, xor_5_out, xor_6_out);
endmodule

module \汉明码解码器  (
  input  [6:0] in_1,
  output [3:0] out_2
);

  wire temp_1_o3, temp_1_o5, temp_1_o6, temp_1_o7, \汉明码检测器_1_p1 , \汉明码检测器_1_p2 , \汉明码检测器_1_p4 ;

  \汉明码检测器  \u_汉明码检测器_1  (.in_1(in_1), .P4(\汉明码检测器_1_p4 ), .P2(\汉明码检测器_1_p2 ), .P1(\汉明码检测器_1_p1 ));
  temp temp_1 (
    .I1(\汉明码检测器_1_p4 ), .I2(\汉明码检测器_1_p2 ), .I4(\汉明码检测器_1_p1 ), .O3(temp_1_o3), .O5(temp_1_o5),
    .O6(temp_1_o6), .O7(temp_1_o7));  // open: O1, O2, O4
  xor xor_1 (out_2[3], temp_1_o3, in_1[4]);
  xor xor_2 (out_2[2], temp_1_o5, in_1[2]);
  xor xor_3 (out_2[1], temp_1_o6, in_1[1]);
  xor xor_4 (out_2[0], temp_1_o7, in_1[0]);
endmodule

module temp (
  input  I1,
  input  I2,
  input  I4,
  output O1,
  output O2,
  output O3,
  output O4,
  output O5,
  output O6,
  output O7
);

  wire nand_1_out, nand_2_out, nand_3_out, nand_4_out, nand_5_out, nand_6_out, nand_7_out, nand_8_out,
       nand_9_out, nand_10_out, nand_11_out, nand_12_out, nand_13_out, nand_14_out, nand_15_out, nand_16_out,
       nand_17_out, nand_18_out, nand_19_out, nand_20_out, nand_21_out, nand_22_out, nand_23_out,
       nand_24_out, nand_25_out, nand_26_out, nand_27_out, nand_28_out, nand_29_out, nand_30_out,
       nand_31_out, nand_32_out, nand_33_out, nand_34_out, nand_35_out, nand_36_out, nand_37_out,
       nand_38_out, nand_39_out, nand_40_out, nand_41_out, nand_42_out, nand_43_out, nand_44_out,
       nand_45_out, nand_46_out, nand_47_out, nand_48_out, nand_49_out, nand_50_out, nand_51_out,
       nand_52_out, nand_53_out, nand_54_out, nand_55_out, nand_56_out, nand_57_out, nand_58_out,
       nand_59_out, nand_60_out, nand_61_out, nand_62_out, nand_63_out, nand_64_out, nand_65_out,
       nand_66_out, nand_67_out, nand_68_out, nand_69_out, nand_70_out, nand_71_out, nand_72_out,
       nand_73_out, nand_74_out, nand_75_out, nand_76_out, nand_77_out, nand_78_out, nand_79_out,
       nand_80_out, nand_81_out, nand_82_out, nand_83_out, nand_84_out, nand_85_out, nand_86_out;

  nand nand_1 (nand_1_out, I1, I1);
  nand nand_2 (nand_2_out, I2, I2);
  nand nand_3 (nand_3_out, I1, I1);
  nand nand_4 (nand_4_out, I2, I2);
  nand nand_5 (nand_5_out, I1, I1);
  nand nand_6 (nand_6_out, I2, I2);
  nand nand_7 (nand_7_out, I1, I1);
  nand nand_8 (nand_8_out, I2, I2);
  nand nand_9 (nand_9_out, I1, I1);
  nand nand_10 (nand_10_out, I1, I1);
  nand nand_11 (nand_11_out, I1, I1);
  nand nand_12 (nand_12_out, I1, I1);
  nand nand_13 (nand_13_out, I1, I1);
  nand nand_14 (nand_14_out, I1, I1);
  nand nand_15 (nand_15_out, I1, I1);
  nand nand_16 (nand_16_out, I1, I1);
  nand nand_17 (nand_17_out, I2, I2);
  nand nand_18 (nand_18_out, I2, I2);
  nand nand_19 (nand_19_out, I2, I2);
  nand nand_20 (nand_20_out, I2, I2);
  nand nand_21 (nand_21_out, I2, I2);
  nand nand_22 (nand_22_out, I2, I2);
  nand nand_23 (nand_23_out, I2, I2);
  nand nand_24 (nand_24_out, I2, I2);
  nand nand_25 (nand_25_out, I1, I2);
  nand nand_26 (nand_26_out, I1, I2);
  nand nand_27 (nand_27_out, I1, I2);
  nand nand_28 (nand_28_out, I1, I2);
  nand nand_29 (nand_29_out, I1, I2);
  nand nand_30 (nand_30_out, I1, I2);
  nand nand_31 (nand_31_out, I1, I2);
  nand nand_32 (nand_32_out, I1, I2);
  nand nand_33 (nand_33_out, nand_1_out, nand_2_out);
  nand nand_34 (nand_34_out, nand_3_out, nand_4_out);
  nand nand_35 (nand_35_out, nand_5_out, nand_6_out);
  nand nand_36 (nand_36_out, nand_7_out, nand_8_out);
  nand nand_37 (nand_37_out, nand_9_out, I2);
  nand nand_38 (nand_38_out, nand_10_out, I2);
  nand nand_39 (nand_39_out, nand_11_out, I2);
  nand nand_40 (nand_40_out, nand_12_out, I2);
  nand nand_41 (nand_41_out, nand_13_out, I2);
  nand nand_42 (nand_42_out, nand_14_out, I2);
  nand nand_43 (nand_43_out, nand_15_out, I2);
  nand nand_44 (nand_44_out, nand_16_out, I2);
  nand nand_45 (nand_45_out, I1, nand_17_out);
  nand nand_46 (nand_46_out, I1, nand_18_out);
  nand nand_47 (nand_47_out, I1, nand_19_out);
  nand nand_48 (nand_48_out, I1, nand_20_out);
  nand nand_49 (nand_49_out, I1, nand_21_out);
  nand nand_50 (nand_50_out, I1, nand_22_out);
  nand nand_51 (nand_51_out, I1, nand_23_out);
  nand nand_52 (nand_52_out, I1, nand_24_out);
  nand nand_53 (nand_53_out, nand_25_out, nand_26_out);
  nand nand_54 (nand_54_out, I4, I4);
  nand nand_55 (nand_55_out, nand_27_out, nand_28_out);
  nand nand_56 (nand_56_out, I4, I4);
  nand nand_57 (nand_57_out, nand_29_out, nand_30_out);
  nand nand_58 (nand_58_out, nand_31_out, nand_32_out);
  nand nand_59 (nand_59_out, nand_33_out, nand_34_out);
  nand nand_60 (nand_60_out, nand_35_out, nand_36_out);
  nand nand_61 (nand_61_out, nand_37_out, nand_38_out);
  nand nand_62 (nand_62_out, I4, I4);
  nand nand_63 (nand_63_out, nand_39_out, nand_40_out);
  nand nand_64 (nand_64_out, I4, I4);
  nand nand_65 (nand_65_out, nand_41_out, nand_42_out);
  nand nand_66 (nand_66_out, nand_43_out, nand_44_out);
  nand nand_67 (nand_67_out, nand_45_out, nand_46_out);
  nand nand_68 (nand_68_out, I4, I4);
  nand nand_69 (nand_69_out, nand_47_out, nand_48_out);
  nand nand_70 (nand_70_out, I4, I4);
  nand nand_71 (nand_71_out, nand_49_out, nand_50_out);
  nand nand_72 (nand_72_out, nand_51_out, nand_52_out);
  nand nand_73 (nand_73_out, nand_53_out, nand_54_out);
  nand nand_74 (nand_74_out, nand_55_out, nand_56_out);
  nand nand_75 (nand_75_out, nand_57_out, I4);
  nand nand_76 (nand_76_out, nand_58_out, I4);
  nand nand_77 (nand_77_out, nand_59_out, I4);
  nand nand_78 (nand_78_out, nand_60_out, I4);
  nand nand_79 (nand_79_out, nand_61_out, nand_62_out);
  nand nand_80 (nand_80_out, nand_63_out, nand_64_out);
  nand nand_81 (nand_81_out, nand_65_out, I4);
  nand nand_82 (nand_82_out, nand_66_out, I4);
  nand nand_83 (nand_83_out, nand_67_out, nand_68_out);
  nand nand_84 (nand_84_out, nand_69_out, nand_70_out);
  nand nand_85 (nand_85_out, nand_71_out, I4);
  nand nand_86 (nand_86_out, nand_72_out, I4);
  nand nand_87 (O6, nand_73_out, nand_74_out);
  nand nand_88 (O7, nand_75_out, nand_76_out);
  nand nand_89 (O1, nand_77_out, nand_78_out);
  nand nand_90 (O2, nand_79_out, nand_80_out);
  nand nand_91 (O3, nand_81_out, nand_82_out);
  nand nand_92 (O4, nand_83_out, nand_84_out);
  nand nand_93 (O5, nand_85_out, nand_86_out);
endmodule
